// Digital circuit bf_cpu_module.dig as structural Verilog
module bf_cpu_module (
  input  Clk,
  input  [7:0] Opcode,
  output [7:0] Chr,
  output Out,
  output [15:0] Addr,
  output PC_plus__plus,
  output End,
  output Rst
);

  wire _1b_ram_1_q, _8b_or_1_or, and_1_out, and_2_out, and_4_out, and_5_out, and_7_out, and_8_out, and_9_out,
       bf_instruction_decoder_1_gt, bf_instruction_decoder_1_lt, bf_instruction_decoder_1_out_3,
       bf_instruction_decoder_1_out_6, bf_instruction_decoder_1_out_7, bf_instruction_decoder_1_out_8,
       bf_instruction_decoder_1_out_9, bf_instruction_decoder_1_plus, bf_instruction_decoder_1_stop,
       delay_1_out, delay_2_out, delay_3_out, delay_4_out, mem_ptr_ovf, not_1_out, not_2_out,
       one_time_bit_1__1st, or_1_out, or_2_out, or_3_out, or_4_out, or_5_out, or_6_out, or_7_out, or_8_out,
       or_9_out, or_10_out, or_11_out, or_13_out, or_14_out;
  wire [7:0] _8x1_and_1_x, memory_d;
  wire [15:0] counterpreset_1_out, loop_ptr_out, mem_ptr_out, multiplexer_1_out;
  wire [16:0] loops_d;
  wire [16:16] or_12_out;

  one_time_bit one_time_bit_1 (.Cl(Clk), .Rst(Rst), ._2nd(PC_plus__plus), ._1st(one_time_bit_1__1st));
  or or_1 (or_1_out, one_time_bit_1__1st, or_2_out);
  Multiplexer #(.Bits(16)) multiplexer_1 (.sel(Rst), .in_0(loops_d[15:0]), .in_1({16{1'b1}}), .out(multiplexer_1_out));
  CounterPreset #(.Bits(16)) counterpreset_1 (
    .en(one_time_bit_1__1st), .C(or_1_out), .dir(1'b0), .in(multiplexer_1_out), .ld(or_2_out), .clr(1'b0),
    .out(counterpreset_1_out));  // open: ovf
  or or_2 (or_2_out, Rst, and_7_out);
  or or_3 (or_3_out, Rst, one_time_bit_1__1st);
  _16b_register _16b_register_1 (.S(or_3_out), .V(counterpreset_1_out), .X(Addr));
  bf_instruction_decoder bf_instruction_decoder_1 (
    .inst(Opcode), .plus(bf_instruction_decoder_1_plus), .out_3(bf_instruction_decoder_1_out_3),
    .gt(bf_instruction_decoder_1_gt), .lt(bf_instruction_decoder_1_lt),
    .out_6(bf_instruction_decoder_1_out_6), .out_7(bf_instruction_decoder_1_out_7),
    .out_8(bf_instruction_decoder_1_out_8), .out_9(bf_instruction_decoder_1_out_9),
    .Stop(bf_instruction_decoder_1_stop));  // open: Brk
  or or_4 (or_4_out, and_1_out, and_2_out);
  or or_5 (or_5_out, and_2_out, and_1_out);
  and and_1 (and_1_out, _1b_ram_1_q, bf_instruction_decoder_1_gt);
  and and_2 (and_2_out, bf_instruction_decoder_1_lt, _1b_ram_1_q);
  CounterPreset #(.Bits(16)) mem_ptr (
    .en(or_4_out), .C(or_4_out), .dir(and_2_out), .in({16{1'b0}}), .ld(1'b0), .clr(1'b0), .out(mem_ptr_out),
    .ovf(mem_ptr_ovf));
  and and_3 (End, bf_instruction_decoder_1_stop, PC_plus__plus);
  Delay #(.delayTime(2)) delay_1 (.in(or_5_out), .out(delay_1_out));
  and and_4 (and_4_out, _1b_ram_1_q, bf_instruction_decoder_1_plus);
  and and_5 (and_5_out, bf_instruction_decoder_1_out_3, _1b_ram_1_q);
  or or_6 (or_6_out, and_4_out, and_5_out);
  or or_7 (or_7_out, or_6_out, delay_1_out);
  or or_8 (or_8_out, and_4_out, and_5_out);
  or or_9 (or_9_out, and_4_out, and_5_out);
  or or_10 (or_10_out, Rst, or_8_out);
  CounterPreset #(.Bits(8)) current_byte (
    .en(or_9_out), .C(or_7_out), .dir(and_5_out), .in(memory_d), .ld(delay_1_out), .clr(1'b0), .out(Chr));  // open: ovf
  not not_1 (not_1_out, Rst);
  Delay #(.delayTime(3)) delay_2 (.in(or_10_out), .out(delay_2_out));
  and and_6 (Out, _1b_ram_1_q, bf_instruction_decoder_1_out_8);
  _8x1_and _8x1_and_1 (.V(Chr), .AND(not_1_out), .X(_8x1_and_1_x));
  _8b_or _8b_or_1 (.\byte (Chr), .\or (_8b_or_1_or));
  RAMDualPort #(.AddrBits(16), .Bits(8)) memory (
    .A(mem_ptr_out), .Din(_8x1_and_1_x), .str(delay_2_out), .C(delay_2_out), .ld(1'b1), .D(memory_d));
  and and_7 (and_7_out, and_8_out, _8b_or_1_or);
  and and_8 (and_8_out, bf_instruction_decoder_1_out_7, _1b_ram_1_q);
  and and_9 (and_9_out, not_2_out, bf_instruction_decoder_1_out_7);
  not not_2 (not_2_out, _8b_or_1_or);
  or or_11 (or_11_out, bf_instruction_decoder_1_out_6, and_9_out);
  CounterPreset #(.Bits(16)) loop_ptr (
    .en(or_11_out), .C(or_11_out), .dir(and_9_out), .in({16{1'b0}}), .ld(1'b0), .clr(1'b0), .out(loop_ptr_out));  // open: ovf
  or or_12 (or_12_out[16], Rst, _8b_or_1_or);
  Delay #(.delayTime(3)) delay_3 (.in(Rst), .out(delay_3_out));
  RAMDualPort #(.AddrBits(16), .Bits(17)) loops (
    .A(loop_ptr_out), .Din({or_12_out[16], Addr}), .str(or_13_out), .C(or_13_out), .ld(1'b1), .D(loops_d));
  or or_13 (or_13_out, delay_3_out, delay_4_out);
  Delay #(.delayTime(3)) delay_4 (.in(bf_instruction_decoder_1_out_6), .out(delay_4_out));
  _1b_ram _1b_ram_1 (.V(loops_d[16]), .S(or_14_out), .Q(_1b_ram_1_q));  // open: NQ
  or or_14 (or_14_out, Rst, one_time_bit_1__1st);

  // Notes on the sheet:
  //   jmp back to while address
  //   jmp address for end while
  //   >
  //   <
  //   +
  //   -
  //   TODO(,)
  //   Reset line
  //   .
  //   current byte != 0
  //   end of while
  //   ]
  //   [
  //   Execute instruction?
  //   Execute loop?
endmodule
