// Digital circuit bf_cpu_standalone.dig as structural Verilog
module bf_cpu_standalone (
  input  clk,
  output [7:0] Chr,
  output Out
);

  wire _1b_ram_1_q, _8b_or_1_or, and_1_out, and_2_out, and_3_out, and_4_out, and_5_out, and_7_out, and_8_out,
       and_9_out, bf_instruction_decoder_1_brk, bf_instruction_decoder_1_gt, bf_instruction_decoder_1_lt,
       bf_instruction_decoder_1_out_3, bf_instruction_decoder_1_out_6, bf_instruction_decoder_1_out_7,
       bf_instruction_decoder_1_out_8, bf_instruction_decoder_1_out_9, bf_instruction_decoder_1_plus,
       bf_instruction_decoder_1_stop, delay_1_out, delay_2_out, delay_3_out, delay_4_out, mem_ptr_ovf,
       not_1_out, one_time_bit_1__1st, one_time_bit_1__2nd, one_time_bit_1_rst, or_1_out, or_2_out, or_3_out,
       or_4_out, or_5_out, or_6_out, or_7_out, or_8_out, or_9_out, or_10_out, or_11_out, or_13_out, or_14_out;
  wire [7:0] memory_d, Program_d;
  wire [15:0] counterpreset_1_out, loop_ptr_out, mem_ptr_out, multiplexer_1_out;
  wire [16:0] _16b_register_1_x, loops_d;

  one_time_bit one_time_bit_1 (
    .Cl(clk), .Rst(one_time_bit_1_rst), ._2nd(one_time_bit_1__2nd), ._1st(one_time_bit_1__1st));
  or or_1 (or_1_out, one_time_bit_1__1st, or_2_out);
  Multiplexer #(.Bits(16)) multiplexer_1 (
    .sel(one_time_bit_1_rst), .in_0(loops_d[15:0]), .in_1({16{1'b1}}), .out(multiplexer_1_out));
  CounterPreset #(.Bits(16)) counterpreset_1 (
    .en(one_time_bit_1__1st), .C(or_1_out), .dir(1'b0), .in(multiplexer_1_out), .ld(or_2_out), .clr(1'b0),
    .out(counterpreset_1_out));  // open: ovf
  or or_2 (or_2_out, one_time_bit_1_rst, and_7_out);
  or or_3 (or_3_out, one_time_bit_1_rst, one_time_bit_1__1st);
  _16b_register _16b_register_1 (.S(or_3_out), .V(counterpreset_1_out), .X(_16b_register_1_x[15:0]));
  EEPROMDualPort #(.AddrBits(16), .isProgramMemory("true"), .Bits(8)) Program (
    .A(_16b_register_1_x[15:0]), .Din({8{1'b0}}), .str(1'b0), .C(one_time_bit_1__2nd),
    .ld(one_time_bit_1__2nd), .D(Program_d));
  bf_instruction_decoder bf_instruction_decoder_1 (
    .inst(Program_d), .plus(bf_instruction_decoder_1_plus), .out_3(bf_instruction_decoder_1_out_3),
    .gt(bf_instruction_decoder_1_gt), .lt(bf_instruction_decoder_1_lt),
    .out_6(bf_instruction_decoder_1_out_6), .out_7(bf_instruction_decoder_1_out_7),
    .out_8(bf_instruction_decoder_1_out_8), .out_9(bf_instruction_decoder_1_out_9),
    .Stop(bf_instruction_decoder_1_stop), .Brk(bf_instruction_decoder_1_brk));
  or or_4 (or_4_out, and_1_out, and_2_out);
  or or_5 (or_5_out, and_2_out, and_1_out);
  and and_1 (and_1_out, _1b_ram_1_q, bf_instruction_decoder_1_gt);
  and and_2 (and_2_out, bf_instruction_decoder_1_lt, _1b_ram_1_q);
  Break #(.Cycles(1000000000)) break_1 (.brk(bf_instruction_decoder_1_brk));
  CounterPreset #(.Bits(16)) mem_ptr (
    .en(or_4_out), .C(or_4_out), .dir(and_2_out), .in({16{1'b0}}), .ld(1'b0), .clr(1'b0), .out(mem_ptr_out),
    .ovf(mem_ptr_ovf));
  and and_3 (and_3_out, bf_instruction_decoder_1_stop, one_time_bit_1__2nd);
  Delay #(.delayTime(2)) delay_1 (.in(or_5_out), .out(delay_1_out));
  Break #(.Cycles(1000000000)) break_2 (.brk(and_3_out));
  and and_4 (and_4_out, _1b_ram_1_q, bf_instruction_decoder_1_plus);
  and and_5 (and_5_out, bf_instruction_decoder_1_out_3, _1b_ram_1_q);
  or or_6 (or_6_out, and_4_out, and_5_out);
  or or_7 (or_7_out, or_6_out, delay_1_out);
  or or_8 (or_8_out, and_4_out, and_5_out);
  or or_9 (or_9_out, and_4_out, and_5_out);
  or or_10 (or_10_out, one_time_bit_1_rst, or_8_out);
  CounterPreset #(.Bits(8)) current_byte (
    .en(or_9_out), .C(or_7_out), .dir(and_5_out), .in(memory_d), .ld(delay_1_out), .clr(1'b0), .out(Chr));  // open: ovf
  Delay #(.delayTime(3)) delay_2 (.in(or_10_out), .out(delay_2_out));
  and and_6 (Out, _1b_ram_1_q, bf_instruction_decoder_1_out_8);
  _8b_or _8b_or_1 (.\byte (Chr), .\or (_8b_or_1_or));
  Break #(.Cycles(1000000000)) break_3 (.brk(Out));
  RAMDualPort #(.AddrBits(16), .Bits(8)) memory (
    .A(mem_ptr_out), .Din(Chr), .str(delay_2_out), .C(delay_2_out), .ld(1'b1), .D(memory_d));
  and and_7 (and_7_out, and_8_out, _8b_or_1_or);
  and and_8 (and_8_out, bf_instruction_decoder_1_out_7, _1b_ram_1_q);
  and and_9 (and_9_out, not_1_out, bf_instruction_decoder_1_out_7);
  not not_1 (not_1_out, _8b_or_1_or);
  or or_11 (or_11_out, bf_instruction_decoder_1_out_6, and_9_out);
  CounterPreset #(.Bits(16)) loop_ptr (
    .en(or_11_out), .C(or_11_out), .dir(and_9_out), .in({16{1'b0}}), .ld(1'b0), .clr(1'b0), .out(loop_ptr_out));  // open: ovf
  or or_12 (_16b_register_1_x[16], one_time_bit_1_rst, _8b_or_1_or);
  Delay #(.delayTime(3)) delay_3 (.in(one_time_bit_1_rst), .out(delay_3_out));
  RAMDualPort #(.AddrBits(16), .Bits(17)) loops (
    .A(loop_ptr_out), .Din(_16b_register_1_x), .str(or_13_out), .C(or_13_out), .ld(1'b1), .D(loops_d));
  or or_13 (or_13_out, delay_3_out, delay_4_out);
  Delay #(.delayTime(3)) delay_4 (.in(bf_instruction_decoder_1_out_6), .out(delay_4_out));
  _1b_ram _1b_ram_1 (.V(loops_d[16]), .S(or_14_out), .Q(_1b_ram_1_q));  // open: NQ
  or or_14 (or_14_out, one_time_bit_1_rst, one_time_bit_1__1st);

  // Notes on the sheet:
  //   jmp back to while address
  //   jmp address for end while
  //   contents of Program (hex, n*v repeats v):
  //   3e,2b,2b,2b,2b,2b,2b,2b,2b,2b,2b,5b,3c,2b,2b,2b,2b,2b,2b,2b,2b,2b,2b,3e,2d,5d,3c,
  //   2d,3e,3e,3e,3e,3e,2b,2b,2b,5b,3e,2b,2b,2b,3e,2b,2b,2b,3c,3c,2d,5d,3c,3c,3c,3c,2b,
  //   3c,5b,3e,5b,3e,2b,a,3e,2b,3c,3c,2d,5d,3e,3e,5b,2d,3c,3c,2b,3e,3e,5d,2b,2b,2b,2b,3e,
  //   2b,3c,5b,2d,3c,2d,3e,5d,3c,5b,5b,2d,5d,3e,3e,2d,3c,3c,5d,3e,3e,23,5b,5b,2d,5d,3c,
  //   3c,2b,3e,3e,5d,3c,3c,23,5b,5b,2d,5d,3e,3e,a,3e,3e,3e,3e,5b,5b,2d,5d,3c,2b,2b,2b,2b,
  //   2b,2b,2b,2b,2b,2b,3c,2d,3e,3e,5d,3c,2d,23,5b,3e,2b,3e,2b,3c,3c,2d,5d,3e,5b,3c,2b,
  //   3e,2d,5d,2b,3e,5b,5b,2d,5d,3c,2d,3e,5d,3c,3c,3c,3c,3c,3c,3c,3c,a,3c,2d,3e,3e,5d,23,
  //   3c,5b,3e,2b,3e,2b,3c,3c,2d,5d,3e,3e,5b,2d,3c,3c,2b,3e,3e,5d,2b,3e,2b,3c,5b,2d,3c,
  //   2d,3e,5d,3c,5b,5b,2d,5d,3e,3e,2d,3c,3c,5d,3e,3e,5b,5b,2d,5d,3c,3c,2b,3e,3e,5d,3c,
  //   3c,a,3c,5b,3e,3e,2b,3e,2b,3c,3c,3c,2d,5d,3e,3e,3e,5b,2d,3c,3c,3c,2b,3e,3e,3e,5d,2b,
  //   2b,3e,2b,3c,5b,2d,3c,2d,3e,5d,3c,5b,5b,2d,5d,3e,3e,2d,3c,3c,5d,3e,3e,5b,5b,2d,5d,
  //   3c,3c,2b,3e,3e,5d,3c,a,3c,5b,3e,2b,3c,5b,2d,5d,5d,3c,5b,3e,3e,2b,3c,3c,5b,2d,5d,5d,
  //   3e,3e,5b,3c,3c,2b,3e,3e,5b,2d,5d,5d,3c,3c,3c,5b,3e,3e,2b,3e,2b,3c,3c,3c,2d,5d,3e,
  //   3e,3e,5b,2d,3c,3c,3c,2b,3e,3e,3e,5d,2b,a,2b,2b,2b,3e,2b,3c,5b,2d,3c,2d,3e,5d,3c,5b,
  //   5b,2d,5d,3e,3e,2d,3c,3c,5d,3e,3e,5b,5b,2d,5d,3c,3c,2b,3e,3e,5d,3c,3c,5b,3e,2b,3c,
  //   5b,2d,5d,5d,3c,5b,3e,3e,2b,3c,3c,5b,2d,5d,5d,3e,3e,5b,3c,a,3c,2b,3e,3e,5b,2d,5d,5d,
  //   3c,3c,5b,5b,2d,5d,3e,3e,3e,2b,2b,2b,2b,2b,2b,2b,2b,5b,3e,3e,2b,2b,2b,2b,2b,2b,3c,
  //   3c,2d,5d,3e,5b,3c,2b,2b,2b,2b,2b,2b,2b,2b,5b,3e,2b,2b,2b,2b,2b,2b,3c,2d,5d,a,3e,23,
  //   2e,3c,2b,2b,2b,2b,2b,2b,2b,2b,5b,3e,2d,2d,2d,2d,2d,2d,3c,2d,5d,3e,5b,3c,3c,2b,3e,
  //   3e,2d,5d,5d,3e,2e,3c,3c,2b,2b,2b,2b,2b,2b,2b,2b,5b,3e,3e,2d,2d,2d,2d,2d,2d,3c,3c,
  //   2d,5d,3c,5b,2d,a,3e,3e,2b,3c,3c,5d,3c,2b,2b,2b,2b,2b,2b,2b,2b,5b,3c,2b,2b,2b,2b,3e,
  //   2d,5d,3c,2e,3e,2b,2b,2b,2b,2b,2b,2b,5b,3e,2b,2b,2b,2b,2b,2b,2b,2b,2b,3c,2d,5d,3e,
  //   2b,2b,2b,2e,3c,2b,2b,2b,2b,2b,5b,a,3e,2b,2b,2b,2b,2b,2b,2b,2b,2b,3c,2d,5d,3e,2e,2b,
  //   2b,2b,2b,2b,2e,2e,2d,2d,2d,2d,2d,2d,2d,2d,2e,2d,2d,2d,2d,2d,2d,2d,2e,2b,2b,2b,2b,
  //   2b,2b,2b,2b,2b,2b,2b,2b,2b,2b,3e,3e,5b,3e,3e,3e,2b,a,3e,2b,3c,3c,3c,3c,2d,5d,3e,3e,
  //   3e,3e,5b,2d,3c,3c,3c,3c,2b,3e,3e,3e,3e,5d,3e,2b,3c,5b,2d,3c,2d,3e,5d,3c,5b,5b,2d,
  //   5d,3e,3e,2d,3c,3c,5d,3e,3e,5b,5b,2d,5d,3c,3c,2b,3e,3e,5d,3c,3c,3c,3c,a,5b,3e,3e,3e,
  //   2b,3e,2b,3c,3c,3c,3c,2d,5d,3e,3e,3e,3e,5b,2d,3c,3c,3c,3c,2b,3e,3e,3e,3e,5d,2b,3e,
  //   2b,3c,5b,2d,3c,2d,3e,5d,3c,5b,5b,2d,5d,3e,3e,2d,3c,3c,5d,3e,3e,5b,5b,2d,5d,3c,3c,
  //   2b,3e,a,3e,5d,3c,3c,3c,5b,3e,3e,2b,3c,3c,5b,2d,5d,5d,3e,5b,3e,2b,3c,5b,2d,5d,5d,2b,
  //   2b,3e,3e,2b,3c,5b,2d,3c,2d,3e,5d,3c,5b,5b,2d,5d,3e,3e,2d,3c,3c,5d,3e,3e,5b,5b,2d,
  //   5d,3c,3c,2b,3e,3e,5d,3c,a,2b,3c,5b,5b,2d,5d,3e,2d,3c,5d,3e,5b,3c,3c,3c,3c,3c,3c,3c,
  //   2e,3e,3e,3e,3e,3e,3e,3e,5b,2d,5d,5d,3c,3c,3c,3c,3c,3c,3c,3c,3c,2e,3e,3e,2d,2d,2d,
  //   2d,2e,2d,2d,2d,2d,2d,2d,2d,2d,2d,2e,3c,3c,a,2e,3e,3e,2d,2d,2d,2d,2e,2b,2b,2b,2e,2e,
  //   2b,2b,2b,2b,2b,2b,2b,2b,2b,2b,2b,2b,2b,2e,5b,2d,5d,3c,3c,5b,2d,5d,5d,3c,5b,3e,2b,
  //   3e,2b,3c,3c,2d,5d,3e,3e,5b,2d,3c,3c,2b,3e,3e,5d,2b,3e,2b,3c,a,5b,2d,3c,2d,3e,5d,3c,
  //   5b,5b,2d,5d,3e,3e,2d,3c,3c,5d,3e,3e,5b,5b,2d,5d,3c,3c,2b,3e,3e,5d,3c,3c,3c,5b,3e,
  //   3e,2b,3e,2b,3c,3c,3c,2d,5d,3e,3e,3e,5b,2d,3c,3c,3c,2b,3e,3e,3e,5d,2b,2b,2b,2b,a,3e,
  //   2b,3c,5b,2d,3c,2d,3e,5d,3c,5b,5b,2d,5d,3e,3e,2d,3c,3c,5d,3e,3e,5b,5b,2d,5d,3c,3c,
  //   2b,3e,3e,5d,3c,3c,5b,3e,2b,3c,5b,2d,5d,5d,3c,5b,3e,3e,2b,3c,3c,5b,2d,5d,5d,3e,3e,
  //   5b,3c,3c,2b,3e,a,3e,5b,2d,5d,5d,3c,3c,5b,5b,2d,5d,3e,2b,2b,2b,2b,2b,2b,2b,2b,5b,3c,
  //   2b,2b,2b,2b,3e,2d,5d,3c,2e,3e,2b,2b,2b,2b,2b,2b,2b,2b,2b,2b,5b,3e,2b,2b,2b,2b,2b,
  //   2b,2b,2b,2b,2b,2b,3c,2d,5d,3e,2b,a,2e,2d,2e,3c,3c,2e,3e,3e,2b,2b,2b,2b,2b,2b,2e,2d,
  //   2d,2d,2d,2d,2d,2d,2d,2d,2d,2d,2d,2e,2d,2d,2d,2e,3c,3c,2e,3e,2b,2b,2b,2b,2b,2b,5b,
  //   3e,2b,2b,2b,3c,2d,5d,3e,2e,3c,2b,2b,2b,2b,2b,2b,5b,a,3e,2d,2d,2d,2d,3c,2d,5d,3e,2b,
  //   2b,2e,2b,2b,2b,2b,2b,2b,2b,2b,2b,2b,2b,2e,2e,5b,2d,5d,3c,3c,5b,2d,5d,2b,2b,2b,2b,
  //   2b,2b,2b,2b,2b,2b,2e,5b,2d,5d,5d,3c,5b,3e,2b,3e,2b,3c,3c,2d,5d,3e,3e,a,5b,2d,3c,3c,
  //   2b,3e,3e,5d,2b,2b,2b,3e,2b,3c,5b,2d,3c,2d,3e,5d,3c,5b,5b,2d,5d,3e,3e,2d,3c,3c,5d,
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  //   >
  //   <
  //   +
  //   -
  //   TODO(,)
  //   Reset line
  //   .
  //   current byte != 0
  //   end of while
  //   ]
  //   [
  //   Execute instruction?
  //   Execute loop?
endmodule
