// Digital circuit bf_cpu_with_preprocessor_standalone.dig as structural Verilog
module bf_cpu_with_preprocessor_standalone (
  input  clk,
  output [7:0] Chr,
  output Out
);

  wire _1b_ram_1_q, _8b_or_1_or, _8b_or_2_or, _8x1_and_1_x0, _8x1_and_1_x1, _8x1_and_1_x2, _8x1_and_1_x3,
       _8x1_and_1_x4, _8x1_and_1_x5, _8x1_and_1_x6, _8x1_and_1_x7, and_1_out, and_2_out, and_3_out,
       and_4_out, and_5_out, and_6_out, and_7_out, and_8_out, and_9_out, and_10_out, and_12_out, and_13_out,
       and_14_out, bf_rle_instruction_decoder_1_gt, bf_rle_instruction_decoder_1_lt,
       bf_rle_instruction_decoder_1_out_4, bf_rle_instruction_decoder_1_out_7,
       bf_rle_instruction_decoder_1_out_8, bf_rle_instruction_decoder_1_out_9,
       bf_rle_instruction_decoder_1_out_10, bf_rle_instruction_decoder_1_plus, comparator_1_eq,
       comparator_2_eq, comparator_3_eq, comparator_4_eq, delay_1_out, delay_2_out, delay_3_out, delay_4_out,
       delay_5_out, delay_6_out, delay_7_out, delay_8_out, mem_ptr_ovf, not_1_out, not_2_out, not_3_out,
       not_4_out, one_time_bit_1_exc, one_time_bit_1_pc_plus__plus, one_time_bit_1_rst, or_1_out, or_2_out,
       or_3_out, or_4_out, or_5_out, or_6_out, or_7_out, or_8_out, or_9_out, or_10_out, or_11_out, or_12_out,
       or_14_out, or_15_out, ram_input_selector_1_c, ram_input_selector_1_ld, ram_input_selector_1_str,
       rom_1_d;
  wire [7:0] add_2_s, ascii_2_opcode_out, BF_Program_d, bf_rle_instruction_encoder_1_rleopc, memory_d,
       multiplexer_1_out, prev_opc_q, ram_input_selector_1_d, Repeat_counter_out, RLE_program_d, xor_1_out;
  wire [15:0] _16b_register_1_x, add_1_s, bf_rle_instruction_decoder_1_count, loop_ptr_out, mem_ptr_out,
       PC_2_out, PC_3_out, PC_out, ram_input_selector_1_a;
  wire [16:0] loops_d;
  wire [16:16] or_13_out;

  one_time_bit one_time_bit_1 (
    .Cl(clk), .Rst(one_time_bit_1_rst), .Exc(one_time_bit_1_exc), .PC_plus__plus(one_time_bit_1_pc_plus__plus));
  not not_1 (not_1_out, comparator_1_eq);
  and and_1 (and_1_out, not_1_out, one_time_bit_1_exc);
  and and_2 (and_2_out, one_time_bit_1_pc_plus__plus, not_1_out);
  Counter #(.Bits(16)) PC (.en(1'b1), .C(and_1_out), .clr(1'b0), .out(PC_out));  // open: ovf
  EEPROMDualPort #(.AddrBits(16), .isProgramMemory("true"), .Bits(8)) BF_Program (
    .A(PC_out), .Din({8{1'b0}}), .str(1'b0), .C(and_2_out), .ld(1'b1), .D(BF_Program_d));
  LookUpTable #(.Bits(8)) ascii_2_opcode (
    .in0(BF_Program_d[0]), .in1(BF_Program_d[1]), .in2(BF_Program_d[2]), .in3(BF_Program_d[3]),
    .in4(BF_Program_d[4]), .in5(BF_Program_d[5]), .in6(BF_Program_d[6]), .in7(BF_Program_d[7]),
    .out(ascii_2_opcode_out));
  Delay #(.delayTime(10)) delay_1 (.in(and_2_out), .out(delay_1_out));
  or or_1 (or_1_out, one_time_bit_1_rst, and_2_out);
  or or_2 (or_2_out, delay_1_out, or_3_out);
  Register #(.Bits(8)) prev_opc (.D(ascii_2_opcode_out), .C(or_1_out), .en(1'b1), .Q(prev_opc_q));
  Counter #(.Bits(8)) Repeat_counter (
    .en(delay_1_out), .C(or_2_out), .clr(or_3_out), .out(Repeat_counter_out));  // open: ovf
  Comparator #(.Bits(8)) comparator_1 (.a(8'h2), .b(ascii_2_opcode_out), .eq(comparator_1_eq));  // open: gt, lt
  Comparator #(.Bits(8)) comparator_2 (.a(8'h1), .b(prev_opc_q), .eq(comparator_2_eq));  // open: gt, lt
  not not_2 (not_2_out, comparator_2_eq);
  assign xor_1_out = ascii_2_opcode_out ^ prev_opc_q;  // XOr xor_1, 8 bits wide
  ROM #(.AddrBits(8)) rom_1 (.A(prev_opc_q), .sel(and_2_out), .D(rom_1_d));
  _8b_or _8b_or_1 (.\byte (xor_1_out), .\or (_8b_or_1_or));
  PullDown pulldown_1 (.out(rom_1_d));
  not not_3 (not_3_out, one_time_bit_1_rst);
  Comparator #(.Bits(8)) comparator_3 (.a(8'h3f), .b(Repeat_counter_out), .eq(comparator_3_eq));  // open: gt, lt
  and and_3 (and_3_out, not_3_out, _8b_or_1_or);
  or or_3 (or_3_out, comparator_1_eq, and_3_out, rom_1_d, comparator_3_eq);
  Delay #(.delayTime(4)) delay_2 (.in(not_2_out), .out(delay_2_out));
  and and_4 (and_4_out, delay_2_out, or_3_out);
  Delay #(.delayTime(6)) delay_3 (.in(one_time_bit_1_rst), .out(delay_3_out));
  or or_4 (or_4_out, and_4_out, delay_3_out);
  bf_rle_instruction_encoder bf_rle_instruction_encoder_1 (
    .Opc(prev_opc_q), .Count(Repeat_counter_out), .RLEopc(bf_rle_instruction_encoder_1_rleopc));
  CounterPreset #(.Bits(16)) PC_2 (
    .en(and_4_out), .C(or_4_out), .dir(1'b0), .in({16{1'b0}}), .ld(1'b0), .clr(delay_3_out), .out(PC_2_out));  // open: ovf
  and and_5 (and_5_out, comparator_1_eq, one_time_bit_1_exc);
  and and_6 (and_6_out, one_time_bit_1_pc_plus__plus, comparator_1_eq);
  or or_5 (or_5_out, and_6_out, or_6_out);
  or or_6 (or_6_out, one_time_bit_1_rst, and_12_out);
  CounterPreset #(.Bits(16)) PC_3 (
    .en(and_6_out), .C(or_5_out), .dir(1'b0), .in(loops_d[15:0]), .ld(or_6_out), .clr(1'b0), .out(PC_3_out));  // open: ovf
  Comparator #(.Bits(16)) comparator_4 (.a(PC_3_out), .b(PC_2_out), .eq(comparator_4_eq));  // open: gt, lt
  or or_7 (or_7_out, one_time_bit_1_rst, and_6_out);
  _16b_register _16b_register_1 (.S(or_7_out), .V(PC_3_out), .X(_16b_register_1_x));
  and and_7 (and_7_out, comparator_4_eq, comparator_1_eq);
  ram_input_selector ram_input_selector_1 (
    .A2(_16b_register_1_x), .D2({8{1'b0}}), .str2(1'b0), .C2(and_5_out), .ld2(and_5_out),
    .Go2(comparator_1_eq), .A1(PC_2_out), .D1(bf_rle_instruction_encoder_1_rleopc), .str1(and_4_out),
    .C1(and_4_out), .ld1(1'b1), .A(ram_input_selector_1_a), .D(ram_input_selector_1_d),
    .str(ram_input_selector_1_str), .C(ram_input_selector_1_c), .ld(ram_input_selector_1_ld));
  Break #(.Cycles(100000000)) break_1 (.brk(and_7_out));
  and and_8 (and_8_out, comparator_1_eq, and_5_out);
  RAMDualPort #(.AddrBits(16), .Bits(8)) RLE_program (
    .A(ram_input_selector_1_a), .Din(ram_input_selector_1_d), .str(ram_input_selector_1_str),
    .C(ram_input_selector_1_c), .ld(ram_input_selector_1_ld), .D(RLE_program_d));
  Delay #(.delayTime(3)) delay_4 (.in(and_8_out), .out(delay_4_out));
  bf_rle_instruction_decoder bf_rle_instruction_decoder_1 (
    .inst(RLE_program_d),
    .Count({bf_rle_instruction_decoder_1_count[15], bf_rle_instruction_decoder_1_count[6:0]}),
    .plus(bf_rle_instruction_decoder_1_plus), .out_4(bf_rle_instruction_decoder_1_out_4),
    .gt(bf_rle_instruction_decoder_1_gt), .lt(bf_rle_instruction_decoder_1_lt),
    .out_7(bf_rle_instruction_decoder_1_out_7), .out_8(bf_rle_instruction_decoder_1_out_8),
    .out_9(bf_rle_instruction_decoder_1_out_9), .out_10(bf_rle_instruction_decoder_1_out_10));
  _8x1_and _8x1_and_1 (
    .A0(bf_rle_instruction_decoder_1_plus), .A1(bf_rle_instruction_decoder_1_out_4),
    .A2(bf_rle_instruction_decoder_1_gt), .A3(bf_rle_instruction_decoder_1_lt),
    .A4(bf_rle_instruction_decoder_1_out_7), .A5(bf_rle_instruction_decoder_1_out_8),
    .A6(bf_rle_instruction_decoder_1_out_9), .A7(bf_rle_instruction_decoder_1_out_10), .AND(delay_4_out),
    .X0(_8x1_and_1_x0), .X1(_8x1_and_1_x1), .X2(_8x1_and_1_x2), .X3(_8x1_and_1_x3), .X4(_8x1_and_1_x4),
    .X5(_8x1_and_1_x5), .X6(_8x1_and_1_x6), .X7(_8x1_and_1_x7));
  and and_9 (and_9_out, or_8_out, _1b_ram_1_q);
  or or_8 (or_8_out, _8x1_and_1_x2, _8x1_and_1_x3);
  CounterPreset #(.Bits(16)) mem_ptr (
    .en(1'b0), .C(and_9_out), .dir(1'b0), .in(add_1_s), .ld(1'b1), .clr(1'b0), .out(mem_ptr_out),
    .ovf(mem_ptr_ovf));
  Add #(.Bits(16)) add_1 (
    .a(mem_ptr_out),
    .b({{9{bf_rle_instruction_decoder_1_count[15]}}, bf_rle_instruction_decoder_1_count[6:0]}), .c_i(1'b0),
    .s(add_1_s));  // open: c_o
  Delay #(.delayTime(2)) delay_5 (.in(and_9_out), .out(delay_5_out));
  and and_10 (and_10_out, or_9_out, _1b_ram_1_q);
  or or_9 (or_9_out, _8x1_and_1_x0, _8x1_and_1_x1);
  or or_10 (or_10_out, and_10_out, delay_5_out);
  Multiplexer #(.Bits(8)) multiplexer_1 (.sel(and_10_out), .in_0(memory_d), .in_1(add_2_s), .out(multiplexer_1_out));
  or or_11 (or_11_out, one_time_bit_1_rst, and_10_out);
  CounterPreset #(.Bits(8)) current_byte (
    .en(1'b0), .C(or_10_out), .dir(1'b0), .in(multiplexer_1_out), .ld(1'b1), .clr(1'b0), .out(Chr));  // open: ovf
  Add #(.Bits(8)) add_2 (
    .a(Chr), .b({bf_rle_instruction_decoder_1_count[15], bf_rle_instruction_decoder_1_count[6:0]}),
    .c_i(1'b0), .s(add_2_s));  // open: c_o
  Delay #(.delayTime(3)) delay_6 (.in(or_11_out), .out(delay_6_out));
  and and_11 (Out, _1b_ram_1_q, _8x1_and_1_x6);
  _8b_or _8b_or_2 (.\byte (Chr), .\or (_8b_or_2_or));
  RAMDualPort #(.AddrBits(16), .Bits(8)) memory (
    .A(mem_ptr_out), .Din(Chr), .str(delay_6_out), .C(delay_6_out), .ld(1'b1), .D(memory_d));
  Break #(.Cycles(1000000000)) break_2 (.brk(Out));
  and and_12 (and_12_out, and_13_out, _8b_or_2_or);
  and and_13 (and_13_out, _8x1_and_1_x5, _1b_ram_1_q);
  and and_14 (and_14_out, not_4_out, _8x1_and_1_x5);
  not not_4 (not_4_out, _8b_or_2_or);
  or or_12 (or_12_out, _8x1_and_1_x4, and_14_out);
  CounterPreset #(.Bits(16)) loop_ptr (
    .en(or_12_out), .C(or_12_out), .dir(and_14_out), .in({16{1'b0}}), .ld(1'b0), .clr(1'b0),
    .out(loop_ptr_out));  // open: ovf
  or or_13 (or_13_out[16], one_time_bit_1_rst, _8b_or_2_or);
  Delay #(.delayTime(3)) delay_7 (.in(one_time_bit_1_rst), .out(delay_7_out));
  or or_14 (or_14_out, delay_7_out, delay_8_out);
  Delay #(.delayTime(3)) delay_8 (.in(_8x1_and_1_x4), .out(delay_8_out));
  RAMDualPort #(.AddrBits(16), .Bits(17)) loops (
    .A(loop_ptr_out), .Din({or_13_out[16], _16b_register_1_x}), .str(or_14_out), .C(or_14_out), .ld(1'b1),
    .D(loops_d));
  _1b_ram _1b_ram_1 (.V(loops_d[16]), .S(or_15_out), .Q(_1b_ram_1_q));  // open: NQ
  or or_15 (or_15_out, one_time_bit_1_rst, and_6_out);

  // Notes on the sheet:
  //   RLE compressor
  //   ASCII reminder
  //   0x2B +
  //   0x2D -
  //   0x3E >
  //   0x3C <
  //   0x5B [
  //   0x5D ]
  //   0x2E .
  //   0x2C ,
  //   0x23 #
  //   not EOF
  //   Reset
  //   PC++
  //   Exec
  //   Program iterator
  //   contents of BF_Program (hex, n*v repeats v):
  //   2b,2b,2b,2b,2b,2b,2b,2b,2b,2b,2b,2b,2b,5b,2d,3e,2b,2b,3e,3e,3e,2b,2b,2b,2b,2b,3e,
  //   2b,2b,3e,2b,3c,3c,3c,3c,3c,3c,5d,3e,3e,3e,3e,3e,2b,2b,2b,2b,2b,2b,3e,2d,2d,2d,3e,
  //   3e,3e,3e,3e,3e,3e,3e,3e,3e,2b,2b,2b,2b,2b,2b,2b,2b,2b,2b,2b,2b,2b,2b,2b,5b,5b,a,3e,
  //   3e,3e,3e,3e,3e,3e,3e,3e,5d,2b,5b,3c,3c,3c,3c,3c,3c,3c,3c,3c,5d,3e,3e,3e,3e,3e,3e,
  //   3e,3e,3e,2d,5d,2b,5b,3e,3e,3e,3e,3e,3e,3e,3e,5b,2d,5d,3e,5d,3c,3c,3c,3c,3c,3c,3c,
  //   3c,3c,5b,3c,3c,3c,3c,3c,3c,3c,3c,3c,5d,3e,3e,3e,3e,3e,3e,3e,3e,5b,2d,5d,2b,a,3c,3c,
  //   3c,3c,3c,3c,3c,2b,2b,2b,2b,2b,5b,2d,5b,2d,3e,3e,3e,3e,3e,3e,3e,3e,3e,2b,3c,3c,3c,
  //   3c,3c,3c,3c,3c,3c,5d,3e,3e,3e,3e,3e,3e,3e,3e,3e,5d,3e,3e,3e,3e,3e,3e,3e,2b,3e,3e,
  //   3e,3e,3e,3e,3e,3e,3e,3e,3e,3e,3e,3e,3e,3e,3e,3e,3e,3e,3e,3e,3e,3e,3e,3e,a,3e,2b,3c,
  //   3c,3c,3c,3c,3c,3c,3c,3c,3c,3c,3c,3c,3c,3c,3c,3c,5b,3c,3c,3c,3c,3c,3c,3c,3c,3c,5d,
  //   3e,3e,3e,5b,2d,5d,2b,5b,3e,3e,3e,3e,3e,3e,5b,3e,3e,3e,3e,3e,3e,3e,5b,2d,5d,3e,3e,
  //   5d,3c,3c,3c,3c,3c,3c,3c,3c,3c,5b,3c,3c,3c,3c,3c,3c,3c,3c,3c,5d,3e,3e,a,3e,3e,3e,3e,
  //   3e,5b,2d,5d,2b,3c,3c,3c,3c,3c,3c,2b,2b,2b,2b,5b,2d,5b,2d,3e,3e,3e,3e,3e,3e,3e,3e,
  //   3e,2b,3c,3c,3c,3c,3c,3c,3c,3c,3c,5d,3e,3e,3e,3e,3e,3e,3e,3e,3e,5d,3e,3e,3e,3e,3e,
  //   3e,2b,3c,3c,3c,3c,3c,3c,2b,2b,2b,2b,2b,2b,2b,5b,2d,5b,2d,3e,3e,3e,a,3e,3e,3e,3e,3e,
  //   3e,2b,3c,3c,3c,3c,3c,3c,3c,3c,3c,5d,3e,3e,3e,3e,3e,3e,3e,3e,3e,5d,3e,3e,3e,3e,3e,
  //   3e,2b,3c,3c,3c,3c,3c,3c,3c,3c,3c,3c,3c,3c,3c,3c,3c,3c,5b,3c,3c,3c,3c,3c,3c,3c,3c,
  //   3c,5d,3e,3e,3e,5b,5b,2d,5d,3e,3e,3e,3e,3e,3e,5b,3e,3e,3e,3e,3e,a,3e,3e,5b,2d,3c,3c,
  //   3c,3c,3c,3c,2b,3e,3e,3e,3e,3e,3e,5d,3c,3c,3c,3c,3c,3c,5b,2d,3e,3e,3e,3e,3e,3e,2b,
  //   3c,3c,2b,3c,3c,3c,2b,3c,5d,3e,3e,3e,3e,3e,3e,3e,3e,5d,3c,3c,3c,3c,3c,3c,3c,3c,3c,
  //   5b,3c,3c,3c,3c,3c,3c,3c,3c,3c,5d,3e,3e,3e,3e,3e,3e,3e,3e,3e,a,5b,3e,3e,3e,3e,3e,3e,
  //   3e,3e,5b,2d,3c,3c,3c,3c,3c,3c,3c,2b,3e,3e,3e,3e,3e,3e,3e,5d,3c,3c,3c,3c,3c,3c,3c,
  //   5b,2d,3e,3e,3e,3e,3e,3e,3e,2b,3c,3c,2b,3c,3c,3c,2b,3c,3c,5d,3e,3e,3e,3e,3e,3e,3e,
  //   3e,5d,3c,3c,3c,3c,3c,3c,3c,3c,3c,5b,3c,3c,3c,3c,3c,3c,3c,a,3c,3c,5d,3e,3e,3e,3e,3e,
  //   3e,3e,5b,2d,3c,3c,3c,3c,3c,3c,3c,2b,3e,3e,3e,3e,3e,3e,3e,5d,3c,3c,3c,3c,3c,3c,3c,
  //   5b,2d,3e,3e,3e,3e,3e,3e,3e,2b,3c,3c,2b,3c,3c,3c,3c,3c,5d,3e,3e,3e,3e,3e,3e,3e,3e,
  //   3e,2b,2b,2b,2b,2b,2b,2b,2b,2b,2b,2b,2b,2b,2b,2b,5b,5b,a,3e,3e,3e,3e,3e,3e,3e,3e,3e,
  //   5d,2b,3e,5b,2d,5d,3e,5b,2d,5d,3e,5b,2d,5d,3e,5b,2d,5d,3e,5b,2d,5d,3e,5b,2d,5d,3e,
  //   5b,2d,5d,3e,5b,2d,5d,3e,5b,2d,5d,3c,3c,3c,3c,3c,3c,3c,3c,3c,5b,3c,3c,3c,3c,3c,3c,
  //   3c,3c,3c,5d,3e,3e,3e,3e,3e,3e,3e,3e,3e,2d,5d,2b,5b,a,3e,2b,3e,3e,3e,3e,3e,3e,3e,3e,
  //   5d,3c,3c,3c,3c,3c,3c,3c,3c,3c,5b,3c,3c,3c,3c,3c,3c,3c,3c,3c,5d,3e,3e,3e,3e,3e,3e,
  //   3e,3e,3e,5b,3e,2d,3e,3e,3e,3e,5b,2d,3c,3c,3c,3c,2b,3e,3e,3e,3e,5d,3c,3c,3c,3c,5b,
  //   2d,3e,3e,3e,3e,2b,3c,3c,3c,3c,3c,5b,2d,3e,3e,5b,a,2d,3c,3c,2b,3e,3e,5d,3c,3c,5b,2d,
  //   3e,3e,2b,3e,3e,2b,3c,3c,3c,3c,5d,2b,3e,3e,3e,3e,3e,3e,3e,3e,3e,5d,3c,3c,3c,3c,3c,
  //   3c,3c,3c,5b,3c,3c,3c,3c,3c,3c,3c,3c,3c,5d,5d,3e,3e,3e,3e,3e,3e,3e,3e,3e,5b,3e,3e,
  //   3e,3e,3e,3e,3e,3e,3e,5d,3c,3c,3c,3c,3c,3c,3c,a,3c,3c,5b,3e,5b,2d,3e,3e,3e,3e,3e,3e,
  //   3e,3e,3e,2b,3c,3c,3c,3c,3c,3c,3c,3c,3c,5d,3c,3c,3c,3c,3c,3c,3c,3c,3c,3c,5d,3e,5b,
  //   2d,3e,3e,3e,3e,3e,3e,3e,3e,3e,2b,3c,3c,3c,3c,3c,3c,3c,3c,3c,5d,3c,2b,3e,3e,3e,3e,
  //   3e,3e,3e,3e,5d,3c,3c,3c,3c,3c,3c,3c,3c,3c,a,5b,3e,5b,2d,5d,3c,2d,3e,3e,3e,3e,5b,2d,
  //   3c,3c,3c,3c,2b,3e,5b,3c,2d,3e,2d,3c,3c,3c,3c,3c,3c,2b,3e,3e,3e,3e,3e,3e,5d,3c,5b,
  //   2d,3e,2b,3c,5d,3e,3e,3e,3e,5d,3c,3c,3c,5b,2d,3e,3e,3e,2b,3c,3c,3c,5d,3c,2b,3c,3c,
  //   3c,3c,3c,3c,3c,3c,3c,5d,3e,3e,3e,3e,3e,a,3e,3e,3e,3e,5b,3e,2b,3e,3e,3e,3e,3e,3e,3e,
  //   3e,5d,3c,3c,3c,3c,3c,3c,3c,3c,3c,5b,3c,3c,3c,3c,3c,3c,3c,3c,3c,5d,3e,3e,3e,3e,3e,
  //   3e,3e,3e,3e,5b,3e,2d,3e,3e,3e,3e,3e,5b,2d,3c,3c,3c,3c,3c,2b,3e,3e,3e,3e,3e,5d,3c,
  //   3c,3c,3c,3c,5b,2d,3e,3e,3e,3e,3e,2b,a,3c,3c,3c,3c,3c,3c,5b,2d,3e,3e,3e,5b,2d,3c,3c,
  //   3c,2b,3e,3e,3e,5d,3c,3c,3c,5b,2d,3e,3e,3e,2b,3e,2b,3c,3c,3c,3c,5d,2b,3e,3e,3e,3e,
  //   3e,3e,3e,3e,3e,5d,3c,3c,3c,3c,3c,3c,3c,3c,5b,3c,3c,3c,3c,3c,3c,3c,3c,3c,5d,5d,3e,
  //   3e,3e,3e,3e,3e,3e,3e,3e,5b,3e,3e,a,3e,3e,3e,3e,3e,3e,3e,5d,3c,3c,3c,3c,3c,3c,3c,3c,
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  //   RLE opcodes:
  //   00000000 [
  //   00...001 +
  //   00...010 ++
  //   00...011 +++
  //   00...100
  //   00...101
  //   00...110
  //   00...111
  //   01000000 ]
  //   01...001
  //   01...010
  //   01...011
  //   01...100
  //   01...101 <<<
  //   01...110 <<
  //   01...111 <
  //   10000000 ,
  //   10...001 >
  //   10...010 >>
  //   10...011 >>>
  //   10...100
  //   10...101
  //   10...110
  //   10...111
  //   11000000 .
  //   11...001
  //   11...010
  //   11...011
  //   11...100
  //   11...101 ---
  //   11...110 --
  //   11...111 -
  //   Clock2
  //   Clock1
  //   Opcode
  //   contents of ascii_2_opcode (hex, n*v repeats v):
  //   2,1,1,1,1,1,1,1,1,1,1,1,1,1,1,1,1,1,1,1,1,1,1,1,1,1,1,1,1,1,1,1,1,1,1,1,1,1,1,1,1,
  //   1,1,2b,80,2d,c0,1,1,1,1,1,1,1,1,1,1,1,1,1,3c,1,3e,1,1,1,1,1,1,1,1,1,1,1,1,1,1,1,1,
  //   1,1,1,1,1,1,1,1,1,1,1,1,0,1,40,1,1,1,1,1,1,1,1,1,1,1,1,1,1,1,1,1,1,1,1,1,1,1,1,1,
  //   1,1,1,1,1,1,1,1,1,1,1,1,1,1,1,1,1,1,1,1,1,1,1,1,1,1,1,1,1,1,1,1,1,1,1,1,1,1,1,1,1,
  //   1,1,1,1,1,1,1,1,1,1,1,1,1,1,1,1,1,1,1,1,1,1,1,1,1,1,1,1,1,1,1,1,1,1,1,1,1,1,1,1,1,
  //   1,1,1,1,1,1,1,1,1,1,1,1,1,1,1,1,1,1,1,1,1,1,1,1,1,1,1,1,1,1,1,1,1,1,1,1,1,1,1,1,1,
  //   1,1,1,1,1,1,1,1,1,1,1,1,1,1
  //   previous opcode
  //   contents of rom_1 (hex, n*v repeats v):
  //   1,0,0,0,0,0,0,0,0,0,0,0,0,0,0,0,0,0,0,0,0,0,0,0,0,0,0,0,0,0,0,0,0,0,0,0,0,0,0,0,0,
  //   0,0,0,0,0,0,0,0,0,0,0,0,0,0,0,0,0,0,0,0,0,0,0,1,0,0,0,0,0,0,0,0,0,0,0,0,0,0,0,0,0,
  //   0,0,0,0,0,0,0,0,0,0,0,0,0,0,0,0,0,0,0,0,0,0,0,0,0,0,0,0,0,0,0,0,0,0,0,0,0,0,0,0,0,
  //   0,0,0,0,0,1,0,0,0,0,0,0,0,0,0,0,0,0,0,0,0,0,0,0,0,0,0,0,0,0,0,0,0,0,0,0,0,0,0,0,0,
  //   0,0,0,0,0,0,0,0,0,0,0,0,0,0,0,0,0,0,0,0,0,0,0,0,0,0,0,0,1
  //   not RLE opcode
  //   prev opcode is valid
  //   opcode changed
  //   EOF
  //   RLE max capacity
  //   write that opcode
  //   and start from zero
  //   Compression finished
  //   CPU
  //   Exc
  //   jmp address for end while
  //   jmp back to while address
  //   Convert 8b to 16b
  //   by extending sign
  //   TODO(,)
  //   Reset line
  //   current byte != 0
  //   end of while
  //   ]
  //   [
  //   Execute instruction?
  //   Execute loop?
endmodule
