// Digital circuit bf_instruction_decoder.dig as structural Verilog
module bf_instruction_decoder (
  input  [7:0] inst,
  output plus,
  output out_3,
  output gt,
  output lt,
  output out_6,
  output out_7,
  output out_8,
  output out_9,
  output Stop,
  output Brk
);

  LookUpTable #(.Bits(10)) lookuptable_1 (
    .in0(inst[0]), .in1(inst[1]), .in2(inst[2]), .in3(inst[3]), .in4(inst[4]), .in5(inst[5]), .in6(inst[6]),
    .in7(inst[7]), .out({Brk, Stop, out_9, out_8, out_7, out_6, lt, gt, out_3, plus}));
  PullUp #(.Bits(8)) pullup_1 (.out(inst));

  // Notes on the sheet:
  //   contents of lookuptable_1 (hex, n*v repeats v):
  //   100,1000,0,1000,1000,1000,1000,1000,1000,1000,1000,1000,1000,1000,1000,1000,1000,
  //   1000,1000,0,0,0,0,0,0,0,0,0,0,0,0,0,0,0,0,200,0,0,0,0,0,0,0,1,80,2,40,0,0,0,0,0,0,
  //   0,0,0,0,0,0,0,8,0,4,0,0,0,0,0,0,0,0,0,0,0,0,0,0,0,0,0,0,0,0,0,0,0,0,0,0,0,0,10,0,
  //   20
endmodule
