// Digital circuit bf_preprocessing_cpu_module_w_console.dig as structural Verilog
module bf_preprocessing_cpu_module_w_console (
  input  Clock
);

  wire bf_cpu_with_preprocessor_module_1_end, bf_cpu_with_preprocessor_module_1_out,
       bf_cpu_with_preprocessor_module_1_pc_plus__plus;
  wire [7:0] bf_cpu_with_preprocessor_module_1_chr, Program_d;
  wire [15:0] bf_cpu_with_preprocessor_module_1_addr;

  bf_cpu_with_preprocessor_module bf_cpu_with_preprocessor_module_1 (
    .Clk(Clock), .Opcode(Program_d), .Chr(bf_cpu_with_preprocessor_module_1_chr),
    .Out(bf_cpu_with_preprocessor_module_1_out), .Addr(bf_cpu_with_preprocessor_module_1_addr),
    .PC_plus__plus(bf_cpu_with_preprocessor_module_1_pc_plus__plus),
    .End(bf_cpu_with_preprocessor_module_1_end));  // open: Rst
  EEPROMDualPort #(.AddrBits(16), .isProgramMemory("true"), .Bits(8)) Program (
    .A(bf_cpu_with_preprocessor_module_1_addr), .Din({8{1'b0}}), .str(1'b0),
    .C(bf_cpu_with_preprocessor_module_1_pc_plus__plus), .ld(1'b1), .D(Program_d));
  Break #(.Cycles(100000000)) break_1 (.brk(bf_cpu_with_preprocessor_module_1_end));
  Terminal #(.termWidth(132), .termHeight(50)) terminal_1 (
    .D(bf_cpu_with_preprocessor_module_1_chr), .C(bf_cpu_with_preprocessor_module_1_out), .en(1'b1));

  // Notes on the sheet:
  //   Clock: Hz: 10000000
  //   contents of Program (hex, n*v repeats v):
  //   2b,2b,2b,2b,2b,2b,2b,2b,2b,2b,2b,2b,2b,5b,2d,3e,2b,2b,3e,3e,3e,2b,2b,2b,2b,2b,3e,
  //   2b,2b,3e,2b,3c,3c,3c,3c,3c,3c,5d,3e,3e,3e,3e,3e,2b,2b,2b,2b,2b,2b,3e,2d,2d,2d,3e,
  //   3e,3e,3e,3e,3e,3e,3e,3e,3e,2b,2b,2b,2b,2b,2b,2b,2b,2b,2b,2b,2b,2b,2b,2b,5b,5b,3e,
  //   3e,3e,3e,3e,3e,3e,3e,3e,5d,2b,5b,3c,3c,3c,3c,3c,3c,3c,3c,3c,5d,3e,3e,3e,3e,3e,3e,
  //   3e,3e,3e,2d,5d,2b,5b,3e,3e,3e,3e,3e,3e,3e,3e,5b,2d,5d,3e,5d,3c,3c,3c,3c,3c,3c,3c,
  //   3c,3c,5b,3c,3c,3c,3c,3c,3c,3c,3c,3c,5d,3e,3e,3e,3e,3e,3e,3e,3e,5b,2d,5d,2b,3c,3c,
  //   3c,3c,3c,3c,3c,2b,2b,2b,2b,2b,5b,2d,5b,2d,3e,3e,3e,3e,3e,3e,3e,3e,3e,2b,3c,3c,3c,
  //   3c,3c,3c,3c,3c,3c,5d,3e,3e,3e,3e,3e,3e,3e,3e,3e,5d,3e,3e,3e,3e,3e,3e,3e,2b,3e,3e,
  //   3e,3e,3e,3e,3e,3e,3e,3e,3e,3e,3e,3e,3e,3e,3e,3e,3e,3e,3e,3e,3e,3e,3e,3e,3e,2b,3c,
  //   3c,3c,3c,3c,3c,3c,3c,3c,3c,3c,3c,3c,3c,3c,3c,3c,5b,3c,3c,3c,3c,3c,3c,3c,3c,3c,5d,
  //   3e,3e,3e,5b,2d,5d,2b,5b,3e,3e,3e,3e,3e,3e,5b,3e,3e,3e,3e,3e,3e,3e,5b,2d,5d,3e,3e,
  //   5d,3c,3c,3c,3c,3c,3c,3c,3c,3c,5b,3c,3c,3c,3c,3c,3c,3c,3c,3c,5d,3e,3e,3e,3e,3e,3e,
  //   3e,5b,2d,5d,2b,3c,3c,3c,3c,3c,3c,2b,2b,2b,2b,5b,2d,5b,2d,3e,3e,3e,3e,3e,3e,3e,3e,
  //   3e,2b,3c,3c,3c,3c,3c,3c,3c,3c,3c,5d,3e,3e,3e,3e,3e,3e,3e,3e,3e,5d,3e,3e,3e,3e,3e,
  //   3e,2b,3c,3c,3c,3c,3c,3c,2b,2b,2b,2b,2b,2b,2b,5b,2d,5b,2d,3e,3e,3e,3e,3e,3e,3e,3e,
  //   3e,2b,3c,3c,3c,3c,3c,3c,3c,3c,3c,5d,3e,3e,3e,3e,3e,3e,3e,3e,3e,5d,3e,3e,3e,3e,3e,
  //   3e,2b,3c,3c,3c,3c,3c,3c,3c,3c,3c,3c,3c,3c,3c,3c,3c,3c,5b,3c,3c,3c,3c,3c,3c,3c,3c,
  //   3c,5d,3e,3e,3e,5b,5b,2d,5d,3e,3e,3e,3e,3e,3e,5b,3e,3e,3e,3e,3e,3e,3e,5b,2d,3c,3c,
  //   3c,3c,3c,3c,2b,3e,3e,3e,3e,3e,3e,5d,3c,3c,3c,3c,3c,3c,5b,2d,3e,3e,3e,3e,3e,3e,2b,
  //   3c,3c,2b,3c,3c,3c,2b,3c,5d,3e,3e,3e,3e,3e,3e,3e,3e,5d,3c,3c,3c,3c,3c,3c,3c,3c,3c,
  //   5b,3c,3c,3c,3c,3c,3c,3c,3c,3c,5d,3e,3e,3e,3e,3e,3e,3e,3e,3e,5b,3e,3e,3e,3e,3e,3e,
  //   3e,3e,5b,2d,3c,3c,3c,3c,3c,3c,3c,2b,3e,3e,3e,3e,3e,3e,3e,5d,3c,3c,3c,3c,3c,3c,3c,
  //   5b,2d,3e,3e,3e,3e,3e,3e,3e,2b,3c,3c,2b,3c,3c,3c,2b,3c,3c,5d,3e,3e,3e,3e,3e,3e,3e,
  //   3e,5d,3c,3c,3c,3c,3c,3c,3c,3c,3c,5b,3c,3c,3c,3c,3c,3c,3c,3c,3c,5d,3e,3e,3e,3e,3e,
  //   3e,3e,5b,2d,3c,3c,3c,3c,3c,3c,3c,2b,3e,3e,3e,3e,3e,3e,3e,5d,3c,3c,3c,3c,3c,3c,3c,
  //   5b,2d,3e,3e,3e,3e,3e,3e,3e,2b,3c,3c,2b,3c,3c,3c,3c,3c,5d,3e,3e,3e,3e,3e,3e,3e,3e,
  //   3e,2b,2b,2b,2b,2b,2b,2b,2b,2b,2b,2b,2b,2b,2b,2b,5b,5b,3e,3e,3e,3e,3e,3e,3e,3e,3e,
  //   5d,2b,3e,5b,2d,5d,3e,5b,2d,5d,3e,5b,2d,5d,3e,5b,2d,5d,3e,5b,2d,5d,3e,5b,2d,5d,3e,
  //   5b,2d,5d,3e,5b,2d,5d,3e,5b,2d,5d,3c,3c,3c,3c,3c,3c,3c,3c,3c,5b,3c,3c,3c,3c,3c,3c,
  //   3c,3c,3c,5d,3e,3e,3e,3e,3e,3e,3e,3e,3e,2d,5d,2b,5b,3e,2b,3e,3e,3e,3e,3e,3e,3e,3e,
  //   5d,3c,3c,3c,3c,3c,3c,3c,3c,3c,5b,3c,3c,3c,3c,3c,3c,3c,3c,3c,5d,3e,3e,3e,3e,3e,3e,
  //   3e,3e,3e,5b,3e,2d,3e,3e,3e,3e,5b,2d,3c,3c,3c,3c,2b,3e,3e,3e,3e,5d,3c,3c,3c,3c,5b,
  //   2d,3e,3e,3e,3e,2b,3c,3c,3c,3c,3c,5b,2d,3e,3e,5b,2d,3c,3c,2b,3e,3e,5d,3c,3c,5b,2d,
  //   3e,3e,2b,3e,3e,2b,3c,3c,3c,3c,5d,2b,3e,3e,3e,3e,3e,3e,3e,3e,3e,5d,3c,3c,3c,3c,3c,
  //   3c,3c,3c,5b,3c,3c,3c,3c,3c,3c,3c,3c,3c,5d,5d,3e,3e,3e,3e,3e,3e,3e,3e,3e,5b,3e,3e,
  //   3e,3e,3e,3e,3e,3e,3e,5d,3c,3c,3c,3c,3c,3c,3c,3c,3c,5b,3e,5b,2d,3e,3e,3e,3e,3e,3e,
  //   3e,3e,3e,2b,3c,3c,3c,3c,3c,3c,3c,3c,3c,5d,3c,3c,3c,3c,3c,3c,3c,3c,3c,3c,5d,3e,5b,
  //   2d,3e,3e,3e,3e,3e,3e,3e,3e,3e,2b,3c,3c,3c,3c,3c,3c,3c,3c,3c,5d,3c,2b,3e,3e,3e,3e,
  //   3e,3e,3e,3e,5d,3c,3c,3c,3c,3c,3c,3c,3c,3c,5b,3e,5b,2d,5d,3c,2d,3e,3e,3e,3e,5b,2d,
  //   3c,3c,3c,3c,2b,3e,5b,3c,2d,3e,2d,3c,3c,3c,3c,3c,3c,2b,3e,3e,3e,3e,3e,3e,5d,3c,5b,
  //   2d,3e,2b,3c,5d,3e,3e,3e,3e,5d,3c,3c,3c,5b,2d,3e,3e,3e,2b,3c,3c,3c,5d,3c,2b,3c,3c,
  //   3c,3c,3c,3c,3c,3c,3c,5d,3e,3e,3e,3e,3e,3e,3e,3e,3e,5b,3e,2b,3e,3e,3e,3e,3e,3e,3e,
  //   3e,5d,3c,3c,3c,3c,3c,3c,3c,3c,3c,5b,3c,3c,3c,3c,3c,3c,3c,3c,3c,5d,3e,3e,3e,3e,3e,
  //   3e,3e,3e,3e,5b,3e,2d,3e,3e,3e,3e,3e,5b,2d,3c,3c,3c,3c,3c,2b,3e,3e,3e,3e,3e,5d,3c,
  //   3c,3c,3c,3c,5b,2d,3e,3e,3e,3e,3e,2b,3c,3c,3c,3c,3c,3c,5b,2d,3e,3e,3e,5b,2d,3c,3c,
  //   3c,2b,3e,3e,3e,5d,3c,3c,3c,5b,2d,3e,3e,3e,2b,3e,2b,3c,3c,3c,3c,5d,2b,3e,3e,3e,3e,
  //   3e,3e,3e,3e,3e,5d,3c,3c,3c,3c,3c,3c,3c,3c,5b,3c,3c,3c,3c,3c,3c,3c,3c,3c,5d,5d,3e,
  //   3e,3e,3e,3e,3e,3e,3e,3e,5b,3e,3e,3e,3e,3e,3e,3e,3e,3e,5d,3c,3c,3c,3c,3c,3c,3c,3c,
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endmodule
