// Digital circuit bf_rle_instruction_decoder.dig as structural Verilog
module bf_rle_instruction_decoder (
  input  [7:0] inst,
  output [7:0] Count,
  output plus,
  output out_4,
  output gt,
  output lt,
  output out_7,
  output out_8,
  output out_9,
  output out_10
);

  PullUp #(.Bits(8)) pullup_1 (.out(inst));
  LookUpTable #(.Bits(8)) lookuptable_1 (
    .in0(inst[0]), .in1(inst[1]), .in2(inst[2]), .in3(inst[3]), .in4(inst[4]), .in5(inst[5]), .in6(inst[6]),
    .in7(inst[7]), .out({out_10, out_9, out_8, out_7, lt, gt, out_4, plus}));

  assign Count = {{2{inst[6]}}, inst[5:0]};

  // Notes on the sheet:
  //   contents of lookuptable_1 (hex, n*v repeats v):
  //   10,1,1,1,1,1,1,1,1,1,1,1,1,1,1,1,1,1,1,1,1,1,1,1,1,1,1,1,1,1,1,1,1,1,1,1,1,1,1,1,
  //   1,1,1,1,1,1,1,1,1,1,1,1,1,1,1,1,1,1,1,1,1,1,1,1,20,8,8,8,8,8,8,8,8,8,8,8,8,8,8,8,
  //   8,8,8,8,8,8,8,8,8,8,8,8,8,8,8,8,8,8,8,8,8,8,8,8,8,8,8,8,8,8,8,8,8,8,8,8,8,8,8,8,8,
  //   8,8,8,8,8,8,8,80,4,4,4,4,4,4,4,4,4,4,4,4,4,4,4,4,4,4,4,4,4,4,4,4,4,4,4,4,4,4,4,4,
  //   4,4,4,4,4,4,4,4,4,4,4,4,4,4,4,4,4,4,4,4,4,4,4,4,4,4,4,4,4,4,4,40,2,2,2,2,2,2,2,2,
  //   2,2,2,2,2,2,2,2,2,2,2,2,2,2,2,2,2,2,2,2,2,2,2,2,2,2,2,2,2,2,2,2,2,2,2,2,2,2,2,2,2,
  //   2,2,2,2,2,2,2,2,2,2,2,2,2,2
endmodule
