// Digital circuit bf_rle_instruction_encoder.dig as structural Verilog
module bf_rle_instruction_encoder (
  input  [7:0] Opc,
  input  [7:0] Count,
  output [7:0] RLEopc
);

  wire comparator_1_eq, comparator_2_eq, comparator_3_eq, comparator_4_eq, comparator_5_eq, comparator_6_eq,
       comparator_7_eq, comparator_8_eq, not_1_out, or_1_out;
  wire [7:0] _8x1_and_1_x, _8x1_and_2_x, _8x1_and_3_x, _8x1_and_4_x, _8x1_and_5_x, _8x1_and_6_x, add_1_s,
       or_2_out, sub_1_s, sub_2_s;

  Comparator #(.Bits(8)) comparator_1 (.a(8'hc0), .b(Opc), .eq(comparator_1_eq));  // open: gt, lt
  Comparator #(.Bits(8)) comparator_2 (.a(8'h80), .b(Opc), .eq(comparator_2_eq));  // open: gt, lt
  Comparator #(.Bits(8)) comparator_3 (.a(8'h40), .b(Opc), .eq(comparator_3_eq));  // open: gt, lt
  Comparator #(.Bits(8)) comparator_4 (.a({8{1'b0}}), .b(Opc), .eq(comparator_4_eq));  // open: gt, lt
  Comparator #(.Bits(8)) comparator_5 (.a(8'h2b), .b(Opc), .eq(comparator_5_eq));  // open: gt, lt
  Comparator #(.Bits(8)) comparator_6 (.a(8'h2d), .b(Opc), .eq(comparator_6_eq));  // open: gt, lt
  Comparator #(.Bits(8)) comparator_7 (.a(8'h3e), .b(Opc), .eq(comparator_7_eq));  // open: gt, lt
  Comparator #(.Bits(8)) comparator_8 (.a(8'h3c), .b(Opc), .eq(comparator_8_eq));  // open: gt, lt
  Sub #(.Bits(8)) sub_1 (.a({8{1'b0}}), .b(Count), .c_i(1'b0), .s(sub_1_s));  // open: c_o
  Add #(.Bits(8)) add_1 (.a(Count), .b(8'h80), .c_i(1'b0), .s(add_1_s));  // open: c_o
  Sub #(.Bits(8)) sub_2 (.a(8'hc0), .b(Count), .c_i(1'b0), .s(sub_2_s));  // open: c_o
  or or_1 (or_1_out, comparator_1_eq, comparator_2_eq, comparator_3_eq, comparator_4_eq);
  _8x1_and _8x1_and_1 (.V(Count), .AND(comparator_5_eq), .X(_8x1_and_1_x));
  _8x1_and _8x1_and_2 (.V(sub_1_s), .AND(comparator_6_eq), .X(_8x1_and_2_x));
  _8x1_and _8x1_and_3 (.V(add_1_s), .AND(comparator_7_eq), .X(_8x1_and_3_x));
  _8x1_and _8x1_and_4 (.V(sub_2_s), .AND(comparator_8_eq), .X(_8x1_and_4_x));
  _8x1_and _8x1_and_5 (.V(Opc), .AND(or_1_out), .X(_8x1_and_5_x));
  not not_1 (not_1_out, or_1_out);
  assign or_2_out = _8x1_and_1_x | _8x1_and_2_x | _8x1_and_3_x | _8x1_and_4_x;  // Or or_2, 8 bits wide
  _8x1_and _8x1_and_6 (.V(or_2_out), .AND(not_1_out), .X(_8x1_and_6_x));
  assign RLEopc = _8x1_and_5_x | _8x1_and_6_x;  // Or or_3, 8 bits wide

  // Notes on the sheet:
  //   0x2B +
  //   0x2D -
  //   0x3E >
  //   0x3C <
  //   0x00 [
  //   0x40 ]
  //   0x80 .
  //   0xC0 .
endmodule
