// Digital circuit 16_segm_display_converter.dig as structural Verilog
module _16_segm_display_converter (
  input  [3:0] nibble,
  input  Pwr,
  output [15:0] segs
);

  wire decoder_1_out_0, decoder_1_out_1, decoder_1_out_2, decoder_1_out_3, decoder_1_out_4, decoder_1_out_5,
       decoder_1_out_6, decoder_1_out_7, decoder_1_out_8, decoder_1_out_9, decoder_1_out_10,
       decoder_1_out_11, decoder_1_out_12, decoder_1_out_13, decoder_1_out_14, decoder_1_out_15, or_1_out,
       or_2_out, or_3_out, or_4_out, or_5_out, or_6_out, or_7_out, or_8_out, or_9_out, or_10_out, or_11_out,
       or_12_out, or_13_out, or_14_out, or_15_out, or_16_out, or_17_out, or_18_out, or_19_out, or_20_out,
       or_21_out, or_22_out, or_23_out, or_24_out, or_25_out, or_26_out, or_27_out, or_28_out, or_29_out,
       or_30_out, or_31_out, or_32_out, or_33_out, or_34_out, or_35_out, or_36_out, or_37_out, or_38_out,
       or_39_out, or_40_out, or_41_out, or_42_out, or_43_out, or_44_out, or_45_out, or_46_out, or_47_out,
       or_48_out, or_49_out, or_50_out, or_51_out, or_52_out, or_53_out, or_54_out, or_55_out, or_56_out,
       or_57_out, or_58_out, or_59_out, or_60_out, or_61_out, or_62_out, or_63_out, or_64_out, or_65_out,
       or_66_out, or_67_out, or_68_out, or_69_out, or_70_out, or_71_out, or_72_out, or_73_out, or_74_out,
       or_75_out, or_76_out, or_77_out, or_78_out, or_79_out, or_80_out, or_81_out, or_82_out, or_83_out,
       or_84_out, or_85_out, or_86_out;

  Decoder #(.Selector_Bits(4)) decoder_1 (
    .sel(nibble), .out_0(decoder_1_out_0), .out_1(decoder_1_out_1), .out_2(decoder_1_out_2),
    .out_3(decoder_1_out_3), .out_4(decoder_1_out_4), .out_5(decoder_1_out_5), .out_6(decoder_1_out_6),
    .out_7(decoder_1_out_7), .out_8(decoder_1_out_8), .out_9(decoder_1_out_9), .out_10(decoder_1_out_10),
    .out_11(decoder_1_out_11), .out_12(decoder_1_out_12), .out_13(decoder_1_out_13),
    .out_14(decoder_1_out_14), .out_15(decoder_1_out_15));
  or or_1 (or_1_out, decoder_1_out_15, decoder_1_out_14);
  or or_2 (or_2_out, decoder_1_out_12, decoder_1_out_10);
  or or_3 (or_3_out, decoder_1_out_9, decoder_1_out_8);
  or or_4 (or_4_out, decoder_1_out_7, decoder_1_out_6);
  or or_5 (or_5_out, decoder_1_out_5, decoder_1_out_3);
  or or_6 (or_6_out, decoder_1_out_2, decoder_1_out_0);
  or or_7 (or_7_out, decoder_1_out_13, decoder_1_out_10);
  or or_8 (or_8_out, decoder_1_out_9, decoder_1_out_8);
  or or_9 (or_9_out, decoder_1_out_7, decoder_1_out_4);
  or or_10 (or_10_out, decoder_1_out_3, decoder_1_out_2);
  or or_11 (or_11_out, decoder_1_out_1, decoder_1_out_0);
  or or_12 (or_12_out, decoder_1_out_10, decoder_1_out_9);
  or or_13 (or_13_out, decoder_1_out_8, decoder_1_out_7);
  or or_14 (or_14_out, decoder_1_out_5, decoder_1_out_4);
  or or_15 (or_15_out, decoder_1_out_3, decoder_1_out_6);
  or or_16 (or_16_out, decoder_1_out_1, decoder_1_out_0);
  or or_17 (or_17_out, decoder_1_out_14, decoder_1_out_13);
  or or_18 (or_18_out, decoder_1_out_12, decoder_1_out_9);
  or or_19 (or_19_out, decoder_1_out_8, decoder_1_out_6);
  or or_20 (or_20_out, decoder_1_out_5, decoder_1_out_3);
  or or_21 (or_21_out, decoder_1_out_2, decoder_1_out_0);
  or or_22 (or_22_out, decoder_1_out_14, decoder_1_out_12);
  or or_23 (or_23_out, decoder_1_out_11, decoder_1_out_9);
  or or_24 (or_24_out, decoder_1_out_8, decoder_1_out_6);
  or or_25 (or_25_out, decoder_1_out_5, decoder_1_out_3);
  or or_26 (or_26_out, decoder_1_out_2, decoder_1_out_0);
  or or_27 (or_27_out, decoder_1_out_14, decoder_1_out_12);
  or or_28 (or_28_out, decoder_1_out_11, decoder_1_out_10);
  or or_29 (or_29_out, decoder_1_out_8, decoder_1_out_6);
  or or_30 (or_30_out, decoder_1_out_2, decoder_1_out_0);
  or or_31 (or_31_out, decoder_1_out_14, decoder_1_out_12);
  or or_32 (or_32_out, decoder_1_out_11, decoder_1_out_10);
  or or_33 (or_33_out, decoder_1_out_9, decoder_1_out_8);
  or or_34 (or_34_out, decoder_1_out_6, decoder_1_out_5);
  or or_35 (or_35_out, decoder_1_out_4, decoder_1_out_0);
  or or_36 (or_36_out, decoder_1_out_15, decoder_1_out_14);
  or or_37 (or_37_out, decoder_1_out_11, decoder_1_out_10);
  or or_38 (or_38_out, decoder_1_out_9, decoder_1_out_8);
  or or_39 (or_39_out, decoder_1_out_6, decoder_1_out_5);
  or or_40 (or_40_out, decoder_1_out_4, decoder_1_out_2);
  or or_41 (or_41_out, decoder_1_out_13, decoder_1_out_10);
  or or_42 (or_42_out, decoder_1_out_9, decoder_1_out_8);
  or or_43 (or_43_out, decoder_1_out_7, decoder_1_out_6);
  or or_44 (or_44_out, decoder_1_out_5, decoder_1_out_4);
  or or_45 (or_45_out, decoder_1_out_3, decoder_1_out_2);
  or or_46 (or_46_out, decoder_1_out_13, decoder_1_out_11);
  or or_47 (or_47_out, or_1_out, or_2_out);
  or or_48 (or_48_out, or_3_out, or_4_out);
  or or_49 (or_49_out, or_5_out, or_6_out);
  or or_50 (or_50_out, or_8_out, or_9_out);
  or or_51 (or_51_out, or_10_out, or_11_out);
  or or_52 (or_52_out, decoder_1_out_13, or_12_out);
  or or_53 (or_53_out, or_13_out, or_14_out);
  or or_54 (or_54_out, or_15_out, or_16_out);
  or or_55 (or_55_out, or_18_out, or_19_out);
  or or_56 (or_56_out, or_20_out, or_21_out);
  or or_57 (or_57_out, or_23_out, or_24_out);
  or or_58 (or_58_out, or_25_out, or_26_out);
  or or_59 (or_59_out, or_27_out, or_28_out);
  or or_60 (or_60_out, or_29_out, or_30_out);
  or or_61 (or_61_out, decoder_1_out_15, or_31_out);
  or or_62 (or_62_out, or_32_out, or_33_out);
  or or_63 (or_63_out, or_34_out, or_35_out);
  or or_64 (or_64_out, or_37_out, or_38_out);
  or or_65 (or_65_out, or_39_out, or_40_out);
  or or_66 (or_66_out, decoder_1_out_14, or_41_out);
  or or_67 (or_67_out, or_42_out, or_43_out);
  or or_68 (or_68_out, or_44_out, or_45_out);
  or or_69 (or_69_out, or_48_out, or_49_out);
  or or_70 (or_70_out, or_50_out, or_51_out);
  or or_71 (or_71_out, or_53_out, or_54_out);
  or or_72 (or_72_out, or_55_out, or_56_out);
  or or_73 (or_73_out, or_57_out, or_58_out);
  or or_74 (or_74_out, or_59_out, or_60_out);
  or or_75 (or_75_out, or_62_out, or_63_out);
  or or_76 (or_76_out, or_64_out, or_65_out);
  or or_77 (or_77_out, or_67_out, or_68_out);
  or or_78 (or_78_out, or_47_out, or_69_out);
  or or_79 (or_79_out, or_7_out, or_70_out);
  or or_80 (or_80_out, or_52_out, or_71_out);
  or or_81 (or_81_out, or_17_out, or_72_out);
  or or_82 (or_82_out, or_22_out, or_73_out);
  or or_83 (or_83_out, decoder_1_out_15, or_74_out);
  or or_84 (or_84_out, or_61_out, or_75_out);
  or or_85 (or_85_out, or_36_out, or_76_out);
  or or_86 (or_86_out, or_66_out, or_77_out);
  and and_1 (segs[1], Pwr, or_78_out);
  and and_2 (segs[2], Pwr, or_79_out);
  and and_3 (segs[3], Pwr, or_80_out);
  and and_4 (segs[4], Pwr, or_81_out);
  and and_5 (segs[5], Pwr, or_82_out);
  and and_6 (segs[6], Pwr, or_83_out);
  and and_7 (segs[7], Pwr, or_84_out);
  and and_8 (segs[8], Pwr, or_85_out);
  and and_9 (segs[9], Pwr, or_86_out);
  and and_10 (segs[14], Pwr, or_46_out);

  assign {segs[15], segs[13:10], segs[0]} = {{5{1'b0}}, segs[1]};

  // Notes on the sheet:
  //   Bits 0,1
  //   Bit 2
  //   Bit 3
  //   Bit 4
  //   Bit 5
  //   Bit 6
  //   Bit 7
  //   Bit 8
  //   Bit 9
  //   Bit 14
endmodule
