// Digital circuit byte_to_rgb.dig as structural Verilog
module byte_to_rgb (
  input  [7:0] V,
  input  col,
  input  row,
  output [2:0] R,
  output [2:0] G,
  output [2:0] B
);

  wire and_1_out;

  and and_1 (and_1_out, col, row);
  Register #(.Bits(8)) register_1 (.D(V), .C(and_1_out), .en(and_1_out), .Q({B[2:1], G, R}));

  assign B[0] = 1'b0;
endmodule
