// Digital circuit terminal_coords.dig as structural Verilog
module terminal_coords (
  input  [7:0] \byte ,
  input  C,
  input  [7:0] MaxCol,
  output [7:0] Col,
  output [7:0] Row
);

  wire counter_1_ovf, endl_eq, LF_eq, not_1_out, or_1_out;
  wire [7:0] counter_1_out, counter_2_out;

  not not_1 (not_1_out, or_1_out);
  Counter #(.Bits(8)) counter_1 (.en(not_1_out), .C(C), .clr(or_1_out), .out(counter_1_out), .ovf(counter_1_ovf));
  Counter #(.Bits(8)) counter_2 (.en(or_1_out), .C(C), .clr(1'b0), .out(counter_2_out));  // open: ovf
  Comparator #(.Bits(8)) LF (.a(\byte ), .b(8'h10), .eq(LF_eq));  // open: gt, lt
  or or_1 (or_1_out, endl_eq, LF_eq);
  Comparator #(.Bits(8)) endl (.a(counter_1_out), .b(MaxCol), .eq(endl_eq));  // open: gt, lt
  Delay #(.Bits(8)) delay_1 (.in(counter_1_out), .out(Row));
  Delay #(.Bits(8), .delayTime(2)) delay_2 (.in(counter_2_out), .out(Col));
endmodule
