// Digital circuit 16x1_and.dig as structural Verilog
module _16x1_and (
  input  A0,
  input  A1,
  input  A2,
  input  A3,
  input  A4,
  input  A5,
  input  A6,
  input  A7,
  input  A8,
  input  A9,
  input  A10,
  input  A11,
  input  A12,
  input  A13,
  input  A14,
  input  A15,
  input  AND,
  output X0,
  output X1,
  output X2,
  output X3,
  output X4,
  output X5,
  output X6,
  output X7,
  output X8,
  output X9,
  output X10,
  output X11,
  output X12,
  output X13,
  output X14,
  output X15
);

  and and_1 (X15, AND, A15);
  and and_2 (X14, AND, A14);
  and and_3 (X13, AND, A13);
  and and_4 (X12, AND, A12);
  and and_5 (X11, AND, A11);
  and and_6 (X10, AND, A10);
  and and_7 (X9, AND, A9);
  and and_8 (X8, AND, A8);
  and and_9 (X7, AND, A7);
  and and_10 (X6, AND, A6);
  and and_11 (X5, AND, A5);
  and and_12 (X4, AND, A4);
  and and_13 (X3, AND, A3);
  and and_14 (X2, AND, A2);
  and and_15 (X1, AND, A1);
  and and_16 (X0, AND, A0);
endmodule
