// Digital circuit 1b_selector.dig as structural Verilog
module _1b_selector (
  input  A,
  input  B,
  input  GoA,
  output X
);

  wire and_1_out, and_2_out, not_1_out;

  not not_1 (not_1_out, GoA);
  and and_1 (and_1_out, A, GoA);
  and and_2 (and_2_out, not_1_out, B);
  or or_1 (X, and_1_out, and_2_out);
endmodule
