// Digital circuit 4b_or.dig as structural Verilog
module _4b_or (
  input  [3:0] \byte ,
  output \or 
);

  wire or_1_out, or_2_out;

  or or_1 (or_1_out, \byte [0], \byte [2]);
  or or_2 (or_2_out, \byte [1], \byte [3]);
  or or_3 (\or , or_1_out, or_2_out);
endmodule
