// Digital circuit 8_2b_ors.dig as structural Verilog
module _8_2b_ors (
  input  A0,
  input  A1,
  input  A2,
  input  A3,
  input  A4,
  input  A5,
  input  A6,
  input  A7,
  input  B0,
  input  B1,
  input  B2,
  input  B3,
  input  B4,
  input  B5,
  input  B6,
  input  B7,
  output X0,
  output X1,
  output X2,
  output X3,
  output X4,
  output X5,
  output X6,
  output X7
);

  or or_1 (X0, A0, B0);
  or or_2 (X1, A1, B1);
  or or_3 (X2, A2, B2);
  or or_4 (X3, A3, B3);
  or or_5 (X4, A4, B4);
  or or_6 (X5, A5, B5);
  or or_7 (X6, A6, B6);
  or or_8 (X7, A7, B7);
endmodule
