// Digital circuit 8b_or.dig as structural Verilog
module _8b_or (
  input  [7:0] \byte ,
  output \or 
);

  wire or_1_out, or_2_out, or_3_out, or_4_out, or_5_out, or_6_out;

  or or_1 (or_1_out, \byte [0], \byte [2]);
  or or_2 (or_2_out, \byte [1], \byte [3]);
  or or_3 (or_3_out, \byte [4], \byte [6]);
  or or_4 (or_4_out, \byte [5], \byte [7]);
  or or_5 (or_5_out, or_1_out, or_2_out);
  or or_6 (or_6_out, or_3_out, or_4_out);
  or or_7 (\or , or_5_out, or_6_out);
endmodule
