// Digital circuit 8x1_and.dig as structural Verilog
module _8x1_and (
  input  A0,
  input  A1,
  input  A2,
  input  A3,
  input  A4,
  input  A5,
  input  A6,
  input  A7,
  input  AND,
  output X0,
  output X1,
  output X2,
  output X3,
  output X4,
  output X5,
  output X6,
  output X7
);

  and and_1 (X7, AND, A7);
  and and_2 (X6, AND, A6);
  and and_3 (X5, AND, A5);
  and and_4 (X4, AND, A4);
  and and_5 (X3, AND, A3);
  and and_6 (X2, AND, A2);
  and and_7 (X1, AND, A1);
  and and_8 (X0, AND, A0);
endmodule
