// Digital circuit _20x1_and.dig as structural Verilog
module _20x1_and (
  input  [19:0] V,
  input  AND,
  output [19:0] X
);

  and and_1 (X[0], V[0], AND);
  and and_2 (X[1], V[1], AND);
  and and_3 (X[2], V[2], AND);
  and and_4 (X[3], V[3], AND);
  and and_5 (X[4], V[4], AND);
  and and_6 (X[5], V[5], AND);
  and and_7 (X[6], V[6], AND);
  and and_8 (X[7], V[7], AND);
  and and_9 (X[8], V[8], AND);
  and and_10 (X[9], V[9], AND);
  and and_11 (X[10], V[10], AND);
  and and_12 (X[11], V[11], AND);
  and and_13 (X[12], V[12], AND);
  and and_14 (X[13], V[13], AND);
  and and_15 (X[14], V[14], AND);
  and and_16 (X[15], V[15], AND);
  and and_17 (X[16], V[16], AND);
  and and_18 (X[17], V[17], AND);
  and and_19 (X[18], V[18], AND);
  and and_20 (X[19], V[19], AND);
endmodule
