// Digital circuit _4x1_and.dig as structural Verilog
module _4x1_and (
  input  [3:0] V,
  input  AND,
  output [3:0] X
);

  and and_1 (X[0], AND, V[0]);
  and and_2 (X[1], AND, V[1]);
  and and_3 (X[2], AND, V[2]);
  and and_4 (X[3], AND, V[3]);
endmodule
