// Digital circuit _8x1_and.dig as structural Verilog
module _8x1_and (
  input  [7:0] V,
  input  AND,
  output [7:0] X
);

  and and_1 (X[0], AND, V[0]);
  and and_2 (X[1], AND, V[1]);
  and and_3 (X[2], AND, V[2]);
  and and_4 (X[3], AND, V[3]);
  and and_5 (X[4], AND, V[4]);
  and and_6 (X[5], AND, V[5]);
  and and_7 (X[6], AND, V[6]);
  and and_8 (X[7], AND, V[7]);
endmodule
