// Digital circuit ram_input_selector.dig as structural Verilog
module ram_input_selector (
  input  [15:0] A2,
  input  [7:0] D2,
  input  str2,
  input  C2,
  input  ld2,
  input  Go2,
  input  [15:0] A1,
  input  [7:0] D1,
  input  str1,
  input  C1,
  input  ld1,
  output [15:0] A,
  output [7:0] D,
  output str,
  output C,
  output ld
);

  wire and_1_out, and_2_out, and_3_out, and_4_out, and_5_out, and_6_out, not_1_out;
  wire [7:0] _8x1_and_1_x, _8x1_and_2_x;
  wire [15:0] _16x1_and_1_x, _16x1_and_2_x;

  _16x1_and _16x1_and_1 (.V(A2), .AND(Go2), .X(_16x1_and_1_x));
  _8x1_and _8x1_and_1 (.V(D2), .AND(Go2), .X(_8x1_and_1_x));
  and and_1 (and_1_out, str2, Go2);
  and and_2 (and_2_out, C2, Go2);
  and and_3 (and_3_out, ld2, Go2);
  not not_1 (not_1_out, Go2);
  _16x1_and _16x1_and_2 (.V(A1), .AND(not_1_out), .X(_16x1_and_2_x));
  _8x1_and _8x1_and_2 (.V(D1), .AND(not_1_out), .X(_8x1_and_2_x));
  and and_4 (and_4_out, str1, not_1_out);
  and and_5 (and_5_out, C1, not_1_out);
  and and_6 (and_6_out, ld1, not_1_out);
  assign A = _16x1_and_1_x | _16x1_and_2_x;  // Or or_1, 16 bits wide
  assign D = _8x1_and_1_x | _8x1_and_2_x;  // Or or_2, 8 bits wide
  or or_3 (str, and_1_out, and_4_out);
  or or_4 (C, and_2_out, and_5_out);
  or or_5 (ld, and_3_out, and_6_out);
endmodule
