// Digital circuit 16b_adder.dig as structural Verilog
module _16b_adder (
  input  Cin,
  input  A0,
  input  A1,
  input  A2,
  input  A3,
  input  A4,
  input  A5,
  input  A6,
  input  A7,
  input  A8,
  input  A9,
  input  A10,
  input  A11,
  input  A12,
  input  A13,
  input  A14,
  input  A15,
  input  B0,
  input  B1,
  input  B2,
  input  B3,
  input  B4,
  input  B5,
  input  B6,
  input  B7,
  input  B8,
  input  B9,
  input  B10,
  input  B11,
  input  B12,
  input  B13,
  input  B14,
  input  B15,
  output C,
  output X0,
  output X1,
  output X2,
  output X3,
  output X4,
  output X5,
  output X6,
  output X7,
  output X8,
  output X9,
  output X10,
  output X11,
  output X12,
  output X13,
  output X14,
  output X15
);

  wire _1b_adder_2_c, _1b_adder_3_c, _1b_adder_4_c, _1b_adder_5_c, _1b_adder_6_c, _1b_adder_7_c,
       _1b_adder_8_c, _1b_adder_9_c, _1b_adder_10_c, _1b_adder_11_c, _1b_adder_12_c, _1b_adder_13_c,
       _1b_adder_14_c, _1b_adder_15_c, _1b_adder_16_c;

  _1b_adder _1b_adder_1 (.Cr(_1b_adder_2_c), .A(A15), .B(B15), .C(C), .X0(X15));
  _1b_adder _1b_adder_2 (.Cr(_1b_adder_3_c), .A(A14), .B(B14), .C(_1b_adder_2_c), .X0(X14));
  _1b_adder _1b_adder_3 (.Cr(_1b_adder_4_c), .A(A13), .B(B13), .C(_1b_adder_3_c), .X0(X13));
  _1b_adder _1b_adder_4 (.Cr(_1b_adder_5_c), .A(A12), .B(B12), .C(_1b_adder_4_c), .X0(X12));
  _1b_adder _1b_adder_5 (.Cr(_1b_adder_6_c), .A(A11), .B(B11), .C(_1b_adder_5_c), .X0(X11));
  _1b_adder _1b_adder_6 (.Cr(_1b_adder_7_c), .A(A10), .B(B10), .C(_1b_adder_6_c), .X0(X10));
  _1b_adder _1b_adder_7 (.Cr(_1b_adder_8_c), .A(A9), .B(B9), .C(_1b_adder_7_c), .X0(X9));
  _1b_adder _1b_adder_8 (.Cr(_1b_adder_9_c), .A(A8), .B(B8), .C(_1b_adder_8_c), .X0(X8));
  _1b_adder _1b_adder_9 (.Cr(_1b_adder_10_c), .A(A7), .B(B7), .C(_1b_adder_9_c), .X0(X7));
  _1b_adder _1b_adder_10 (.Cr(_1b_adder_11_c), .A(A6), .B(B6), .C(_1b_adder_10_c), .X0(X6));
  _1b_adder _1b_adder_11 (.Cr(_1b_adder_12_c), .A(A5), .B(B5), .C(_1b_adder_11_c), .X0(X5));
  _1b_adder _1b_adder_12 (.Cr(_1b_adder_13_c), .A(A4), .B(B4), .C(_1b_adder_12_c), .X0(X4));
  _1b_adder _1b_adder_13 (.Cr(_1b_adder_14_c), .A(A3), .B(B3), .C(_1b_adder_13_c), .X0(X3));
  _1b_adder _1b_adder_14 (.Cr(_1b_adder_15_c), .A(A2), .B(B2), .C(_1b_adder_14_c), .X0(X2));
  _1b_adder _1b_adder_15 (.Cr(_1b_adder_16_c), .A(A1), .B(B1), .C(_1b_adder_15_c), .X0(X1));
  _1b_adder _1b_adder_16 (.Cr(Cin), .A(A0), .B(B0), .C(_1b_adder_16_c), .X0(X0));
endmodule
