// Digital circuit 1b_adder.dig as structural Verilog
module _1b_adder (
  input  Cr,
  input  A,
  input  B,
  output C,
  output X0
);

  wire and_1_out, and_2_out, xor_1_out;

  and and_1 (and_1_out, B, A);
  xor xor_1 (xor_1_out, B, A);
  and and_2 (and_2_out, xor_1_out, Cr);
  or or_1 (C, and_1_out, and_2_out);
  xor xor_2 (X0, xor_1_out, Cr);
endmodule
