// Digital circuit 8b_adder.dig as structural Verilog
module _8b_adder (
  input  A0,
  input  A1,
  input  A2,
  input  A3,
  input  A4,
  input  A5,
  input  A6,
  input  A7,
  input  B0,
  input  B1,
  input  B2,
  input  B3,
  input  B4,
  input  B5,
  input  B6,
  input  B7,
  input  Cin,
  output X0,
  output X1,
  output X2,
  output X3,
  output X4,
  output X5,
  output X6,
  output X7,
  output C
);

  wire _1b_adder_2_c, _1b_adder_3_c, _1b_adder_4_c, _1b_adder_5_c, _1b_adder_6_c, _1b_adder_7_c,
       _1b_adder_8_c;

  _1b_adder _1b_adder_1 (.Cr(_1b_adder_2_c), .A(A7), .B(B7), .C(C), .X0(X7));
  _1b_adder _1b_adder_2 (.Cr(_1b_adder_3_c), .A(A6), .B(B6), .C(_1b_adder_2_c), .X0(X6));
  _1b_adder _1b_adder_3 (.Cr(_1b_adder_4_c), .A(A5), .B(B5), .C(_1b_adder_3_c), .X0(X5));
  _1b_adder _1b_adder_4 (.Cr(_1b_adder_5_c), .A(A4), .B(B4), .C(_1b_adder_4_c), .X0(X4));
  _1b_adder _1b_adder_5 (.Cr(_1b_adder_6_c), .A(A3), .B(B3), .C(_1b_adder_5_c), .X0(X3));
  _1b_adder _1b_adder_6 (.Cr(_1b_adder_7_c), .A(A2), .B(B2), .C(_1b_adder_6_c), .X0(X2));
  _1b_adder _1b_adder_7 (.Cr(_1b_adder_8_c), .A(A1), .B(B1), .C(_1b_adder_7_c), .X0(X1));
  _1b_adder _1b_adder_8 (.Cr(Cin), .A(A0), .B(B0), .C(_1b_adder_8_c), .X0(X0));
endmodule
