// Digital circuit 8b_mul.dig as structural Verilog
module _8b_mul (
  input  B7,
  input  B6,
  input  B5,
  input  B4,
  input  B3,
  input  B2,
  input  B1,
  input  B0,
  input  A7,
  input  A6,
  input  A5,
  input  A4,
  input  A3,
  input  A2,
  input  A1,
  input  A0,
  output X15,
  output X14,
  output X13,
  output X12,
  output X11,
  output X10,
  output X9,
  output X8,
  output X7,
  output X6,
  output X5,
  output X4,
  output X3,
  output X2,
  output X1,
  output X0
);

  wire _8x1_and_1_x0, _8x1_and_1_x1, _8x1_and_1_x2, _8x1_and_1_x3, _8x1_and_1_x4, _8x1_and_1_x5,
       _8x1_and_1_x6, _8x1_and_1_x7, _8x1_and_2_x0, _8x1_and_2_x1, _8x1_and_2_x2, _8x1_and_2_x3,
       _8x1_and_2_x4, _8x1_and_2_x5, _8x1_and_2_x6, _8x1_and_2_x7, _8x1_and_3_x0, _8x1_and_3_x1,
       _8x1_and_3_x2, _8x1_and_3_x3, _8x1_and_3_x4, _8x1_and_3_x5, _8x1_and_3_x6, _8x1_and_3_x7,
       _8x1_and_4_x0, _8x1_and_4_x1, _8x1_and_4_x2, _8x1_and_4_x3, _8x1_and_4_x4, _8x1_and_4_x5,
       _8x1_and_4_x6, _8x1_and_4_x7, _8x1_and_5_x0, _8x1_and_5_x1, _8x1_and_5_x2, _8x1_and_5_x3,
       _8x1_and_5_x4, _8x1_and_5_x5, _8x1_and_5_x6, _8x1_and_5_x7, _8x1_and_6_x0, _8x1_and_6_x1,
       _8x1_and_6_x2, _8x1_and_6_x3, _8x1_and_6_x4, _8x1_and_6_x5, _8x1_and_6_x6, _8x1_and_6_x7,
       _8x1_and_7_x0, _8x1_and_7_x1, _8x1_and_7_x2, _8x1_and_7_x3, _8x1_and_7_x4, _8x1_and_7_x5,
       _8x1_and_7_x6, _8x1_and_7_x7, _8x1_and_8_x0, _8x1_and_8_x1, _8x1_and_8_x2, _8x1_and_8_x3,
       _8x1_and_8_x4, _8x1_and_8_x5, _8x1_and_8_x6, _8x1_and_8_x7, _16b_adder_1_x6, _16b_adder_1_x7,
       _16b_adder_1_x8, _16b_adder_1_x9, _16b_adder_1_x10, _16b_adder_1_x11, _16b_adder_1_x12,
       _16b_adder_1_x13, _16b_adder_1_x14, _16b_adder_1_x15, _16b_adder_2_x6, _16b_adder_2_x7,
       _16b_adder_2_x8, _16b_adder_2_x9, _16b_adder_2_x10, _16b_adder_2_x11, _16b_adder_2_x12,
       _16b_adder_2_x13, _16b_adder_2_x14, _16b_adder_2_x15, _16b_adder_3_x6, _16b_adder_3_x7,
       _16b_adder_3_x8, _16b_adder_3_x9, _16b_adder_3_x10, _16b_adder_3_x11, _16b_adder_3_x12,
       _16b_adder_3_x13, _16b_adder_3_x14, _16b_adder_3_x15, _16b_adder_4_x6, _16b_adder_4_x7,
       _16b_adder_4_x8, _16b_adder_4_x9, _16b_adder_4_x10, _16b_adder_4_x11, _16b_adder_4_x12,
       _16b_adder_4_x13, _16b_adder_4_x14, _16b_adder_4_x15, _16b_adder_5_x4, _16b_adder_5_x5,
       _16b_adder_5_x6, _16b_adder_5_x7, _16b_adder_5_x8, _16b_adder_5_x9, _16b_adder_5_x10,
       _16b_adder_5_x11, _16b_adder_5_x12, _16b_adder_5_x13, _16b_adder_5_x14, _16b_adder_5_x15,
       _16b_adder_6_x4, _16b_adder_6_x5, _16b_adder_6_x6, _16b_adder_6_x7, _16b_adder_6_x8, _16b_adder_6_x9,
       _16b_adder_6_x10, _16b_adder_6_x11, _16b_adder_6_x12, _16b_adder_6_x13, _16b_adder_6_x14,
       _16b_adder_6_x15, _16b_adder_7_p24;

  _8x1_and _8x1_and_1 (
    .A0(A7), .A1(A6), .A2(A5), .A3(A4), .A4(A3), .A5(A2), .A6(A1), .A7(A0), .AND(B7), .X0(_8x1_and_1_x0),
    .X1(_8x1_and_1_x1), .X2(_8x1_and_1_x2), .X3(_8x1_and_1_x3), .X4(_8x1_and_1_x4), .X5(_8x1_and_1_x5),
    .X6(_8x1_and_1_x6), .X7(_8x1_and_1_x7));
  _8x1_and _8x1_and_2 (
    .A0(A7), .A1(A6), .A2(A5), .A3(A4), .A4(A3), .A5(A2), .A6(A1), .A7(A0), .AND(B6), .X0(_8x1_and_2_x0),
    .X1(_8x1_and_2_x1), .X2(_8x1_and_2_x2), .X3(_8x1_and_2_x3), .X4(_8x1_and_2_x4), .X5(_8x1_and_2_x5),
    .X6(_8x1_and_2_x6), .X7(_8x1_and_2_x7));
  _8x1_and _8x1_and_3 (
    .A0(A7), .A1(A6), .A2(A5), .A3(A4), .A4(A3), .A5(A2), .A6(A1), .A7(A0), .AND(B5), .X0(_8x1_and_3_x0),
    .X1(_8x1_and_3_x1), .X2(_8x1_and_3_x2), .X3(_8x1_and_3_x3), .X4(_8x1_and_3_x4), .X5(_8x1_and_3_x5),
    .X6(_8x1_and_3_x6), .X7(_8x1_and_3_x7));
  _8x1_and _8x1_and_4 (
    .A0(A7), .A1(A6), .A2(A5), .A3(A4), .A4(A3), .A5(A2), .A6(A1), .A7(A0), .AND(B4), .X0(_8x1_and_4_x0),
    .X1(_8x1_and_4_x1), .X2(_8x1_and_4_x2), .X3(_8x1_and_4_x3), .X4(_8x1_and_4_x4), .X5(_8x1_and_4_x5),
    .X6(_8x1_and_4_x6), .X7(_8x1_and_4_x7));
  _8x1_and _8x1_and_5 (
    .A0(A7), .A1(A6), .A2(A5), .A3(A4), .A4(A3), .A5(A2), .A6(A1), .A7(A0), .AND(B3), .X0(_8x1_and_5_x0),
    .X1(_8x1_and_5_x1), .X2(_8x1_and_5_x2), .X3(_8x1_and_5_x3), .X4(_8x1_and_5_x4), .X5(_8x1_and_5_x5),
    .X6(_8x1_and_5_x6), .X7(_8x1_and_5_x7));
  _8x1_and _8x1_and_6 (
    .A0(A7), .A1(A6), .A2(A5), .A3(A4), .A4(A3), .A5(A2), .A6(A1), .A7(A0), .AND(B2), .X0(_8x1_and_6_x0),
    .X1(_8x1_and_6_x1), .X2(_8x1_and_6_x2), .X3(_8x1_and_6_x3), .X4(_8x1_and_6_x4), .X5(_8x1_and_6_x5),
    .X6(_8x1_and_6_x6), .X7(_8x1_and_6_x7));
  _8x1_and _8x1_and_7 (
    .A0(A7), .A1(A6), .A2(A5), .A3(A4), .A4(A3), .A5(A2), .A6(A1), .A7(A0), .AND(B1), .X0(_8x1_and_7_x0),
    .X1(_8x1_and_7_x1), .X2(_8x1_and_7_x2), .X3(_8x1_and_7_x3), .X4(_8x1_and_7_x4), .X5(_8x1_and_7_x5),
    .X6(_8x1_and_7_x6), .X7(_8x1_and_7_x7));
  _8x1_and _8x1_and_8 (
    .A0(A7), .A1(A6), .A2(A5), .A3(A4), .A4(A3), .A5(A2), .A6(A1), .A7(A0), .AND(B0), .X0(_8x1_and_8_x0),
    .X1(_8x1_and_8_x1), .X2(_8x1_and_8_x2), .X3(_8x1_and_8_x3), .X4(_8x1_and_8_x4), .X5(_8x1_and_8_x5),
    .X6(_8x1_and_8_x6), .X7(_8x1_and_8_x7));
  _16b_adder _16b_adder_1 (
    .Cin(1'b0), .A0(1'b0), .A1(1'b0), .A2(1'b0), .A3(1'b0), .A4(1'b0), .A5(1'b0), .A6(_8x1_and_1_x0),
    .A7(_8x1_and_1_x1), .A8(_8x1_and_1_x2), .A9(_8x1_and_1_x3), .A10(_8x1_and_1_x4), .A11(_8x1_and_1_x5),
    .A12(_8x1_and_1_x6), .A13(_8x1_and_1_x7), .A14(1'b0), .A15(1'b0), .B0(1'b0), .B1(1'b0), .B2(1'b0),
    .B3(1'b0), .B4(1'b0), .B5(1'b0), .B6(1'b0), .B7(_8x1_and_2_x0), .B8(_8x1_and_2_x1), .B9(_8x1_and_2_x2),
    .B10(_8x1_and_2_x3), .B11(_8x1_and_2_x4), .B12(_8x1_and_2_x5), .B13(_8x1_and_2_x6), .B14(_8x1_and_2_x7),
    .B15(1'b0), .X6(_16b_adder_1_x6), .X7(_16b_adder_1_x7), .X8(_16b_adder_1_x8), .X9(_16b_adder_1_x9),
    .X10(_16b_adder_1_x10), .X11(_16b_adder_1_x11), .X12(_16b_adder_1_x12), .X13(_16b_adder_1_x13),
    .X14(_16b_adder_1_x14), .X15(_16b_adder_1_x15));  // open: C, X0, X1, X2, X3, X4, X5
  _16b_adder _16b_adder_2 (
    .Cin(1'b0), .A0(1'b0), .A1(1'b0), .A2(1'b0), .A3(1'b0), .A4(1'b0), .A5(1'b0), .A6(_8x1_and_3_x0),
    .A7(_8x1_and_3_x1), .A8(_8x1_and_3_x2), .A9(_8x1_and_3_x3), .A10(_8x1_and_3_x4), .A11(_8x1_and_3_x5),
    .A12(_8x1_and_3_x6), .A13(_8x1_and_3_x7), .A14(1'b0), .A15(1'b0), .B0(1'b0), .B1(1'b0), .B2(1'b0),
    .B3(1'b0), .B4(1'b0), .B5(1'b0), .B6(1'b0), .B7(_8x1_and_4_x0), .B8(_8x1_and_4_x1), .B9(_8x1_and_4_x2),
    .B10(_8x1_and_4_x3), .B11(_8x1_and_4_x4), .B12(_8x1_and_4_x5), .B13(_8x1_and_4_x6), .B14(_8x1_and_4_x7),
    .B15(1'b0), .X6(_16b_adder_2_x6), .X7(_16b_adder_2_x7), .X8(_16b_adder_2_x8), .X9(_16b_adder_2_x9),
    .X10(_16b_adder_2_x10), .X11(_16b_adder_2_x11), .X12(_16b_adder_2_x12), .X13(_16b_adder_2_x13),
    .X14(_16b_adder_2_x14), .X15(_16b_adder_2_x15));  // open: C, X0, X1, X2, X3, X4, X5
  _16b_adder _16b_adder_3 (
    .Cin(1'b0), .A0(1'b0), .A1(1'b0), .A2(1'b0), .A3(1'b0), .A4(1'b0), .A5(1'b0), .A6(_8x1_and_5_x0),
    .A7(_8x1_and_5_x1), .A8(_8x1_and_5_x2), .A9(_8x1_and_5_x3), .A10(_8x1_and_5_x4), .A11(_8x1_and_5_x5),
    .A12(_8x1_and_5_x6), .A13(_8x1_and_5_x7), .A14(1'b0), .A15(1'b0), .B0(1'b0), .B1(1'b0), .B2(1'b0),
    .B3(1'b0), .B4(1'b0), .B5(1'b0), .B6(1'b0), .B7(_8x1_and_6_x0), .B8(_8x1_and_6_x1), .B9(_8x1_and_6_x2),
    .B10(_8x1_and_6_x3), .B11(_8x1_and_6_x4), .B12(_8x1_and_6_x5), .B13(_8x1_and_6_x6), .B14(_8x1_and_6_x7),
    .B15(1'b0), .X6(_16b_adder_3_x6), .X7(_16b_adder_3_x7), .X8(_16b_adder_3_x8), .X9(_16b_adder_3_x9),
    .X10(_16b_adder_3_x10), .X11(_16b_adder_3_x11), .X12(_16b_adder_3_x12), .X13(_16b_adder_3_x13),
    .X14(_16b_adder_3_x14), .X15(_16b_adder_3_x15));  // open: C, X0, X1, X2, X3, X4, X5
  _16b_adder _16b_adder_4 (
    .Cin(1'b0), .A0(1'b0), .A1(1'b0), .A2(1'b0), .A3(1'b0), .A4(1'b0), .A5(1'b0), .A6(_8x1_and_7_x0),
    .A7(_8x1_and_7_x1), .A8(_8x1_and_7_x2), .A9(_8x1_and_7_x3), .A10(_8x1_and_7_x4), .A11(_8x1_and_7_x5),
    .A12(_8x1_and_7_x6), .A13(_8x1_and_7_x7), .A14(1'b0), .A15(1'b0), .B0(1'b0), .B1(1'b0), .B2(1'b0),
    .B3(1'b0), .B4(1'b0), .B5(1'b0), .B6(1'b0), .B7(_8x1_and_8_x0), .B8(_8x1_and_8_x1), .B9(_8x1_and_8_x2),
    .B10(_8x1_and_8_x3), .B11(_8x1_and_8_x4), .B12(_8x1_and_8_x5), .B13(_8x1_and_8_x6), .B14(_8x1_and_8_x7),
    .B15(1'b0), .X6(_16b_adder_4_x6), .X7(_16b_adder_4_x7), .X8(_16b_adder_4_x8), .X9(_16b_adder_4_x9),
    .X10(_16b_adder_4_x10), .X11(_16b_adder_4_x11), .X12(_16b_adder_4_x12), .X13(_16b_adder_4_x13),
    .X14(_16b_adder_4_x14), .X15(_16b_adder_4_x15));  // open: C, X0, X1, X2, X3, X4, X5
  _16b_adder _16b_adder_5 (
    .Cin(1'b0), .A0(1'b0), .A1(1'b0), .A2(1'b0), .A3(_16b_adder_1_x6), .A4(_16b_adder_1_x7),
    .A5(_16b_adder_1_x8), .A6(_16b_adder_1_x9), .A7(_16b_adder_1_x10), .A8(_16b_adder_1_x11),
    .A9(_16b_adder_1_x12), .A10(_16b_adder_1_x13), .A11(_16b_adder_1_x14), .A12(_16b_adder_1_x15),
    .A13(1'b0), .A14(1'b0), .A15(1'b0), .B0(1'b0), .B1(1'b0), .B2(1'b0), .B3(1'b0), .B4(1'b0),
    .B5(_16b_adder_2_x6), .B6(_16b_adder_2_x7), .B7(_16b_adder_2_x8), .B8(_16b_adder_2_x9),
    .B9(_16b_adder_2_x10), .B10(_16b_adder_2_x11), .B11(_16b_adder_2_x12), .B12(_16b_adder_2_x13),
    .B13(_16b_adder_2_x14), .B14(_16b_adder_2_x15), .B15(1'b0), .X4(_16b_adder_5_x4), .X5(_16b_adder_5_x5),
    .X6(_16b_adder_5_x6), .X7(_16b_adder_5_x7), .X8(_16b_adder_5_x8), .X9(_16b_adder_5_x9),
    .X10(_16b_adder_5_x10), .X11(_16b_adder_5_x11), .X12(_16b_adder_5_x12), .X13(_16b_adder_5_x13),
    .X14(_16b_adder_5_x14), .X15(_16b_adder_5_x15));  // open: C, X0, X1, X2, X3
  _16b_adder _16b_adder_6 (
    .Cin(1'b0), .A0(1'b0), .A1(1'b0), .A2(1'b0), .A3(_16b_adder_3_x6), .A4(_16b_adder_3_x7),
    .A5(_16b_adder_3_x8), .A6(_16b_adder_3_x9), .A7(_16b_adder_3_x10), .A8(_16b_adder_3_x11),
    .A9(_16b_adder_3_x12), .A10(_16b_adder_3_x13), .A11(_16b_adder_3_x14), .A12(_16b_adder_3_x15),
    .A13(1'b0), .A14(1'b0), .A15(1'b0), .B0(1'b0), .B1(1'b0), .B2(1'b0), .B3(1'b0), .B4(1'b0),
    .B5(_16b_adder_4_x6), .B6(_16b_adder_4_x7), .B7(_16b_adder_4_x8), .B8(_16b_adder_4_x9),
    .B9(_16b_adder_4_x10), .B10(_16b_adder_4_x11), .B11(_16b_adder_4_x12), .B12(_16b_adder_4_x13),
    .B13(_16b_adder_4_x14), .B14(_16b_adder_4_x15), .B15(1'b0), .X4(_16b_adder_6_x4), .X5(_16b_adder_6_x5),
    .X6(_16b_adder_6_x6), .X7(_16b_adder_6_x7), .X8(_16b_adder_6_x8), .X9(_16b_adder_6_x9),
    .X10(_16b_adder_6_x10), .X11(_16b_adder_6_x11), .X12(_16b_adder_6_x12), .X13(_16b_adder_6_x13),
    .X14(_16b_adder_6_x14), .X15(_16b_adder_6_x15));  // open: C, X0, X1, X2, X3
  // _16b_adder _16b_adder_7: pin names not known; wires that end beside it: _16b_adder_5_x4, _16b_adder_5_x5, _16b_adder_5_x6, _16b_adder_5_x7, _16b_adder_5_x8, _16b_adder_5_x9, _16b_adder_5_x10, _16b_adder_5_x11, _16b_adder_5_x12, _16b_adder_5_x13, _16b_adder_5_x14, _16b_adder_5_x15, _16b_adder_6_x4, _16b_adder_6_x5, _16b_adder_6_x6, _16b_adder_6_x7, _16b_adder_6_x8, _16b_adder_6_x9, _16b_adder_6_x10, _16b_adder_6_x11, _16b_adder_6_x12, _16b_adder_6_x13, 1'b0, _16b_adder_7_p24, X15, X14, X13, X12, X11, X10, X9, X8, X7, X6, X5, X4, X3, X2, X1, X0, _16b_adder_7_p24, 1'b0, 1'b0, 1'b0, 1'b0, 1'b0, 1'b0, 1'b0
endmodule
