// Digital circuit _16b_add.dig as structural Verilog
module _16b_add (
  input  [15:0] A,
  input  [15:0] B,
  input  Cin,
  output [15:0] X,
  output Cout
);

  wire _1b_adder_2_c, _1b_adder_3_c, _1b_adder_4_c, _1b_adder_5_c, _1b_adder_6_c, _1b_adder_7_c,
       _1b_adder_8_c, _1b_adder_9_c, _1b_adder_10_c, _1b_adder_11_c, _1b_adder_12_c, _1b_adder_13_c,
       _1b_adder_14_c, _1b_adder_15_c, _1b_adder_16_c;

  _1b_adder _1b_adder_1 (.Cr(_1b_adder_2_c), .A(A[15]), .B(B[15]), .C(Cout), .X0(X[15]));
  _1b_adder _1b_adder_2 (.Cr(_1b_adder_3_c), .A(A[14]), .B(B[14]), .C(_1b_adder_2_c), .X0(X[14]));
  _1b_adder _1b_adder_3 (.Cr(_1b_adder_4_c), .A(A[13]), .B(B[13]), .C(_1b_adder_3_c), .X0(X[13]));
  _1b_adder _1b_adder_4 (.Cr(_1b_adder_5_c), .A(A[12]), .B(B[12]), .C(_1b_adder_4_c), .X0(X[12]));
  _1b_adder _1b_adder_5 (.Cr(_1b_adder_6_c), .A(A[11]), .B(B[11]), .C(_1b_adder_5_c), .X0(X[11]));
  _1b_adder _1b_adder_6 (.Cr(_1b_adder_7_c), .A(A[10]), .B(B[10]), .C(_1b_adder_6_c), .X0(X[10]));
  _1b_adder _1b_adder_7 (.Cr(_1b_adder_8_c), .A(A[9]), .B(B[9]), .C(_1b_adder_7_c), .X0(X[9]));
  _1b_adder _1b_adder_8 (.Cr(_1b_adder_9_c), .A(A[8]), .B(B[8]), .C(_1b_adder_8_c), .X0(X[8]));
  _1b_adder _1b_adder_9 (.Cr(_1b_adder_10_c), .A(A[7]), .B(B[7]), .C(_1b_adder_9_c), .X0(X[7]));
  _1b_adder _1b_adder_10 (.Cr(_1b_adder_11_c), .A(A[6]), .B(B[6]), .C(_1b_adder_10_c), .X0(X[6]));
  _1b_adder _1b_adder_11 (.Cr(_1b_adder_12_c), .A(A[5]), .B(B[5]), .C(_1b_adder_11_c), .X0(X[5]));
  _1b_adder _1b_adder_12 (.Cr(_1b_adder_13_c), .A(A[4]), .B(B[4]), .C(_1b_adder_12_c), .X0(X[4]));
  _1b_adder _1b_adder_13 (.Cr(_1b_adder_14_c), .A(A[3]), .B(B[3]), .C(_1b_adder_13_c), .X0(X[3]));
  _1b_adder _1b_adder_14 (.Cr(_1b_adder_15_c), .A(A[2]), .B(B[2]), .C(_1b_adder_14_c), .X0(X[2]));
  _1b_adder _1b_adder_15 (.Cr(_1b_adder_16_c), .A(A[1]), .B(B[1]), .C(_1b_adder_15_c), .X0(X[1]));
  _1b_adder _1b_adder_16 (.Cr(Cin), .A(A[0]), .B(B[0]), .C(_1b_adder_16_c), .X0(X[0]));
endmodule
