// Digital circuit 16_byte_memory_line.dig as structural Verilog
module _16_byte_memory_line (
  input  A0,
  input  A1,
  input  A2,
  input  A3,
  input  V0,
  input  V1,
  input  V2,
  input  V3,
  input  V4,
  input  V5,
  input  V6,
  input  V7,
  input  S,
  output X0,
  output X1,
  output X2,
  output X3,
  output X4,
  output X5,
  output X6,
  output X7
);

  wire _4b_decoder_1_p5, _4b_decoder_1_p6, _4b_decoder_1_p7, _4b_decoder_1_p8, _4b_decoder_1_p9,
       _4b_decoder_1_p10, _4b_decoder_1_p11, _4b_decoder_1_p12, _4b_decoder_1_p13, _4b_decoder_1_p14,
       _4b_decoder_1_p15, _4b_decoder_1_p16, _4b_decoder_1_p17, _4b_decoder_1_p18, _4b_decoder_1_p19,
       _4b_decoder_1_p20, _8_2b_ors_2_x0, _8_2b_ors_2_x1, _8_2b_ors_2_x2, _8_2b_ors_2_x3, _8_2b_ors_2_x4,
       _8_2b_ors_2_x5, _8_2b_ors_2_x6, _8_2b_ors_2_x7, _8_2b_ors_3_x0, _8_2b_ors_3_x1, _8_2b_ors_3_x2,
       _8_2b_ors_3_x3, _8_2b_ors_3_x4, _8_2b_ors_3_x5, _8_2b_ors_3_x6, _8_2b_ors_3_x7, _8_2b_ors_4_x0,
       _8_2b_ors_4_x1, _8_2b_ors_4_x2, _8_2b_ors_4_x3, _8_2b_ors_4_x4, _8_2b_ors_4_x5, _8_2b_ors_4_x6,
       _8_2b_ors_4_x7, _8_2b_ors_5_x0, _8_2b_ors_5_x1, _8_2b_ors_5_x2, _8_2b_ors_5_x3, _8_2b_ors_5_x4,
       _8_2b_ors_5_x5, _8_2b_ors_5_x6, _8_2b_ors_5_x7, _8_2b_ors_6_x0, _8_2b_ors_6_x1, _8_2b_ors_6_x2,
       _8_2b_ors_6_x3, _8_2b_ors_6_x4, _8_2b_ors_6_x5, _8_2b_ors_6_x6, _8_2b_ors_6_x7, _8_2b_ors_7_x0,
       _8_2b_ors_7_x1, _8_2b_ors_7_x2, _8_2b_ors_7_x3, _8_2b_ors_7_x4, _8_2b_ors_7_x5, _8_2b_ors_7_x6,
       _8_2b_ors_7_x7, _8_2b_ors_8_x0, _8_2b_ors_8_x1, _8_2b_ors_8_x2, _8_2b_ors_8_x3, _8_2b_ors_8_x4,
       _8_2b_ors_8_x5, _8_2b_ors_8_x6, _8_2b_ors_8_x7, _8_2b_ors_9_x0, _8_2b_ors_9_x1, _8_2b_ors_9_x2,
       _8_2b_ors_9_x3, _8_2b_ors_9_x4, _8_2b_ors_9_x5, _8_2b_ors_9_x6, _8_2b_ors_9_x7, _8_2b_ors_10_x0,
       _8_2b_ors_10_x1, _8_2b_ors_10_x2, _8_2b_ors_10_x3, _8_2b_ors_10_x4, _8_2b_ors_10_x5, _8_2b_ors_10_x6,
       _8_2b_ors_10_x7, _8_2b_ors_11_x0, _8_2b_ors_11_x1, _8_2b_ors_11_x2, _8_2b_ors_11_x3, _8_2b_ors_11_x4,
       _8_2b_ors_11_x5, _8_2b_ors_11_x6, _8_2b_ors_11_x7, _8_2b_ors_12_x0, _8_2b_ors_12_x1, _8_2b_ors_12_x2,
       _8_2b_ors_12_x3, _8_2b_ors_12_x4, _8_2b_ors_12_x5, _8_2b_ors_12_x6, _8_2b_ors_12_x7, _8_2b_ors_13_x0,
       _8_2b_ors_13_x1, _8_2b_ors_13_x2, _8_2b_ors_13_x3, _8_2b_ors_13_x4, _8_2b_ors_13_x5, _8_2b_ors_13_x6,
       _8_2b_ors_13_x7, _8_2b_ors_14_x0, _8_2b_ors_14_x1, _8_2b_ors_14_x2, _8_2b_ors_14_x3, _8_2b_ors_14_x4,
       _8_2b_ors_14_x5, _8_2b_ors_14_x6, _8_2b_ors_14_x7, _8_2b_ors_15_x0, _8_2b_ors_15_x1, _8_2b_ors_15_x2,
       _8_2b_ors_15_x3, _8_2b_ors_15_x4, _8_2b_ors_15_x5, _8_2b_ors_15_x6, _8_2b_ors_15_x7, _8x1_and_1_x0,
       _8x1_and_1_x1, _8x1_and_1_x2, _8x1_and_1_x3, _8x1_and_1_x4, _8x1_and_1_x5, _8x1_and_1_x6,
       _8x1_and_1_x7, _8x1_and_2_x0, _8x1_and_2_x1, _8x1_and_2_x2, _8x1_and_2_x3, _8x1_and_2_x4,
       _8x1_and_2_x5, _8x1_and_2_x6, _8x1_and_2_x7, _8x1_and_3_x0, _8x1_and_3_x1, _8x1_and_3_x2,
       _8x1_and_3_x3, _8x1_and_3_x4, _8x1_and_3_x5, _8x1_and_3_x6, _8x1_and_3_x7, _8x1_and_4_x0,
       _8x1_and_4_x1, _8x1_and_4_x2, _8x1_and_4_x3, _8x1_and_4_x4, _8x1_and_4_x5, _8x1_and_4_x6,
       _8x1_and_4_x7, _8x1_and_5_x0, _8x1_and_5_x1, _8x1_and_5_x2, _8x1_and_5_x3, _8x1_and_5_x4,
       _8x1_and_5_x5, _8x1_and_5_x6, _8x1_and_5_x7, _8x1_and_6_x0, _8x1_and_6_x1, _8x1_and_6_x2,
       _8x1_and_6_x3, _8x1_and_6_x4, _8x1_and_6_x5, _8x1_and_6_x6, _8x1_and_6_x7, _8x1_and_7_x0,
       _8x1_and_7_x1, _8x1_and_7_x2, _8x1_and_7_x3, _8x1_and_7_x4, _8x1_and_7_x5, _8x1_and_7_x6,
       _8x1_and_7_x7, _8x1_and_8_x0, _8x1_and_8_x1, _8x1_and_8_x2, _8x1_and_8_x3, _8x1_and_8_x4,
       _8x1_and_8_x5, _8x1_and_8_x6, _8x1_and_8_x7, _8x1_and_9_x0, _8x1_and_9_x1, _8x1_and_9_x2,
       _8x1_and_9_x3, _8x1_and_9_x4, _8x1_and_9_x5, _8x1_and_9_x6, _8x1_and_9_x7, _8x1_and_10_x0,
       _8x1_and_10_x1, _8x1_and_10_x2, _8x1_and_10_x3, _8x1_and_10_x4, _8x1_and_10_x5, _8x1_and_10_x6,
       _8x1_and_10_x7, _8x1_and_11_x0, _8x1_and_11_x1, _8x1_and_11_x2, _8x1_and_11_x3, _8x1_and_11_x4,
       _8x1_and_11_x5, _8x1_and_11_x6, _8x1_and_11_x7, _8x1_and_12_x0, _8x1_and_12_x1, _8x1_and_12_x2,
       _8x1_and_12_x3, _8x1_and_12_x4, _8x1_and_12_x5, _8x1_and_12_x6, _8x1_and_12_x7, _8x1_and_13_x0,
       _8x1_and_13_x1, _8x1_and_13_x2, _8x1_and_13_x3, _8x1_and_13_x4, _8x1_and_13_x5, _8x1_and_13_x6,
       _8x1_and_13_x7, _8x1_and_14_x0, _8x1_and_14_x1, _8x1_and_14_x2, _8x1_and_14_x3, _8x1_and_14_x4,
       _8x1_and_14_x5, _8x1_and_14_x6, _8x1_and_14_x7, _8x1_and_15_x0, _8x1_and_15_x1, _8x1_and_15_x2,
       _8x1_and_15_x3, _8x1_and_15_x4, _8x1_and_15_x5, _8x1_and_15_x6, _8x1_and_15_x7, _8x1_and_16_x0,
       _8x1_and_16_x1, _8x1_and_16_x2, _8x1_and_16_x3, _8x1_and_16_x4, _8x1_and_16_x5, _8x1_and_16_x6,
       _8x1_and_16_x7, and_1_out, and_2_out, and_3_out, and_4_out, and_5_out, and_6_out, and_7_out,
       and_8_out, and_9_out, and_10_out, and_11_out, and_12_out, and_13_out, and_14_out, and_15_out,
       and_16_out, Byte0_x0, Byte0_x1, Byte0_x2, Byte0_x3, Byte0_x4, Byte0_x5, Byte0_x6, Byte0_x7, Byte1_x0,
       Byte1_x1, Byte1_x2, Byte1_x3, Byte1_x4, Byte1_x5, Byte1_x6, Byte1_x7, Byte2_x0, Byte2_x1, Byte2_x2,
       Byte2_x3, Byte2_x4, Byte2_x5, Byte2_x6, Byte2_x7, Byte3_x0, Byte3_x1, Byte3_x2, Byte3_x3, Byte3_x4,
       Byte3_x5, Byte3_x6, Byte3_x7, Byte4_x0, Byte4_x1, Byte4_x2, Byte4_x3, Byte4_x4, Byte4_x5, Byte4_x6,
       Byte4_x7, Byte5_x0, Byte5_x1, Byte5_x2, Byte5_x3, Byte5_x4, Byte5_x5, Byte5_x6, Byte5_x7, Byte6_x0,
       Byte6_x1, Byte6_x2, Byte6_x3, Byte6_x4, Byte6_x5, Byte6_x6, Byte6_x7, Byte7_x0, Byte7_x1, Byte7_x2,
       Byte7_x3, Byte7_x4, Byte7_x5, Byte7_x6, Byte7_x7, Byte8_x0, Byte8_x1, Byte8_x2, Byte8_x3, Byte8_x4,
       Byte8_x5, Byte8_x6, Byte8_x7, Byte9_x0, Byte9_x1, Byte9_x2, Byte9_x3, Byte9_x4, Byte9_x5, Byte9_x6,
       Byte9_x7, Byte10_x0, Byte10_x1, Byte10_x2, Byte10_x3, Byte10_x4, Byte10_x5, Byte10_x6, Byte10_x7,
       Byte11_x0, Byte11_x1, Byte11_x2, Byte11_x3, Byte11_x4, Byte11_x5, Byte11_x6, Byte11_x7, Byte12_x0,
       Byte12_x1, Byte12_x2, Byte12_x3, Byte12_x4, Byte12_x5, Byte12_x6, Byte12_x7, Byte13_x0, Byte13_x1,
       Byte13_x2, Byte13_x3, Byte13_x4, Byte13_x5, Byte13_x6, Byte13_x7, Byte14_x0, Byte14_x1, Byte14_x2,
       Byte14_x3, Byte14_x4, Byte14_x5, Byte14_x6, Byte14_x7, Byte15_x0, Byte15_x1, Byte15_x2, Byte15_x3,
       Byte15_x4, Byte15_x5, Byte15_x6, Byte15_x7;

  // _4b_decoder _4b_decoder_1: pin names not known; wires that end beside it: A0, A1, A2, A3, _4b_decoder_1_p5, _4b_decoder_1_p6, _4b_decoder_1_p7, _4b_decoder_1_p8, _4b_decoder_1_p9, _4b_decoder_1_p10, _4b_decoder_1_p11, _4b_decoder_1_p12, _4b_decoder_1_p13, _4b_decoder_1_p14, _4b_decoder_1_p15, _4b_decoder_1_p16, _4b_decoder_1_p17, _4b_decoder_1_p18, _4b_decoder_1_p19, _4b_decoder_1_p20
  _8_2b_ors _8_2b_ors_1 (
    .A0(_8_2b_ors_2_x0), .A1(_8_2b_ors_2_x1), .A2(_8_2b_ors_2_x2), .A3(_8_2b_ors_2_x3), .A4(_8_2b_ors_2_x4),
    .A5(_8_2b_ors_2_x5), .A6(_8_2b_ors_2_x6), .A7(_8_2b_ors_2_x7), .B0(_8_2b_ors_9_x0), .B1(_8_2b_ors_9_x1),
    .B2(_8_2b_ors_9_x2), .B3(_8_2b_ors_9_x3), .B4(_8_2b_ors_9_x4), .B5(_8_2b_ors_9_x5), .B6(_8_2b_ors_9_x6),
    .B7(_8_2b_ors_9_x7), .X0(X0), .X1(X1), .X2(X2), .X3(X3), .X4(X4), .X5(X5), .X6(X6), .X7(X7));
  _8_2b_ors _8_2b_ors_2 (
    .A0(_8_2b_ors_3_x0), .A1(_8_2b_ors_3_x1), .A2(_8_2b_ors_3_x2), .A3(_8_2b_ors_3_x3), .A4(_8_2b_ors_3_x4),
    .A5(_8_2b_ors_3_x5), .A6(_8_2b_ors_3_x6), .A7(_8_2b_ors_3_x7), .B0(_8_2b_ors_6_x0), .B1(_8_2b_ors_6_x1),
    .B2(_8_2b_ors_6_x2), .B3(_8_2b_ors_6_x3), .B4(_8_2b_ors_6_x4), .B5(_8_2b_ors_6_x5), .B6(_8_2b_ors_6_x6),
    .B7(_8_2b_ors_6_x7), .X0(_8_2b_ors_2_x0), .X1(_8_2b_ors_2_x1), .X2(_8_2b_ors_2_x2), .X3(_8_2b_ors_2_x3),
    .X4(_8_2b_ors_2_x4), .X5(_8_2b_ors_2_x5), .X6(_8_2b_ors_2_x6), .X7(_8_2b_ors_2_x7));
  _8_2b_ors _8_2b_ors_3 (
    .A0(_8_2b_ors_4_x0), .A1(_8_2b_ors_4_x1), .A2(_8_2b_ors_4_x2), .A3(_8_2b_ors_4_x3), .A4(_8_2b_ors_4_x4),
    .A5(_8_2b_ors_4_x5), .A6(_8_2b_ors_4_x6), .A7(_8_2b_ors_4_x7), .B0(_8_2b_ors_5_x0), .B1(_8_2b_ors_5_x1),
    .B2(_8_2b_ors_5_x2), .B3(_8_2b_ors_5_x3), .B4(_8_2b_ors_5_x4), .B5(_8_2b_ors_5_x5), .B6(_8_2b_ors_5_x6),
    .B7(_8_2b_ors_5_x7), .X0(_8_2b_ors_3_x0), .X1(_8_2b_ors_3_x1), .X2(_8_2b_ors_3_x2), .X3(_8_2b_ors_3_x3),
    .X4(_8_2b_ors_3_x4), .X5(_8_2b_ors_3_x5), .X6(_8_2b_ors_3_x6), .X7(_8_2b_ors_3_x7));
  _8_2b_ors _8_2b_ors_4 (
    .A0(_8x1_and_1_x0), .A1(_8x1_and_1_x1), .A2(_8x1_and_1_x2), .A3(_8x1_and_1_x3), .A4(_8x1_and_1_x4),
    .A5(_8x1_and_1_x5), .A6(_8x1_and_1_x6), .A7(_8x1_and_1_x7), .B0(_8x1_and_2_x0), .B1(_8x1_and_2_x1),
    .B2(_8x1_and_2_x2), .B3(_8x1_and_2_x3), .B4(_8x1_and_2_x4), .B5(_8x1_and_2_x5), .B6(_8x1_and_2_x6),
    .B7(_8x1_and_2_x7), .X0(_8_2b_ors_4_x0), .X1(_8_2b_ors_4_x1), .X2(_8_2b_ors_4_x2), .X3(_8_2b_ors_4_x3),
    .X4(_8_2b_ors_4_x4), .X5(_8_2b_ors_4_x5), .X6(_8_2b_ors_4_x6), .X7(_8_2b_ors_4_x7));
  _8x1_and _8x1_and_1 (
    .A0(Byte0_x0), .A1(Byte0_x1), .A2(Byte0_x2), .A3(Byte0_x3), .A4(Byte0_x4), .A5(Byte0_x5), .A6(Byte0_x6),
    .A7(Byte0_x7), .AND(_4b_decoder_1_p5), .X0(_8x1_and_1_x0), .X1(_8x1_and_1_x1), .X2(_8x1_and_1_x2),
    .X3(_8x1_and_1_x3), .X4(_8x1_and_1_x4), .X5(_8x1_and_1_x5), .X6(_8x1_and_1_x6), .X7(_8x1_and_1_x7));
  _8b_register Byte0 (
    .A0(V0), .A1(V1), .A2(V2), .A3(V3), .A4(V4), .A5(V5), .A6(V6), .A7(V7), .S(and_1_out), .X0(Byte0_x0),
    .X1(Byte0_x1), .X2(Byte0_x2), .X3(Byte0_x3), .X4(Byte0_x4), .X5(Byte0_x5), .X6(Byte0_x6), .X7(Byte0_x7));
  and and_1 (and_1_out, S, _4b_decoder_1_p5);
  _8x1_and _8x1_and_2 (
    .A0(Byte1_x0), .A1(Byte1_x1), .A2(Byte1_x2), .A3(Byte1_x3), .A4(Byte1_x4), .A5(Byte1_x5), .A6(Byte1_x6),
    .A7(Byte1_x7), .AND(_4b_decoder_1_p6), .X0(_8x1_and_2_x0), .X1(_8x1_and_2_x1), .X2(_8x1_and_2_x2),
    .X3(_8x1_and_2_x3), .X4(_8x1_and_2_x4), .X5(_8x1_and_2_x5), .X6(_8x1_and_2_x6), .X7(_8x1_and_2_x7));
  _8b_register Byte1 (
    .A0(V0), .A1(V1), .A2(V2), .A3(V3), .A4(V4), .A5(V5), .A6(V6), .A7(V7), .S(and_2_out), .X0(Byte1_x0),
    .X1(Byte1_x1), .X2(Byte1_x2), .X3(Byte1_x3), .X4(Byte1_x4), .X5(Byte1_x5), .X6(Byte1_x6), .X7(Byte1_x7));
  and and_2 (and_2_out, S, _4b_decoder_1_p6);
  _8_2b_ors _8_2b_ors_5 (
    .A0(_8x1_and_3_x0), .A1(_8x1_and_3_x1), .A2(_8x1_and_3_x2), .A3(_8x1_and_3_x3), .A4(_8x1_and_3_x4),
    .A5(_8x1_and_3_x5), .A6(_8x1_and_3_x6), .A7(_8x1_and_3_x7), .B0(_8x1_and_4_x0), .B1(_8x1_and_4_x1),
    .B2(_8x1_and_4_x2), .B3(_8x1_and_4_x3), .B4(_8x1_and_4_x4), .B5(_8x1_and_4_x5), .B6(_8x1_and_4_x6),
    .B7(_8x1_and_4_x7), .X0(_8_2b_ors_5_x0), .X1(_8_2b_ors_5_x1), .X2(_8_2b_ors_5_x2), .X3(_8_2b_ors_5_x3),
    .X4(_8_2b_ors_5_x4), .X5(_8_2b_ors_5_x5), .X6(_8_2b_ors_5_x6), .X7(_8_2b_ors_5_x7));
  _8x1_and _8x1_and_3 (
    .A0(Byte2_x0), .A1(Byte2_x1), .A2(Byte2_x2), .A3(Byte2_x3), .A4(Byte2_x4), .A5(Byte2_x5), .A6(Byte2_x6),
    .A7(Byte2_x7), .AND(_4b_decoder_1_p7), .X0(_8x1_and_3_x0), .X1(_8x1_and_3_x1), .X2(_8x1_and_3_x2),
    .X3(_8x1_and_3_x3), .X4(_8x1_and_3_x4), .X5(_8x1_and_3_x5), .X6(_8x1_and_3_x6), .X7(_8x1_and_3_x7));
  _8b_register Byte2 (
    .A0(V0), .A1(V1), .A2(V2), .A3(V3), .A4(V4), .A5(V5), .A6(V6), .A7(V7), .S(and_3_out), .X0(Byte2_x0),
    .X1(Byte2_x1), .X2(Byte2_x2), .X3(Byte2_x3), .X4(Byte2_x4), .X5(Byte2_x5), .X6(Byte2_x6), .X7(Byte2_x7));
  and and_3 (and_3_out, S, _4b_decoder_1_p7);
  _8x1_and _8x1_and_4 (
    .A0(Byte3_x0), .A1(Byte3_x1), .A2(Byte3_x2), .A3(Byte3_x3), .A4(Byte3_x4), .A5(Byte3_x5), .A6(Byte3_x6),
    .A7(Byte3_x7), .AND(_4b_decoder_1_p8), .X0(_8x1_and_4_x0), .X1(_8x1_and_4_x1), .X2(_8x1_and_4_x2),
    .X3(_8x1_and_4_x3), .X4(_8x1_and_4_x4), .X5(_8x1_and_4_x5), .X6(_8x1_and_4_x6), .X7(_8x1_and_4_x7));
  _8b_register Byte3 (
    .A0(V0), .A1(V1), .A2(V2), .A3(V3), .A4(V4), .A5(V5), .A6(V6), .A7(V7), .S(and_4_out), .X0(Byte3_x0),
    .X1(Byte3_x1), .X2(Byte3_x2), .X3(Byte3_x3), .X4(Byte3_x4), .X5(Byte3_x5), .X6(Byte3_x6), .X7(Byte3_x7));
  and and_4 (and_4_out, S, _4b_decoder_1_p8);
  _8_2b_ors _8_2b_ors_6 (
    .A0(_8_2b_ors_7_x0), .A1(_8_2b_ors_7_x1), .A2(_8_2b_ors_7_x2), .A3(_8_2b_ors_7_x3), .A4(_8_2b_ors_7_x4),
    .A5(_8_2b_ors_7_x5), .A6(_8_2b_ors_7_x6), .A7(_8_2b_ors_7_x7), .B0(_8_2b_ors_8_x0), .B1(_8_2b_ors_8_x1),
    .B2(_8_2b_ors_8_x2), .B3(_8_2b_ors_8_x3), .B4(_8_2b_ors_8_x4), .B5(_8_2b_ors_8_x5), .B6(_8_2b_ors_8_x6),
    .B7(_8_2b_ors_8_x7), .X0(_8_2b_ors_6_x0), .X1(_8_2b_ors_6_x1), .X2(_8_2b_ors_6_x2), .X3(_8_2b_ors_6_x3),
    .X4(_8_2b_ors_6_x4), .X5(_8_2b_ors_6_x5), .X6(_8_2b_ors_6_x6), .X7(_8_2b_ors_6_x7));
  _8_2b_ors _8_2b_ors_7 (
    .A0(_8x1_and_5_x0), .A1(_8x1_and_5_x1), .A2(_8x1_and_5_x2), .A3(_8x1_and_5_x3), .A4(_8x1_and_5_x4),
    .A5(_8x1_and_5_x5), .A6(_8x1_and_5_x6), .A7(_8x1_and_5_x7), .B0(_8x1_and_6_x0), .B1(_8x1_and_6_x1),
    .B2(_8x1_and_6_x2), .B3(_8x1_and_6_x3), .B4(_8x1_and_6_x4), .B5(_8x1_and_6_x5), .B6(_8x1_and_6_x6),
    .B7(_8x1_and_6_x7), .X0(_8_2b_ors_7_x0), .X1(_8_2b_ors_7_x1), .X2(_8_2b_ors_7_x2), .X3(_8_2b_ors_7_x3),
    .X4(_8_2b_ors_7_x4), .X5(_8_2b_ors_7_x5), .X6(_8_2b_ors_7_x6), .X7(_8_2b_ors_7_x7));
  _8x1_and _8x1_and_5 (
    .A0(Byte4_x0), .A1(Byte4_x1), .A2(Byte4_x2), .A3(Byte4_x3), .A4(Byte4_x4), .A5(Byte4_x5), .A6(Byte4_x6),
    .A7(Byte4_x7), .AND(_4b_decoder_1_p9), .X0(_8x1_and_5_x0), .X1(_8x1_and_5_x1), .X2(_8x1_and_5_x2),
    .X3(_8x1_and_5_x3), .X4(_8x1_and_5_x4), .X5(_8x1_and_5_x5), .X6(_8x1_and_5_x6), .X7(_8x1_and_5_x7));
  _8b_register Byte4 (
    .A0(V0), .A1(V1), .A2(V2), .A3(V3), .A4(V4), .A5(V5), .A6(V6), .A7(V7), .S(and_5_out), .X0(Byte4_x0),
    .X1(Byte4_x1), .X2(Byte4_x2), .X3(Byte4_x3), .X4(Byte4_x4), .X5(Byte4_x5), .X6(Byte4_x6), .X7(Byte4_x7));
  and and_5 (and_5_out, S, _4b_decoder_1_p9);
  _8x1_and _8x1_and_6 (
    .A0(Byte5_x0), .A1(Byte5_x1), .A2(Byte5_x2), .A3(Byte5_x3), .A4(Byte5_x4), .A5(Byte5_x5), .A6(Byte5_x6),
    .A7(Byte5_x7), .AND(_4b_decoder_1_p10), .X0(_8x1_and_6_x0), .X1(_8x1_and_6_x1), .X2(_8x1_and_6_x2),
    .X3(_8x1_and_6_x3), .X4(_8x1_and_6_x4), .X5(_8x1_and_6_x5), .X6(_8x1_and_6_x6), .X7(_8x1_and_6_x7));
  _8b_register Byte5 (
    .A0(V0), .A1(V1), .A2(V2), .A3(V3), .A4(V4), .A5(V5), .A6(V6), .A7(V7), .S(and_6_out), .X0(Byte5_x0),
    .X1(Byte5_x1), .X2(Byte5_x2), .X3(Byte5_x3), .X4(Byte5_x4), .X5(Byte5_x5), .X6(Byte5_x6), .X7(Byte5_x7));
  and and_6 (and_6_out, S, _4b_decoder_1_p10);
  _8_2b_ors _8_2b_ors_8 (
    .A0(_8x1_and_7_x0), .A1(_8x1_and_7_x1), .A2(_8x1_and_7_x2), .A3(_8x1_and_7_x3), .A4(_8x1_and_7_x4),
    .A5(_8x1_and_7_x5), .A6(_8x1_and_7_x6), .A7(_8x1_and_7_x7), .B0(_8x1_and_8_x0), .B1(_8x1_and_8_x1),
    .B2(_8x1_and_8_x2), .B3(_8x1_and_8_x3), .B4(_8x1_and_8_x4), .B5(_8x1_and_8_x5), .B6(_8x1_and_8_x6),
    .B7(_8x1_and_8_x7), .X0(_8_2b_ors_8_x0), .X1(_8_2b_ors_8_x1), .X2(_8_2b_ors_8_x2), .X3(_8_2b_ors_8_x3),
    .X4(_8_2b_ors_8_x4), .X5(_8_2b_ors_8_x5), .X6(_8_2b_ors_8_x6), .X7(_8_2b_ors_8_x7));
  _8x1_and _8x1_and_7 (
    .A0(Byte6_x0), .A1(Byte6_x1), .A2(Byte6_x2), .A3(Byte6_x3), .A4(Byte6_x4), .A5(Byte6_x5), .A6(Byte6_x6),
    .A7(Byte6_x7), .AND(_4b_decoder_1_p11), .X0(_8x1_and_7_x0), .X1(_8x1_and_7_x1), .X2(_8x1_and_7_x2),
    .X3(_8x1_and_7_x3), .X4(_8x1_and_7_x4), .X5(_8x1_and_7_x5), .X6(_8x1_and_7_x6), .X7(_8x1_and_7_x7));
  _8b_register Byte6 (
    .A0(V0), .A1(V1), .A2(V2), .A3(V3), .A4(V4), .A5(V5), .A6(V6), .A7(V7), .S(and_7_out), .X0(Byte6_x0),
    .X1(Byte6_x1), .X2(Byte6_x2), .X3(Byte6_x3), .X4(Byte6_x4), .X5(Byte6_x5), .X6(Byte6_x6), .X7(Byte6_x7));
  and and_7 (and_7_out, S, _4b_decoder_1_p11);
  _8x1_and _8x1_and_8 (
    .A0(Byte7_x0), .A1(Byte7_x1), .A2(Byte7_x2), .A3(Byte7_x3), .A4(Byte7_x4), .A5(Byte7_x5), .A6(Byte7_x6),
    .A7(Byte7_x7), .AND(_4b_decoder_1_p12), .X0(_8x1_and_8_x0), .X1(_8x1_and_8_x1), .X2(_8x1_and_8_x2),
    .X3(_8x1_and_8_x3), .X4(_8x1_and_8_x4), .X5(_8x1_and_8_x5), .X6(_8x1_and_8_x6), .X7(_8x1_and_8_x7));
  _8b_register Byte7 (
    .A0(V0), .A1(V1), .A2(V2), .A3(V3), .A4(V4), .A5(V5), .A6(V6), .A7(V7), .S(and_8_out), .X0(Byte7_x0),
    .X1(Byte7_x1), .X2(Byte7_x2), .X3(Byte7_x3), .X4(Byte7_x4), .X5(Byte7_x5), .X6(Byte7_x6), .X7(Byte7_x7));
  and and_8 (and_8_out, S, _4b_decoder_1_p12);
  _8_2b_ors _8_2b_ors_9 (
    .A0(_8_2b_ors_10_x0), .A1(_8_2b_ors_10_x1), .A2(_8_2b_ors_10_x2), .A3(_8_2b_ors_10_x3),
    .A4(_8_2b_ors_10_x4), .A5(_8_2b_ors_10_x5), .A6(_8_2b_ors_10_x6), .A7(_8_2b_ors_10_x7),
    .B0(_8_2b_ors_13_x0), .B1(_8_2b_ors_13_x1), .B2(_8_2b_ors_13_x2), .B3(_8_2b_ors_13_x3),
    .B4(_8_2b_ors_13_x4), .B5(_8_2b_ors_13_x5), .B6(_8_2b_ors_13_x6), .B7(_8_2b_ors_13_x7),
    .X0(_8_2b_ors_9_x0), .X1(_8_2b_ors_9_x1), .X2(_8_2b_ors_9_x2), .X3(_8_2b_ors_9_x3), .X4(_8_2b_ors_9_x4),
    .X5(_8_2b_ors_9_x5), .X6(_8_2b_ors_9_x6), .X7(_8_2b_ors_9_x7));
  _8_2b_ors _8_2b_ors_10 (
    .A0(_8_2b_ors_11_x0), .A1(_8_2b_ors_11_x1), .A2(_8_2b_ors_11_x2), .A3(_8_2b_ors_11_x3),
    .A4(_8_2b_ors_11_x4), .A5(_8_2b_ors_11_x5), .A6(_8_2b_ors_11_x6), .A7(_8_2b_ors_11_x7),
    .B0(_8_2b_ors_12_x0), .B1(_8_2b_ors_12_x1), .B2(_8_2b_ors_12_x2), .B3(_8_2b_ors_12_x3),
    .B4(_8_2b_ors_12_x4), .B5(_8_2b_ors_12_x5), .B6(_8_2b_ors_12_x6), .B7(_8_2b_ors_12_x7),
    .X0(_8_2b_ors_10_x0), .X1(_8_2b_ors_10_x1), .X2(_8_2b_ors_10_x2), .X3(_8_2b_ors_10_x3),
    .X4(_8_2b_ors_10_x4), .X5(_8_2b_ors_10_x5), .X6(_8_2b_ors_10_x6), .X7(_8_2b_ors_10_x7));
  _8_2b_ors _8_2b_ors_11 (
    .A0(_8x1_and_9_x0), .A1(_8x1_and_9_x1), .A2(_8x1_and_9_x2), .A3(_8x1_and_9_x3), .A4(_8x1_and_9_x4),
    .A5(_8x1_and_9_x5), .A6(_8x1_and_9_x6), .A7(_8x1_and_9_x7), .B0(_8x1_and_10_x0), .B1(_8x1_and_10_x1),
    .B2(_8x1_and_10_x2), .B3(_8x1_and_10_x3), .B4(_8x1_and_10_x4), .B5(_8x1_and_10_x5), .B6(_8x1_and_10_x6),
    .B7(_8x1_and_10_x7), .X0(_8_2b_ors_11_x0), .X1(_8_2b_ors_11_x1), .X2(_8_2b_ors_11_x2),
    .X3(_8_2b_ors_11_x3), .X4(_8_2b_ors_11_x4), .X5(_8_2b_ors_11_x5), .X6(_8_2b_ors_11_x6),
    .X7(_8_2b_ors_11_x7));
  _8x1_and _8x1_and_9 (
    .A0(Byte8_x0), .A1(Byte8_x1), .A2(Byte8_x2), .A3(Byte8_x3), .A4(Byte8_x4), .A5(Byte8_x5), .A6(Byte8_x6),
    .A7(Byte8_x7), .AND(_4b_decoder_1_p13), .X0(_8x1_and_9_x0), .X1(_8x1_and_9_x1), .X2(_8x1_and_9_x2),
    .X3(_8x1_and_9_x3), .X4(_8x1_and_9_x4), .X5(_8x1_and_9_x5), .X6(_8x1_and_9_x6), .X7(_8x1_and_9_x7));
  _8b_register Byte8 (
    .A0(V0), .A1(V1), .A2(V2), .A3(V3), .A4(V4), .A5(V5), .A6(V6), .A7(V7), .S(and_9_out), .X0(Byte8_x0),
    .X1(Byte8_x1), .X2(Byte8_x2), .X3(Byte8_x3), .X4(Byte8_x4), .X5(Byte8_x5), .X6(Byte8_x6), .X7(Byte8_x7));
  and and_9 (and_9_out, S, _4b_decoder_1_p13);
  _8x1_and _8x1_and_10 (
    .A0(Byte9_x0), .A1(Byte9_x1), .A2(Byte9_x2), .A3(Byte9_x3), .A4(Byte9_x4), .A5(Byte9_x5), .A6(Byte9_x6),
    .A7(Byte9_x7), .AND(_4b_decoder_1_p14), .X0(_8x1_and_10_x0), .X1(_8x1_and_10_x1), .X2(_8x1_and_10_x2),
    .X3(_8x1_and_10_x3), .X4(_8x1_and_10_x4), .X5(_8x1_and_10_x5), .X6(_8x1_and_10_x6), .X7(_8x1_and_10_x7));
  _8b_register Byte9 (
    .A0(V0), .A1(V1), .A2(V2), .A3(V3), .A4(V4), .A5(V5), .A6(V6), .A7(V7), .S(and_10_out), .X0(Byte9_x0),
    .X1(Byte9_x1), .X2(Byte9_x2), .X3(Byte9_x3), .X4(Byte9_x4), .X5(Byte9_x5), .X6(Byte9_x6), .X7(Byte9_x7));
  and and_10 (and_10_out, S, _4b_decoder_1_p14);
  _8_2b_ors _8_2b_ors_12 (
    .A0(_8x1_and_11_x0), .A1(_8x1_and_11_x1), .A2(_8x1_and_11_x2), .A3(_8x1_and_11_x3), .A4(_8x1_and_11_x4),
    .A5(_8x1_and_11_x5), .A6(_8x1_and_11_x6), .A7(_8x1_and_11_x7), .B0(_8x1_and_12_x0), .B1(_8x1_and_12_x1),
    .B2(_8x1_and_12_x2), .B3(_8x1_and_12_x3), .B4(_8x1_and_12_x4), .B5(_8x1_and_12_x5), .B6(_8x1_and_12_x6),
    .B7(_8x1_and_12_x7), .X0(_8_2b_ors_12_x0), .X1(_8_2b_ors_12_x1), .X2(_8_2b_ors_12_x2),
    .X3(_8_2b_ors_12_x3), .X4(_8_2b_ors_12_x4), .X5(_8_2b_ors_12_x5), .X6(_8_2b_ors_12_x6),
    .X7(_8_2b_ors_12_x7));
  _8x1_and _8x1_and_11 (
    .A0(Byte10_x0), .A1(Byte10_x1), .A2(Byte10_x2), .A3(Byte10_x3), .A4(Byte10_x4), .A5(Byte10_x5),
    .A6(Byte10_x6), .A7(Byte10_x7), .AND(_4b_decoder_1_p15), .X0(_8x1_and_11_x0), .X1(_8x1_and_11_x1),
    .X2(_8x1_and_11_x2), .X3(_8x1_and_11_x3), .X4(_8x1_and_11_x4), .X5(_8x1_and_11_x5), .X6(_8x1_and_11_x6),
    .X7(_8x1_and_11_x7));
  _8b_register Byte10 (
    .A0(V0), .A1(V1), .A2(V2), .A3(V3), .A4(V4), .A5(V5), .A6(V6), .A7(V7), .S(and_11_out), .X0(Byte10_x0),
    .X1(Byte10_x1), .X2(Byte10_x2), .X3(Byte10_x3), .X4(Byte10_x4), .X5(Byte10_x5), .X6(Byte10_x6),
    .X7(Byte10_x7));
  and and_11 (and_11_out, S, _4b_decoder_1_p15);
  _8x1_and _8x1_and_12 (
    .A0(Byte11_x0), .A1(Byte11_x1), .A2(Byte11_x2), .A3(Byte11_x3), .A4(Byte11_x4), .A5(Byte11_x5),
    .A6(Byte11_x6), .A7(Byte11_x7), .AND(_4b_decoder_1_p16), .X0(_8x1_and_12_x0), .X1(_8x1_and_12_x1),
    .X2(_8x1_and_12_x2), .X3(_8x1_and_12_x3), .X4(_8x1_and_12_x4), .X5(_8x1_and_12_x5), .X6(_8x1_and_12_x6),
    .X7(_8x1_and_12_x7));
  _8b_register Byte11 (
    .A0(V0), .A1(V1), .A2(V2), .A3(V3), .A4(V4), .A5(V5), .A6(V6), .A7(V7), .S(and_12_out), .X0(Byte11_x0),
    .X1(Byte11_x1), .X2(Byte11_x2), .X3(Byte11_x3), .X4(Byte11_x4), .X5(Byte11_x5), .X6(Byte11_x6),
    .X7(Byte11_x7));
  and and_12 (and_12_out, S, _4b_decoder_1_p16);
  _8_2b_ors _8_2b_ors_13 (
    .A0(_8_2b_ors_14_x0), .A1(_8_2b_ors_14_x1), .A2(_8_2b_ors_14_x2), .A3(_8_2b_ors_14_x3),
    .A4(_8_2b_ors_14_x4), .A5(_8_2b_ors_14_x5), .A6(_8_2b_ors_14_x6), .A7(_8_2b_ors_14_x7),
    .B0(_8_2b_ors_15_x0), .B1(_8_2b_ors_15_x1), .B2(_8_2b_ors_15_x2), .B3(_8_2b_ors_15_x3),
    .B4(_8_2b_ors_15_x4), .B5(_8_2b_ors_15_x5), .B6(_8_2b_ors_15_x6), .B7(_8_2b_ors_15_x7),
    .X0(_8_2b_ors_13_x0), .X1(_8_2b_ors_13_x1), .X2(_8_2b_ors_13_x2), .X3(_8_2b_ors_13_x3),
    .X4(_8_2b_ors_13_x4), .X5(_8_2b_ors_13_x5), .X6(_8_2b_ors_13_x6), .X7(_8_2b_ors_13_x7));
  _8_2b_ors _8_2b_ors_14 (
    .A0(_8x1_and_13_x0), .A1(_8x1_and_13_x1), .A2(_8x1_and_13_x2), .A3(_8x1_and_13_x3), .A4(_8x1_and_13_x4),
    .A5(_8x1_and_13_x5), .A6(_8x1_and_13_x6), .A7(_8x1_and_13_x7), .B0(_8x1_and_14_x0), .B1(_8x1_and_14_x1),
    .B2(_8x1_and_14_x2), .B3(_8x1_and_14_x3), .B4(_8x1_and_14_x4), .B5(_8x1_and_14_x5), .B6(_8x1_and_14_x6),
    .B7(_8x1_and_14_x7), .X0(_8_2b_ors_14_x0), .X1(_8_2b_ors_14_x1), .X2(_8_2b_ors_14_x2),
    .X3(_8_2b_ors_14_x3), .X4(_8_2b_ors_14_x4), .X5(_8_2b_ors_14_x5), .X6(_8_2b_ors_14_x6),
    .X7(_8_2b_ors_14_x7));
  _8x1_and _8x1_and_13 (
    .A0(Byte12_x0), .A1(Byte12_x1), .A2(Byte12_x2), .A3(Byte12_x3), .A4(Byte12_x4), .A5(Byte12_x5),
    .A6(Byte12_x6), .A7(Byte12_x7), .AND(_4b_decoder_1_p17), .X0(_8x1_and_13_x0), .X1(_8x1_and_13_x1),
    .X2(_8x1_and_13_x2), .X3(_8x1_and_13_x3), .X4(_8x1_and_13_x4), .X5(_8x1_and_13_x5), .X6(_8x1_and_13_x6),
    .X7(_8x1_and_13_x7));
  _8b_register Byte12 (
    .A0(V0), .A1(V1), .A2(V2), .A3(V3), .A4(V4), .A5(V5), .A6(V6), .A7(V7), .S(and_13_out), .X0(Byte12_x0),
    .X1(Byte12_x1), .X2(Byte12_x2), .X3(Byte12_x3), .X4(Byte12_x4), .X5(Byte12_x5), .X6(Byte12_x6),
    .X7(Byte12_x7));
  and and_13 (and_13_out, S, _4b_decoder_1_p17);
  _8x1_and _8x1_and_14 (
    .A0(Byte13_x0), .A1(Byte13_x1), .A2(Byte13_x2), .A3(Byte13_x3), .A4(Byte13_x4), .A5(Byte13_x5),
    .A6(Byte13_x6), .A7(Byte13_x7), .AND(_4b_decoder_1_p18), .X0(_8x1_and_14_x0), .X1(_8x1_and_14_x1),
    .X2(_8x1_and_14_x2), .X3(_8x1_and_14_x3), .X4(_8x1_and_14_x4), .X5(_8x1_and_14_x5), .X6(_8x1_and_14_x6),
    .X7(_8x1_and_14_x7));
  _8b_register Byte13 (
    .A0(V0), .A1(V1), .A2(V2), .A3(V3), .A4(V4), .A5(V5), .A6(V6), .A7(V7), .S(and_14_out), .X0(Byte13_x0),
    .X1(Byte13_x1), .X2(Byte13_x2), .X3(Byte13_x3), .X4(Byte13_x4), .X5(Byte13_x5), .X6(Byte13_x6),
    .X7(Byte13_x7));
  and and_14 (and_14_out, S, _4b_decoder_1_p18);
  _8_2b_ors _8_2b_ors_15 (
    .A0(_8x1_and_15_x0), .A1(_8x1_and_15_x1), .A2(_8x1_and_15_x2), .A3(_8x1_and_15_x3), .A4(_8x1_and_15_x4),
    .A5(_8x1_and_15_x5), .A6(_8x1_and_15_x6), .A7(_8x1_and_15_x7), .B0(_8x1_and_16_x0), .B1(_8x1_and_16_x1),
    .B2(_8x1_and_16_x2), .B3(_8x1_and_16_x3), .B4(_8x1_and_16_x4), .B5(_8x1_and_16_x5), .B6(_8x1_and_16_x6),
    .B7(_8x1_and_16_x7), .X0(_8_2b_ors_15_x0), .X1(_8_2b_ors_15_x1), .X2(_8_2b_ors_15_x2),
    .X3(_8_2b_ors_15_x3), .X4(_8_2b_ors_15_x4), .X5(_8_2b_ors_15_x5), .X6(_8_2b_ors_15_x6),
    .X7(_8_2b_ors_15_x7));
  _8x1_and _8x1_and_15 (
    .A0(Byte14_x0), .A1(Byte14_x1), .A2(Byte14_x2), .A3(Byte14_x3), .A4(Byte14_x4), .A5(Byte14_x5),
    .A6(Byte14_x6), .A7(Byte14_x7), .AND(_4b_decoder_1_p19), .X0(_8x1_and_15_x0), .X1(_8x1_and_15_x1),
    .X2(_8x1_and_15_x2), .X3(_8x1_and_15_x3), .X4(_8x1_and_15_x4), .X5(_8x1_and_15_x5), .X6(_8x1_and_15_x6),
    .X7(_8x1_and_15_x7));
  _8b_register Byte14 (
    .A0(V0), .A1(V1), .A2(V2), .A3(V3), .A4(V4), .A5(V5), .A6(V6), .A7(V7), .S(and_15_out), .X0(Byte14_x0),
    .X1(Byte14_x1), .X2(Byte14_x2), .X3(Byte14_x3), .X4(Byte14_x4), .X5(Byte14_x5), .X6(Byte14_x6),
    .X7(Byte14_x7));
  and and_15 (and_15_out, S, _4b_decoder_1_p19);
  _8x1_and _8x1_and_16 (
    .A0(Byte15_x0), .A1(Byte15_x1), .A2(Byte15_x2), .A3(Byte15_x3), .A4(Byte15_x4), .A5(Byte15_x5),
    .A6(Byte15_x6), .A7(Byte15_x7), .AND(_4b_decoder_1_p20), .X0(_8x1_and_16_x0), .X1(_8x1_and_16_x1),
    .X2(_8x1_and_16_x2), .X3(_8x1_and_16_x3), .X4(_8x1_and_16_x4), .X5(_8x1_and_16_x5), .X6(_8x1_and_16_x6),
    .X7(_8x1_and_16_x7));
  _8b_register Byte15 (
    .A0(V0), .A1(V1), .A2(V2), .A3(V3), .A4(V4), .A5(V5), .A6(V6), .A7(V7), .S(and_16_out), .X0(Byte15_x0),
    .X1(Byte15_x1), .X2(Byte15_x2), .X3(Byte15_x3), .X4(Byte15_x4), .X5(Byte15_x5), .X6(Byte15_x6),
    .X7(Byte15_x7));
  and and_16 (and_16_out, S, _4b_decoder_1_p20);
endmodule
