// Digital circuit 16_byte_rom_line.dig as structural Verilog
module _16_byte_rom_line (
  input  A0,
  input  A1,
  input  A2,
  input  A3,
  input  in_13,
  input  in_14,
  input  in_15,
  input  in_16,
  input  in_17,
  input  in_18,
  input  in_19,
  input  in_20,
  input  in_21,
  input  in_22,
  input  in_23,
  input  in_24,
  input  in_25,
  input  in_26,
  input  in_27,
  input  in_28,
  input  in_29,
  input  in_30,
  input  in_31,
  input  in_32,
  input  in_33,
  input  in_34,
  input  in_35,
  input  in_36,
  input  in_37,
  input  in_38,
  input  in_39,
  input  in_40,
  input  in_41,
  input  in_42,
  input  in_43,
  input  in_44,
  input  in_45,
  input  in_46,
  input  in_47,
  input  in_48,
  input  in_49,
  input  in_50,
  input  in_51,
  input  in_52,
  input  in_53,
  input  in_54,
  input  in_55,
  input  in_56,
  input  in_57,
  input  in_58,
  input  in_59,
  input  in_60,
  input  in_61,
  input  in_62,
  input  in_63,
  input  in_64,
  input  in_65,
  input  in_66,
  input  in_67,
  input  in_68,
  input  in_69,
  input  in_70,
  input  in_71,
  input  in_72,
  input  in_73,
  input  in_74,
  input  in_75,
  input  in_76,
  input  in_77,
  input  in_78,
  input  in_79,
  input  in_80,
  input  in_81,
  input  in_82,
  input  in_83,
  input  in_84,
  input  in_85,
  input  in_86,
  input  in_87,
  input  in_88,
  input  in_89,
  input  in_90,
  input  in_91,
  input  in_92,
  input  in_93,
  input  in_94,
  input  in_95,
  input  in_96,
  input  in_97,
  input  in_98,
  input  in_99,
  input  in_100,
  input  in_101,
  input  in_102,
  input  in_103,
  input  in_104,
  input  in_105,
  input  in_106,
  input  in_107,
  input  in_108,
  input  in_109,
  input  in_110,
  input  in_111,
  input  in_112,
  input  in_113,
  input  in_114,
  input  in_115,
  input  in_116,
  input  in_117,
  input  in_118,
  input  in_119,
  input  in_120,
  input  in_121,
  input  in_122,
  input  in_123,
  input  in_124,
  input  in_125,
  input  in_126,
  input  in_127,
  input  in_128,
  input  in_129,
  input  in_130,
  input  in_131,
  input  in_132,
  input  in_133,
  input  in_134,
  input  in_135,
  input  in_136,
  input  in_137,
  input  in_138,
  input  in_139,
  input  in_140,
  output X0,
  output X1,
  output X2,
  output X3,
  output X4,
  output X5,
  output X6,
  output X7
);

  wire _4b_decoder_1_p5, _4b_decoder_1_p6, _4b_decoder_1_p7, _4b_decoder_1_p8, _4b_decoder_1_p9,
       _4b_decoder_1_p10, _4b_decoder_1_p11, _4b_decoder_1_p12, _4b_decoder_1_p13, _4b_decoder_1_p14,
       _4b_decoder_1_p15, _4b_decoder_1_p16, _4b_decoder_1_p17, _4b_decoder_1_p18, _4b_decoder_1_p19,
       _4b_decoder_1_p20, _8_2b_ors_2_x0, _8_2b_ors_2_x1, _8_2b_ors_2_x2, _8_2b_ors_2_x3, _8_2b_ors_2_x4,
       _8_2b_ors_2_x5, _8_2b_ors_2_x6, _8_2b_ors_2_x7, _8_2b_ors_3_x0, _8_2b_ors_3_x1, _8_2b_ors_3_x2,
       _8_2b_ors_3_x3, _8_2b_ors_3_x4, _8_2b_ors_3_x5, _8_2b_ors_3_x6, _8_2b_ors_3_x7, _8_2b_ors_4_x0,
       _8_2b_ors_4_x1, _8_2b_ors_4_x2, _8_2b_ors_4_x3, _8_2b_ors_4_x4, _8_2b_ors_4_x5, _8_2b_ors_4_x6,
       _8_2b_ors_4_x7, _8_2b_ors_5_x0, _8_2b_ors_5_x1, _8_2b_ors_5_x2, _8_2b_ors_5_x3, _8_2b_ors_5_x4,
       _8_2b_ors_5_x5, _8_2b_ors_5_x6, _8_2b_ors_5_x7, _8_2b_ors_6_x0, _8_2b_ors_6_x1, _8_2b_ors_6_x2,
       _8_2b_ors_6_x3, _8_2b_ors_6_x4, _8_2b_ors_6_x5, _8_2b_ors_6_x6, _8_2b_ors_6_x7, _8_2b_ors_7_x0,
       _8_2b_ors_7_x1, _8_2b_ors_7_x2, _8_2b_ors_7_x3, _8_2b_ors_7_x4, _8_2b_ors_7_x5, _8_2b_ors_7_x6,
       _8_2b_ors_7_x7, _8_2b_ors_8_x0, _8_2b_ors_8_x1, _8_2b_ors_8_x2, _8_2b_ors_8_x3, _8_2b_ors_8_x4,
       _8_2b_ors_8_x5, _8_2b_ors_8_x6, _8_2b_ors_8_x7, _8_2b_ors_9_x0, _8_2b_ors_9_x1, _8_2b_ors_9_x2,
       _8_2b_ors_9_x3, _8_2b_ors_9_x4, _8_2b_ors_9_x5, _8_2b_ors_9_x6, _8_2b_ors_9_x7, _8_2b_ors_10_x0,
       _8_2b_ors_10_x1, _8_2b_ors_10_x2, _8_2b_ors_10_x3, _8_2b_ors_10_x4, _8_2b_ors_10_x5, _8_2b_ors_10_x6,
       _8_2b_ors_10_x7, _8_2b_ors_11_x0, _8_2b_ors_11_x1, _8_2b_ors_11_x2, _8_2b_ors_11_x3, _8_2b_ors_11_x4,
       _8_2b_ors_11_x5, _8_2b_ors_11_x6, _8_2b_ors_11_x7, _8_2b_ors_12_x0, _8_2b_ors_12_x1, _8_2b_ors_12_x2,
       _8_2b_ors_12_x3, _8_2b_ors_12_x4, _8_2b_ors_12_x5, _8_2b_ors_12_x6, _8_2b_ors_12_x7, _8_2b_ors_13_x0,
       _8_2b_ors_13_x1, _8_2b_ors_13_x2, _8_2b_ors_13_x3, _8_2b_ors_13_x4, _8_2b_ors_13_x5, _8_2b_ors_13_x6,
       _8_2b_ors_13_x7, _8_2b_ors_14_x0, _8_2b_ors_14_x1, _8_2b_ors_14_x2, _8_2b_ors_14_x3, _8_2b_ors_14_x4,
       _8_2b_ors_14_x5, _8_2b_ors_14_x6, _8_2b_ors_14_x7, _8_2b_ors_15_x0, _8_2b_ors_15_x1, _8_2b_ors_15_x2,
       _8_2b_ors_15_x3, _8_2b_ors_15_x4, _8_2b_ors_15_x5, _8_2b_ors_15_x6, _8_2b_ors_15_x7, Byte0_p1,
       Byte0_p3, Byte0_p5, Byte0_p7, Byte0_p9, Byte0_p11, Byte0_p13, Byte1_p1, Byte1_p4, Byte1_p6, Byte1_p8,
       Byte1_p10, Byte1_p12, Byte1_p14, Byte1_p16, Byte2_p1, Byte2_p4, Byte2_p6, Byte2_p8, Byte2_p10,
       Byte2_p12, Byte2_p14, Byte2_p16, Byte3_p1, Byte3_p4, Byte3_p6, Byte3_p8, Byte3_p10, Byte3_p12,
       Byte3_p14, Byte3_p16, Byte4_p1, Byte4_p4, Byte4_p6, Byte4_p8, Byte4_p10, Byte4_p12, Byte4_p14,
       Byte4_p16, Byte5_p1, Byte5_p4, Byte5_p6, Byte5_p8, Byte5_p10, Byte5_p12, Byte5_p14, Byte5_p16,
       Byte6_p1, Byte6_p4, Byte6_p6, Byte6_p8, Byte6_p10, Byte6_p12, Byte6_p14, Byte6_p16, Byte7_p1,
       Byte7_p4, Byte7_p6, Byte7_p8, Byte7_p10, Byte7_p12, Byte7_p14, Byte7_p16, Byte8_p1, Byte8_p4,
       Byte8_p6, Byte8_p8, Byte8_p10, Byte8_p12, Byte8_p14, Byte8_p16, Byte9_p1, Byte9_p4, Byte9_p6,
       Byte9_p8, Byte9_p10, Byte9_p12, Byte9_p14, Byte9_p16, Byte10_p1, Byte10_p4, Byte10_p6, Byte10_p8,
       Byte10_p10, Byte10_p12, Byte10_p14, Byte10_p16, Byte11_p1, Byte11_p4, Byte11_p6, Byte11_p8,
       Byte11_p10, Byte11_p12, Byte11_p14, Byte11_p16, Byte12_p1, Byte12_p4, Byte12_p6, Byte12_p8,
       Byte12_p10, Byte12_p12, Byte12_p14, Byte12_p16, Byte13_p1, Byte13_p4, Byte13_p6, Byte13_p8,
       Byte13_p10, Byte13_p12, Byte13_p14, Byte13_p16, Byte14_p1, Byte14_p4, Byte14_p6, Byte14_p8,
       Byte14_p10, Byte14_p12, Byte14_p14, Byte14_p16, Byte15_p1, Byte15_p4, Byte15_p6, Byte15_p8,
       Byte15_p10, Byte15_p12, Byte15_p14, Byte15_p16, Byte15_p18;

  _8_2b_ors _8_2b_ors_1 (
    .A0(_8_2b_ors_2_x0), .A1(_8_2b_ors_2_x1), .A2(_8_2b_ors_2_x2), .A3(_8_2b_ors_2_x3), .A4(_8_2b_ors_2_x4),
    .A5(_8_2b_ors_2_x5), .A6(_8_2b_ors_2_x6), .A7(_8_2b_ors_2_x7), .B0(_8_2b_ors_9_x0), .B1(_8_2b_ors_9_x1),
    .B2(_8_2b_ors_9_x2), .B3(_8_2b_ors_9_x3), .B4(_8_2b_ors_9_x4), .B5(_8_2b_ors_9_x5), .B6(_8_2b_ors_9_x6),
    .B7(_8_2b_ors_9_x7), .X0(X0), .X1(X1), .X2(X2), .X3(X3), .X4(X4), .X5(X5), .X6(X6), .X7(X7));
  _8_2b_ors _8_2b_ors_2 (
    .A0(_8_2b_ors_3_x0), .A1(_8_2b_ors_3_x1), .A2(_8_2b_ors_3_x2), .A3(_8_2b_ors_3_x3), .A4(_8_2b_ors_3_x4),
    .A5(_8_2b_ors_3_x5), .A6(_8_2b_ors_3_x6), .A7(_8_2b_ors_3_x7), .B0(_8_2b_ors_6_x0), .B1(_8_2b_ors_6_x1),
    .B2(_8_2b_ors_6_x2), .B3(_8_2b_ors_6_x3), .B4(_8_2b_ors_6_x4), .B5(_8_2b_ors_6_x5), .B6(_8_2b_ors_6_x6),
    .B7(_8_2b_ors_6_x7), .X0(_8_2b_ors_2_x0), .X1(_8_2b_ors_2_x1), .X2(_8_2b_ors_2_x2), .X3(_8_2b_ors_2_x3),
    .X4(_8_2b_ors_2_x4), .X5(_8_2b_ors_2_x5), .X6(_8_2b_ors_2_x6), .X7(_8_2b_ors_2_x7));
  _8_2b_ors _8_2b_ors_3 (
    .A0(_8_2b_ors_4_x0), .A1(_8_2b_ors_4_x1), .A2(_8_2b_ors_4_x2), .A3(_8_2b_ors_4_x3), .A4(_8_2b_ors_4_x4),
    .A5(_8_2b_ors_4_x5), .A6(_8_2b_ors_4_x6), .A7(_8_2b_ors_4_x7), .B0(_8_2b_ors_5_x0), .B1(_8_2b_ors_5_x1),
    .B2(_8_2b_ors_5_x2), .B3(_8_2b_ors_5_x3), .B4(_8_2b_ors_5_x4), .B5(_8_2b_ors_5_x5), .B6(_8_2b_ors_5_x6),
    .B7(_8_2b_ors_5_x7), .X0(_8_2b_ors_3_x0), .X1(_8_2b_ors_3_x1), .X2(_8_2b_ors_3_x2), .X3(_8_2b_ors_3_x3),
    .X4(_8_2b_ors_3_x4), .X5(_8_2b_ors_3_x5), .X6(_8_2b_ors_3_x6), .X7(_8_2b_ors_3_x7));
  _8_2b_ors _8_2b_ors_4 (
    .A0(Byte0_p1), .A1(Byte0_p3), .A2(Byte0_p5), .A3(Byte0_p7), .A4(Byte0_p9), .A5(Byte0_p11),
    .A6(Byte0_p13), .A7(Byte1_p1), .B0(Byte1_p4), .B1(Byte1_p6), .B2(Byte1_p8), .B3(Byte1_p10),
    .B4(Byte1_p12), .B5(Byte1_p14), .B6(Byte1_p16), .B7(Byte2_p1), .X0(_8_2b_ors_4_x0), .X1(_8_2b_ors_4_x1),
    .X2(_8_2b_ors_4_x2), .X3(_8_2b_ors_4_x3), .X4(_8_2b_ors_4_x4), .X5(_8_2b_ors_4_x5), .X6(_8_2b_ors_4_x6),
    .X7(_8_2b_ors_4_x7));
  // bf_instruction Byte0: pin names not known; wires that end beside it: Byte0_p1, in_13, Byte0_p3, in_14, Byte0_p5, in_15, Byte0_p7, in_16, Byte0_p9, in_17, Byte0_p11, in_18, Byte0_p13, in_19
  // _4b_decoder _4b_decoder_1: pin names not known; wires that end beside it: A0, A1, A2, A3, _4b_decoder_1_p5, _4b_decoder_1_p6, _4b_decoder_1_p7, _4b_decoder_1_p8, _4b_decoder_1_p9, _4b_decoder_1_p10, _4b_decoder_1_p11, _4b_decoder_1_p12, _4b_decoder_1_p13, _4b_decoder_1_p14, _4b_decoder_1_p15, _4b_decoder_1_p16, _4b_decoder_1_p17, _4b_decoder_1_p18, _4b_decoder_1_p19, _4b_decoder_1_p20
  // bf_instruction Byte1: pin names not known; wires that end beside it: Byte1_p1, in_20, _4b_decoder_1_p5, Byte1_p4, in_21, Byte1_p6, in_22, Byte1_p8, in_23, Byte1_p10, in_24, Byte1_p12, in_25, Byte1_p14, in_26, Byte1_p16, in_27
  _8_2b_ors _8_2b_ors_5 (
    .A0(Byte2_p4), .A1(Byte2_p6), .A2(Byte2_p8), .A3(Byte2_p10), .A4(Byte2_p12), .A5(Byte2_p14),
    .A6(Byte2_p16), .A7(Byte3_p1), .B0(Byte3_p4), .B1(Byte3_p6), .B2(Byte3_p8), .B3(Byte3_p10),
    .B4(Byte3_p12), .B5(Byte3_p14), .B6(Byte3_p16), .B7(Byte4_p1), .X0(_8_2b_ors_5_x0), .X1(_8_2b_ors_5_x1),
    .X2(_8_2b_ors_5_x2), .X3(_8_2b_ors_5_x3), .X4(_8_2b_ors_5_x4), .X5(_8_2b_ors_5_x5), .X6(_8_2b_ors_5_x6),
    .X7(_8_2b_ors_5_x7));
  // bf_instruction Byte2: pin names not known; wires that end beside it: Byte2_p1, in_28, _4b_decoder_1_p6, Byte2_p4, in_29, Byte2_p6, in_30, Byte2_p8, in_31, Byte2_p10, in_32, Byte2_p12, in_33, Byte2_p14, in_34, Byte2_p16, in_35
  // bf_instruction Byte3: pin names not known; wires that end beside it: Byte3_p1, in_36, _4b_decoder_1_p7, Byte3_p4, in_37, Byte3_p6, in_38, Byte3_p8, in_39, Byte3_p10, in_40, Byte3_p12, in_41, Byte3_p14, in_42, Byte3_p16, in_43
  _8_2b_ors _8_2b_ors_6 (
    .A0(_8_2b_ors_7_x0), .A1(_8_2b_ors_7_x1), .A2(_8_2b_ors_7_x2), .A3(_8_2b_ors_7_x3), .A4(_8_2b_ors_7_x4),
    .A5(_8_2b_ors_7_x5), .A6(_8_2b_ors_7_x6), .A7(_8_2b_ors_7_x7), .B0(_8_2b_ors_8_x0), .B1(_8_2b_ors_8_x1),
    .B2(_8_2b_ors_8_x2), .B3(_8_2b_ors_8_x3), .B4(_8_2b_ors_8_x4), .B5(_8_2b_ors_8_x5), .B6(_8_2b_ors_8_x6),
    .B7(_8_2b_ors_8_x7), .X0(_8_2b_ors_6_x0), .X1(_8_2b_ors_6_x1), .X2(_8_2b_ors_6_x2), .X3(_8_2b_ors_6_x3),
    .X4(_8_2b_ors_6_x4), .X5(_8_2b_ors_6_x5), .X6(_8_2b_ors_6_x6), .X7(_8_2b_ors_6_x7));
  _8_2b_ors _8_2b_ors_7 (
    .A0(Byte4_p4), .A1(Byte4_p6), .A2(Byte4_p8), .A3(Byte4_p10), .A4(Byte4_p12), .A5(Byte4_p14),
    .A6(Byte4_p16), .A7(Byte5_p1), .B0(Byte5_p4), .B1(Byte5_p6), .B2(Byte5_p8), .B3(Byte5_p10),
    .B4(Byte5_p12), .B5(Byte5_p14), .B6(Byte5_p16), .B7(Byte6_p1), .X0(_8_2b_ors_7_x0), .X1(_8_2b_ors_7_x1),
    .X2(_8_2b_ors_7_x2), .X3(_8_2b_ors_7_x3), .X4(_8_2b_ors_7_x4), .X5(_8_2b_ors_7_x5), .X6(_8_2b_ors_7_x6),
    .X7(_8_2b_ors_7_x7));
  // bf_instruction Byte4: pin names not known; wires that end beside it: Byte4_p1, in_44, _4b_decoder_1_p8, Byte4_p4, in_45, Byte4_p6, in_46, Byte4_p8, in_47, Byte4_p10, in_48, Byte4_p12, in_49, Byte4_p14, in_50, Byte4_p16, in_51
  // bf_instruction Byte5: pin names not known; wires that end beside it: Byte5_p1, in_52, _4b_decoder_1_p9, Byte5_p4, in_53, Byte5_p6, in_54, Byte5_p8, in_55, Byte5_p10, in_56, Byte5_p12, in_57, Byte5_p14, in_58, Byte5_p16, in_59
  _8_2b_ors _8_2b_ors_8 (
    .A0(Byte6_p4), .A1(Byte6_p6), .A2(Byte6_p8), .A3(Byte6_p10), .A4(Byte6_p12), .A5(Byte6_p14),
    .A6(Byte6_p16), .A7(Byte7_p1), .B0(Byte7_p4), .B1(Byte7_p6), .B2(Byte7_p8), .B3(Byte7_p10),
    .B4(Byte7_p12), .B5(Byte7_p14), .B6(Byte7_p16), .B7(Byte8_p1), .X0(_8_2b_ors_8_x0), .X1(_8_2b_ors_8_x1),
    .X2(_8_2b_ors_8_x2), .X3(_8_2b_ors_8_x3), .X4(_8_2b_ors_8_x4), .X5(_8_2b_ors_8_x5), .X6(_8_2b_ors_8_x6),
    .X7(_8_2b_ors_8_x7));
  // bf_instruction Byte6: pin names not known; wires that end beside it: Byte6_p1, in_60, _4b_decoder_1_p10, Byte6_p4, in_61, Byte6_p6, in_62, Byte6_p8, in_63, Byte6_p10, in_64, Byte6_p12, in_65, Byte6_p14, in_66, Byte6_p16, in_67
  // bf_instruction Byte7: pin names not known; wires that end beside it: Byte7_p1, in_68, _4b_decoder_1_p11, Byte7_p4, in_69, Byte7_p6, in_70, Byte7_p8, in_71, Byte7_p10, in_72, Byte7_p12, in_73, Byte7_p14, in_74, Byte7_p16, in_75
  _8_2b_ors _8_2b_ors_9 (
    .A0(_8_2b_ors_10_x0), .A1(_8_2b_ors_10_x1), .A2(_8_2b_ors_10_x2), .A3(_8_2b_ors_10_x3),
    .A4(_8_2b_ors_10_x4), .A5(_8_2b_ors_10_x5), .A6(_8_2b_ors_10_x6), .A7(_8_2b_ors_10_x7),
    .B0(_8_2b_ors_13_x0), .B1(_8_2b_ors_13_x1), .B2(_8_2b_ors_13_x2), .B3(_8_2b_ors_13_x3),
    .B4(_8_2b_ors_13_x4), .B5(_8_2b_ors_13_x5), .B6(_8_2b_ors_13_x6), .B7(_8_2b_ors_13_x7),
    .X0(_8_2b_ors_9_x0), .X1(_8_2b_ors_9_x1), .X2(_8_2b_ors_9_x2), .X3(_8_2b_ors_9_x3), .X4(_8_2b_ors_9_x4),
    .X5(_8_2b_ors_9_x5), .X6(_8_2b_ors_9_x6), .X7(_8_2b_ors_9_x7));
  _8_2b_ors _8_2b_ors_10 (
    .A0(_8_2b_ors_11_x0), .A1(_8_2b_ors_11_x1), .A2(_8_2b_ors_11_x2), .A3(_8_2b_ors_11_x3),
    .A4(_8_2b_ors_11_x4), .A5(_8_2b_ors_11_x5), .A6(_8_2b_ors_11_x6), .A7(_8_2b_ors_11_x7),
    .B0(_8_2b_ors_12_x0), .B1(_8_2b_ors_12_x1), .B2(_8_2b_ors_12_x2), .B3(_8_2b_ors_12_x3),
    .B4(_8_2b_ors_12_x4), .B5(_8_2b_ors_12_x5), .B6(_8_2b_ors_12_x6), .B7(_8_2b_ors_12_x7),
    .X0(_8_2b_ors_10_x0), .X1(_8_2b_ors_10_x1), .X2(_8_2b_ors_10_x2), .X3(_8_2b_ors_10_x3),
    .X4(_8_2b_ors_10_x4), .X5(_8_2b_ors_10_x5), .X6(_8_2b_ors_10_x6), .X7(_8_2b_ors_10_x7));
  _8_2b_ors _8_2b_ors_11 (
    .A0(Byte8_p4), .A1(Byte8_p6), .A2(Byte8_p8), .A3(Byte8_p10), .A4(Byte8_p12), .A5(Byte8_p14),
    .A6(Byte8_p16), .A7(Byte9_p1), .B0(Byte9_p4), .B1(Byte9_p6), .B2(Byte9_p8), .B3(Byte9_p10),
    .B4(Byte9_p12), .B5(Byte9_p14), .B6(Byte9_p16), .B7(Byte10_p1), .X0(_8_2b_ors_11_x0),
    .X1(_8_2b_ors_11_x1), .X2(_8_2b_ors_11_x2), .X3(_8_2b_ors_11_x3), .X4(_8_2b_ors_11_x4),
    .X5(_8_2b_ors_11_x5), .X6(_8_2b_ors_11_x6), .X7(_8_2b_ors_11_x7));
  // bf_instruction Byte8: pin names not known; wires that end beside it: Byte8_p1, in_76, _4b_decoder_1_p12, Byte8_p4, in_77, Byte8_p6, in_78, Byte8_p8, in_79, Byte8_p10, in_80, Byte8_p12, in_81, Byte8_p14, in_82, Byte8_p16, in_83
  // bf_instruction Byte9: pin names not known; wires that end beside it: Byte9_p1, in_84, _4b_decoder_1_p13, Byte9_p4, in_85, Byte9_p6, in_86, Byte9_p8, in_87, Byte9_p10, in_88, Byte9_p12, in_89, Byte9_p14, in_90, Byte9_p16, in_91
  _8_2b_ors _8_2b_ors_12 (
    .A0(Byte10_p4), .A1(Byte10_p6), .A2(Byte10_p8), .A3(Byte10_p10), .A4(Byte10_p12), .A5(Byte10_p14),
    .A6(Byte10_p16), .A7(Byte11_p1), .B0(Byte11_p4), .B1(Byte11_p6), .B2(Byte11_p8), .B3(Byte11_p10),
    .B4(Byte11_p12), .B5(Byte11_p14), .B6(Byte11_p16), .B7(Byte12_p1), .X0(_8_2b_ors_12_x0),
    .X1(_8_2b_ors_12_x1), .X2(_8_2b_ors_12_x2), .X3(_8_2b_ors_12_x3), .X4(_8_2b_ors_12_x4),
    .X5(_8_2b_ors_12_x5), .X6(_8_2b_ors_12_x6), .X7(_8_2b_ors_12_x7));
  // bf_instruction Byte10: pin names not known; wires that end beside it: Byte10_p1, in_92, _4b_decoder_1_p14, Byte10_p4, in_93, Byte10_p6, in_94, Byte10_p8, in_95, Byte10_p10, in_96, Byte10_p12, in_97, Byte10_p14, in_98, Byte10_p16, in_99
  // bf_instruction Byte11: pin names not known; wires that end beside it: Byte11_p1, in_100, _4b_decoder_1_p15, Byte11_p4, in_101, Byte11_p6, in_102, Byte11_p8, in_103, Byte11_p10, in_104, Byte11_p12, in_105, Byte11_p14, in_106, Byte11_p16, in_107
  _8_2b_ors _8_2b_ors_13 (
    .A0(_8_2b_ors_14_x0), .A1(_8_2b_ors_14_x1), .A2(_8_2b_ors_14_x2), .A3(_8_2b_ors_14_x3),
    .A4(_8_2b_ors_14_x4), .A5(_8_2b_ors_14_x5), .A6(_8_2b_ors_14_x6), .A7(_8_2b_ors_14_x7),
    .B0(_8_2b_ors_15_x0), .B1(_8_2b_ors_15_x1), .B2(_8_2b_ors_15_x2), .B3(_8_2b_ors_15_x3),
    .B4(_8_2b_ors_15_x4), .B5(_8_2b_ors_15_x5), .B6(_8_2b_ors_15_x6), .B7(_8_2b_ors_15_x7),
    .X0(_8_2b_ors_13_x0), .X1(_8_2b_ors_13_x1), .X2(_8_2b_ors_13_x2), .X3(_8_2b_ors_13_x3),
    .X4(_8_2b_ors_13_x4), .X5(_8_2b_ors_13_x5), .X6(_8_2b_ors_13_x6), .X7(_8_2b_ors_13_x7));
  _8_2b_ors _8_2b_ors_14 (
    .A0(Byte12_p4), .A1(Byte12_p6), .A2(Byte12_p8), .A3(Byte12_p10), .A4(Byte12_p12), .A5(Byte12_p14),
    .A6(Byte12_p16), .A7(Byte13_p1), .B0(Byte13_p4), .B1(Byte13_p6), .B2(Byte13_p8), .B3(Byte13_p10),
    .B4(Byte13_p12), .B5(Byte13_p14), .B6(Byte13_p16), .B7(Byte14_p1), .X0(_8_2b_ors_14_x0),
    .X1(_8_2b_ors_14_x1), .X2(_8_2b_ors_14_x2), .X3(_8_2b_ors_14_x3), .X4(_8_2b_ors_14_x4),
    .X5(_8_2b_ors_14_x5), .X6(_8_2b_ors_14_x6), .X7(_8_2b_ors_14_x7));
  // bf_instruction Byte12: pin names not known; wires that end beside it: Byte12_p1, in_108, _4b_decoder_1_p16, Byte12_p4, in_109, Byte12_p6, in_110, Byte12_p8, in_111, Byte12_p10, in_112, Byte12_p12, in_113, Byte12_p14, in_114, Byte12_p16, in_115
  // bf_instruction Byte13: pin names not known; wires that end beside it: Byte13_p1, in_116, _4b_decoder_1_p17, Byte13_p4, in_117, Byte13_p6, in_118, Byte13_p8, in_119, Byte13_p10, in_120, Byte13_p12, in_121, Byte13_p14, in_122, Byte13_p16, in_123
  _8_2b_ors _8_2b_ors_15 (
    .A0(Byte14_p4), .A1(Byte14_p6), .A2(Byte14_p8), .A3(Byte14_p10), .A4(Byte14_p12), .A5(Byte14_p14),
    .A6(Byte14_p16), .A7(Byte15_p1), .B0(Byte15_p4), .B1(Byte15_p6), .B2(Byte15_p8), .B3(Byte15_p10),
    .B4(Byte15_p12), .B5(Byte15_p14), .B6(Byte15_p16), .B7(Byte15_p18), .X0(_8_2b_ors_15_x0),
    .X1(_8_2b_ors_15_x1), .X2(_8_2b_ors_15_x2), .X3(_8_2b_ors_15_x3), .X4(_8_2b_ors_15_x4),
    .X5(_8_2b_ors_15_x5), .X6(_8_2b_ors_15_x6), .X7(_8_2b_ors_15_x7));
  // bf_instruction Byte14: pin names not known; wires that end beside it: Byte14_p1, in_124, _4b_decoder_1_p18, Byte14_p4, in_125, Byte14_p6, in_126, Byte14_p8, in_127, Byte14_p10, in_128, Byte14_p12, in_129, Byte14_p14, in_130, Byte14_p16, in_131
  // bf_instruction Byte15: pin names not known; wires that end beside it: Byte15_p1, in_132, _4b_decoder_1_p19, Byte15_p4, in_133, Byte15_p6, in_134, Byte15_p8, in_135, Byte15_p10, in_136, Byte15_p12, in_137, Byte15_p14, in_138, Byte15_p16, in_139, Byte15_p18, in_140, _4b_decoder_1_p20
endmodule
