// Digital circuit 16b_register.dig as structural Verilog
module _16b_register (
  input  A0,
  input  A1,
  input  A2,
  input  A3,
  input  A4,
  input  A5,
  input  A6,
  input  A7,
  input  A8,
  input  A9,
  input  A10,
  input  A11,
  input  A12,
  input  A13,
  input  A14,
  input  A15,
  input  S,
  output X0,
  output X1,
  output X2,
  output X3,
  output X4,
  output X5,
  output X6,
  output X7,
  output X8,
  output X9,
  output X10,
  output X11,
  output X12,
  output X13,
  output X14,
  output X15
);

  wire _1b_ram_1_nq, _1b_ram_2_nq, _1b_ram_3_nq, _1b_ram_4_nq, _1b_ram_5_nq, _1b_ram_6_nq, _1b_ram_7_nq,
       _1b_ram_8_nq, _1b_ram_9_nq, _1b_ram_10_nq, _1b_ram_11_nq, _1b_ram_12_nq, _1b_ram_13_nq, _1b_ram_14_nq,
       _1b_ram_15_nq, _1b_ram_16_nq;

  _1b_ram _1b_ram_1 (.V(A0), .S(S), .Q(X0), .NQ(_1b_ram_1_nq));
  _1b_ram _1b_ram_2 (.V(A1), .S(S), .Q(X1), .NQ(_1b_ram_2_nq));
  _1b_ram _1b_ram_3 (.V(A2), .S(S), .Q(X2), .NQ(_1b_ram_3_nq));
  _1b_ram _1b_ram_4 (.V(A3), .S(S), .Q(X3), .NQ(_1b_ram_4_nq));
  _1b_ram _1b_ram_5 (.V(A4), .S(S), .Q(X4), .NQ(_1b_ram_5_nq));
  _1b_ram _1b_ram_6 (.V(A5), .S(S), .Q(X5), .NQ(_1b_ram_6_nq));
  _1b_ram _1b_ram_7 (.V(A6), .S(S), .Q(X6), .NQ(_1b_ram_7_nq));
  _1b_ram _1b_ram_8 (.V(A7), .S(S), .Q(X7), .NQ(_1b_ram_8_nq));
  _1b_ram _1b_ram_9 (.V(A8), .S(S), .Q(X8), .NQ(_1b_ram_9_nq));
  _1b_ram _1b_ram_10 (.V(A9), .S(S), .Q(X9), .NQ(_1b_ram_10_nq));
  _1b_ram _1b_ram_11 (.V(A10), .S(S), .Q(X10), .NQ(_1b_ram_11_nq));
  _1b_ram _1b_ram_12 (.V(A11), .S(S), .Q(X11), .NQ(_1b_ram_12_nq));
  _1b_ram _1b_ram_13 (.V(A12), .S(S), .Q(X12), .NQ(_1b_ram_13_nq));
  _1b_ram _1b_ram_14 (.V(A13), .S(S), .Q(X13), .NQ(_1b_ram_14_nq));
  _1b_ram _1b_ram_15 (.V(A14), .S(S), .Q(X14), .NQ(_1b_ram_15_nq));
  _1b_ram _1b_ram_16 (.V(A15), .S(S), .Q(X15), .NQ(_1b_ram_16_nq));
endmodule
