// Digital circuit 16b_register_w_half_cycle_delay.dig as structural Verilog
module _16b_register_w_half_cycle_delay (
  input  [15:0] V,
  input  Cl,
  output [15:0] X
);

  wire _16b_register_1_x0, _16b_register_1_x1, _16b_register_1_x2, _16b_register_1_x3, _16b_register_1_x4,
       _16b_register_1_x5, _16b_register_1_x6, _16b_register_1_x7, _16b_register_1_x8, _16b_register_1_x9,
       _16b_register_1_x10, _16b_register_1_x11, _16b_register_1_x12, _16b_register_1_x13,
       _16b_register_1_x14, _16b_register_1_x15, not_1_out;

  _16b_register _16b_register_1 (
    .A0(V[0]), .A1(V[1]), .A2(V[2]), .A3(V[3]), .A4(V[4]), .A5(V[5]), .A6(V[6]), .A7(V[7]), .A8(V[8]),
    .A9(V[9]), .A10(V[10]), .A11(V[11]), .A12(V[12]), .A13(V[13]), .A14(V[14]), .A15(V[15]), .S(Cl),
    .X0(_16b_register_1_x0), .X1(_16b_register_1_x1), .X2(_16b_register_1_x2), .X3(_16b_register_1_x3),
    .X4(_16b_register_1_x4), .X5(_16b_register_1_x5), .X6(_16b_register_1_x6), .X7(_16b_register_1_x7),
    .X8(_16b_register_1_x8), .X9(_16b_register_1_x9), .X10(_16b_register_1_x10), .X11(_16b_register_1_x11),
    .X12(_16b_register_1_x12), .X13(_16b_register_1_x13), .X14(_16b_register_1_x14), .X15(_16b_register_1_x15));
  not not_1 (not_1_out, Cl);
  _16b_register _16b_register_2 (
    .A0(_16b_register_1_x0), .A1(_16b_register_1_x1), .A2(_16b_register_1_x2), .A3(_16b_register_1_x3),
    .A4(_16b_register_1_x4), .A5(_16b_register_1_x5), .A6(_16b_register_1_x6), .A7(_16b_register_1_x7),
    .A8(_16b_register_1_x8), .A9(_16b_register_1_x9), .A10(_16b_register_1_x10), .A11(_16b_register_1_x11),
    .A12(_16b_register_1_x12), .A13(_16b_register_1_x13), .A14(_16b_register_1_x14),
    .A15(_16b_register_1_x15), .S(not_1_out), .X0(X[0]), .X1(X[1]), .X2(X[2]), .X3(X[3]), .X4(X[4]),
    .X5(X[5]), .X6(X[6]), .X7(X[7]), .X8(X[8]), .X9(X[9]), .X10(X[10]), .X11(X[11]), .X12(X[12]),
    .X13(X[13]), .X14(X[14]), .X15(X[15]));
  // Pins of 1 and 16 bits meet at X
endmodule
