// Digital circuit 1b_ram.dig as structural Verilog
module _1b_ram (
  input  V,
  input  S,
  output Q,
  output NQ
);

  wire and_1_out, and_2_out, not_1_out;

  not not_1 (not_1_out, V);
  and and_1 (and_1_out, S, not_1_out);
  and and_2 (and_2_out, V, S);
  nor nor_1 (Q, and_1_out, NQ);
  nor nor_2 (NQ, Q, and_2_out);
endmodule
