// Digital circuit 256_bytes_rom.dig as structural Verilog
module _256_bytes_rom (
  input  A0,
  input  A1,
  input  A2,
  input  A3,
  input  A4,
  input  A5,
  input  A6,
  input  A7,
  output X0,
  output X1,
  output X2,
  output X3,
  output X4,
  output X5,
  output X6,
  output X7
);

  wire _4b_decoder_1_p8, _4b_decoder_1_p9, _4b_decoder_1_p10, _4b_decoder_1_p11, _4b_decoder_1_p12,
       _4b_decoder_1_p13, _4b_decoder_1_p14, _4b_decoder_1_p15, _4b_decoder_1_p16, _4b_decoder_1_p17,
       _4b_decoder_1_p18, _4b_decoder_1_p19, _4b_decoder_1_p20, _4b_decoder_1_p21, _4b_decoder_1_p22,
       _4b_decoder_1_p23, _8_2b_ors_2_x0, _8_2b_ors_2_x1, _8_2b_ors_2_x2, _8_2b_ors_2_x3, _8_2b_ors_2_x4,
       _8_2b_ors_2_x5, _8_2b_ors_2_x6, _8_2b_ors_2_x7, _8_2b_ors_3_x0, _8_2b_ors_3_x1, _8_2b_ors_3_x2,
       _8_2b_ors_3_x3, _8_2b_ors_3_x4, _8_2b_ors_3_x5, _8_2b_ors_3_x6, _8_2b_ors_3_x7, _8_2b_ors_4_x0,
       _8_2b_ors_4_x1, _8_2b_ors_4_x2, _8_2b_ors_4_x3, _8_2b_ors_4_x4, _8_2b_ors_4_x5, _8_2b_ors_4_x6,
       _8_2b_ors_4_x7, _8_2b_ors_5_x0, _8_2b_ors_5_x1, _8_2b_ors_5_x2, _8_2b_ors_5_x3, _8_2b_ors_5_x4,
       _8_2b_ors_5_x5, _8_2b_ors_5_x6, _8_2b_ors_5_x7, _8_2b_ors_6_x0, _8_2b_ors_6_x1, _8_2b_ors_6_x2,
       _8_2b_ors_7_x0, _8_2b_ors_7_x1, _8_2b_ors_7_x2, _8_2b_ors_7_x3, _8_2b_ors_7_x4, _8_2b_ors_7_x5,
       _8_2b_ors_7_x6, _8_2b_ors_7_x7, _8_2b_ors_8_x0, _8_2b_ors_8_x1, _8_2b_ors_8_x2, _8_2b_ors_8_x3,
       _8_2b_ors_8_x4, _8_2b_ors_8_x5, _8_2b_ors_8_x6, _8_2b_ors_8_x7, _8_2b_ors_9_x0, _8_2b_ors_9_x1,
       _8_2b_ors_9_x2, _8_2b_ors_9_x3, _8_2b_ors_9_x4, _8_2b_ors_9_x5, _8_2b_ors_9_x6, _8_2b_ors_9_x7,
       _8_2b_ors_10_x0, _8_2b_ors_10_x1, _8_2b_ors_10_x2, _8_2b_ors_10_x3, _8_2b_ors_10_x4, _8_2b_ors_10_x5,
       _8_2b_ors_10_x6, _8_2b_ors_10_x7, _8_2b_ors_11_x0, _8_2b_ors_11_x1, _8_2b_ors_11_x2, _8_2b_ors_11_x3,
       _8_2b_ors_11_x4, _8_2b_ors_11_x5, _8_2b_ors_11_x6, _8_2b_ors_11_x7, _8_2b_ors_12_x0, _8_2b_ors_12_x1,
       _8_2b_ors_12_x2, _8_2b_ors_12_x3, _8_2b_ors_12_x4, _8_2b_ors_12_x5, _8_2b_ors_12_x6, _8_2b_ors_12_x7,
       _8_2b_ors_13_x0, _8_2b_ors_13_x1, _8_2b_ors_13_x2, _8_2b_ors_13_x3, _8_2b_ors_13_x4, _8_2b_ors_13_x5,
       _8_2b_ors_13_x6, _8_2b_ors_13_x7, _8_2b_ors_14_x0, _8_2b_ors_14_x1, _8_2b_ors_14_x2, _8_2b_ors_14_x3,
       _8_2b_ors_14_x4, _8_2b_ors_14_x5, _8_2b_ors_14_x6, _8_2b_ors_14_x7, _8_2b_ors_15_x0, _8_2b_ors_15_x1,
       _8_2b_ors_15_x2, _8_2b_ors_15_x3, _8_2b_ors_15_x4, _8_2b_ors_15_x5, _8_2b_ors_15_x6, _8_2b_ors_15_x7,
       _8x1_and_1_x0, _8x1_and_1_x1, _8x1_and_1_x2, _8x1_and_1_x3, _8x1_and_1_x4, _8x1_and_1_x5,
       _8x1_and_1_x6, _8x1_and_1_x7, _8x1_and_2_x0, _8x1_and_2_x1, _8x1_and_2_x2, _8x1_and_2_x3,
       _8x1_and_2_x4, _8x1_and_2_x5, _8x1_and_2_x6, _8x1_and_2_x7, _8x1_and_3_x0, _8x1_and_3_x1,
       _8x1_and_3_x2, _8x1_and_3_x3, _8x1_and_3_x4, _8x1_and_3_x5, _8x1_and_3_x6, _8x1_and_3_x7,
       _8x1_and_4_x0, _8x1_and_4_x1, _8x1_and_4_x2, _8x1_and_4_x3, _8x1_and_4_x4, _8x1_and_4_x5,
       _8x1_and_4_x6, _8x1_and_4_x7, _8x1_and_5_x0, _8x1_and_5_x1, _8x1_and_5_x2, _8x1_and_5_x3,
       _8x1_and_5_x4, _8x1_and_5_x5, _8x1_and_5_x6, _8x1_and_5_x7, _8x1_and_6_x0, _8x1_and_6_x1,
       _8x1_and_6_x2, _8x1_and_6_x3, _8x1_and_6_x4, _8x1_and_6_x5, _8x1_and_6_x6, _8x1_and_6_x7,
       _8x1_and_7_x0, _8x1_and_7_x1, _8x1_and_7_x2, _8x1_and_7_x3, _8x1_and_7_x4, _8x1_and_7_x5,
       _8x1_and_7_x6, _8x1_and_7_x7, _8x1_and_8_x0, _8x1_and_8_x1, _8x1_and_8_x2, _8x1_and_8_x3,
       _8x1_and_8_x4, _8x1_and_8_x5, _8x1_and_8_x6, _8x1_and_8_x7, _8x1_and_9_x0, _8x1_and_9_x1,
       _8x1_and_9_x2, _8x1_and_9_x3, _8x1_and_9_x4, _8x1_and_9_x5, _8x1_and_9_x6, _8x1_and_9_x7,
       _8x1_and_10_x0, _8x1_and_10_x1, _8x1_and_10_x2, _8x1_and_10_x3, _8x1_and_10_x4, _8x1_and_10_x5,
       _8x1_and_10_x6, _8x1_and_10_x7, _8x1_and_11_x0, _8x1_and_11_x1, _8x1_and_11_x2, _8x1_and_11_x3,
       _8x1_and_11_x4, _8x1_and_11_x5, _8x1_and_11_x6, _8x1_and_11_x7, _8x1_and_12_x0, _8x1_and_12_x1,
       _8x1_and_12_x2, _8x1_and_12_x3, _8x1_and_12_x4, _8x1_and_12_x5, _8x1_and_12_x6, _8x1_and_12_x7,
       _8x1_and_13_x0, _8x1_and_13_x1, _8x1_and_13_x2, _8x1_and_13_x3, _8x1_and_13_x4, _8x1_and_13_x5,
       _8x1_and_13_x6, _8x1_and_13_x7, _8x1_and_14_x0, _8x1_and_14_x1, _8x1_and_14_x2, _8x1_and_14_x3,
       _8x1_and_14_x4, _8x1_and_14_x5, _8x1_and_14_x6, _8x1_and_14_x7, _8x1_and_15_x0, _8x1_and_15_x1,
       _8x1_and_15_x2, _8x1_and_15_x3, _8x1_and_15_x4, _8x1_and_15_x5, _8x1_and_15_x6, _8x1_and_15_x7,
       Byte1_x0, Byte1_x1, Byte1_x2, Byte1_x3, Byte1_x4, Byte1_x5, Byte1_x6, Byte1_x7, Byte2_x0, Byte2_x1,
       Byte2_x2, Byte2_x3, Byte2_x4, Byte2_x5, Byte2_x6, Byte2_x7, Byte3_x0, Byte3_x1, Byte3_x2, Byte3_x3,
       Byte3_x4, Byte3_x5, Byte3_x6, Byte3_x7, Byte4_x0, Byte4_x1, Byte4_x2, Byte4_x3, Byte4_x4, Byte4_x5,
       Byte4_x6, Byte4_x7, Byte5_x0, Byte5_x1, Byte5_x2, Byte5_x3, Byte5_x4, Byte5_x5, Byte5_x6, Byte5_x7,
       Byte6_x0, Byte6_x1, Byte6_x2, Byte6_x3, Byte6_x4, Byte6_x5, Byte6_x6, Byte6_x7, Byte7_x0, Byte7_x1,
       Byte7_x2, Byte7_x3, Byte7_x4, Byte7_x5, Byte7_x6, Byte7_x7, Byte8_x0, Byte8_x1, Byte8_x2, Byte8_x3,
       Byte8_x4, Byte8_x5, Byte8_x6, Byte8_x7, Byte9_x0, Byte9_x1, Byte9_x2, Byte9_x3, Byte9_x4, Byte9_x5,
       Byte9_x6, Byte9_x7, Byte10_x0, Byte10_x1, Byte10_x2, Byte10_x3, Byte10_x4, Byte10_x5, Byte10_x6,
       Byte10_x7, Byte11_x0, Byte11_x1, Byte11_x2, Byte11_x3, Byte11_x4, Byte11_x5, Byte11_x6, Byte11_x7,
       Byte12_x0, Byte12_x1, Byte12_x2, Byte12_x3, Byte12_x4, Byte12_x5, Byte12_x6, Byte12_x7, Byte13_x0,
       Byte13_x1, Byte13_x2, Byte13_x3, Byte13_x4, Byte13_x5, Byte13_x6, Byte13_x7, Byte14_x0, Byte14_x1,
       Byte14_x2, Byte14_x3, Byte14_x4, Byte14_x5, Byte14_x6, Byte14_x7, Byte15_x0, Byte15_x1, Byte15_x2,
       Byte15_x3, Byte15_x4, Byte15_x5, Byte15_x6, Byte15_x7, undriven, undriven_2, undriven_3, undriven_4,
       undriven_5, undriven_6, undriven_7, undriven_8;

  _8_2b_ors _8_2b_ors_1 (
    .A0(_8_2b_ors_2_x0), .A1(_8_2b_ors_2_x1), .A2(_8_2b_ors_2_x2), .A3(_8_2b_ors_2_x3), .A4(_8_2b_ors_2_x4),
    .A5(_8_2b_ors_2_x5), .A6(_8_2b_ors_2_x6), .A7(_8_2b_ors_2_x7), .B0(_8_2b_ors_9_x0), .B1(_8_2b_ors_9_x1),
    .B2(_8_2b_ors_9_x2), .B3(_8_2b_ors_9_x3), .B4(_8_2b_ors_9_x4), .B5(_8_2b_ors_9_x5), .B6(_8_2b_ors_9_x6),
    .B7(_8_2b_ors_9_x7), .X0(X0), .X1(X1), .X2(X2), .X3(X3), .X4(X4), .X5(X5), .X6(X6), .X7(X7));
  _8_2b_ors _8_2b_ors_2 (
    .A0(_8_2b_ors_3_x0), .A1(_8_2b_ors_3_x1), .A2(_8_2b_ors_3_x2), .A3(_8_2b_ors_3_x3), .A4(_8_2b_ors_3_x4),
    .A5(_8_2b_ors_3_x5), .A6(_8_2b_ors_3_x6), .A7(_8_2b_ors_3_x7), .B0(_8_2b_ors_6_x0), .B1(_8_2b_ors_6_x1),
    .B2(_8_2b_ors_6_x2), .B3(_8_2b_ors_6_x2), .B4(_8_2b_ors_6_x2), .B5(_8_2b_ors_6_x2), .B6(_8_2b_ors_6_x2),
    .B7(_8_2b_ors_6_x2), .X0(_8_2b_ors_2_x0), .X1(_8_2b_ors_2_x1), .X2(_8_2b_ors_2_x2), .X3(_8_2b_ors_2_x3),
    .X4(_8_2b_ors_2_x4), .X5(_8_2b_ors_2_x5), .X6(_8_2b_ors_2_x6), .X7(_8_2b_ors_2_x7));
  _8_2b_ors _8_2b_ors_3 (
    .A0(_8_2b_ors_4_x0), .A1(_8_2b_ors_4_x1), .A2(_8_2b_ors_4_x2), .A3(_8_2b_ors_4_x3), .A4(_8_2b_ors_4_x4),
    .A5(_8_2b_ors_4_x5), .A6(_8_2b_ors_4_x6), .A7(_8_2b_ors_4_x7), .B0(_8_2b_ors_5_x0), .B1(_8_2b_ors_5_x1),
    .B2(_8_2b_ors_5_x2), .B3(_8_2b_ors_5_x3), .B4(_8_2b_ors_5_x4), .B5(_8_2b_ors_5_x5), .B6(_8_2b_ors_5_x6),
    .B7(_8_2b_ors_5_x7), .X0(_8_2b_ors_3_x0), .X1(_8_2b_ors_3_x1), .X2(_8_2b_ors_3_x2), .X3(_8_2b_ors_3_x3),
    .X4(_8_2b_ors_3_x4), .X5(_8_2b_ors_3_x5), .X6(_8_2b_ors_3_x6), .X7(_8_2b_ors_3_x7));
  _8_2b_ors _8_2b_ors_4 (
    .A0(undriven_8), .A1(undriven_7), .A2(undriven_6), .A3(undriven_5), .A4(undriven_4), .A5(undriven_3),
    .A6(undriven_2), .A7(undriven), .B0(_8x1_and_1_x0), .B1(_8x1_and_1_x1), .B2(_8x1_and_1_x2),
    .B3(_8x1_and_1_x3), .B4(_8x1_and_1_x4), .B5(_8x1_and_1_x5), .B6(_8x1_and_1_x6), .B7(_8x1_and_1_x7),
    .X0(_8_2b_ors_4_x0), .X1(_8_2b_ors_4_x1), .X2(_8_2b_ors_4_x2), .X3(_8_2b_ors_4_x3), .X4(_8_2b_ors_4_x4),
    .X5(_8_2b_ors_4_x5), .X6(_8_2b_ors_4_x6), .X7(_8_2b_ors_4_x7));
  // _4b_decoder _4b_decoder_1: pin names not known; wires that end beside it: A4, A0, A1, A2, A3, A5, A6, _4b_decoder_1_p8, _4b_decoder_1_p9, _4b_decoder_1_p10, _4b_decoder_1_p11, _4b_decoder_1_p12, _4b_decoder_1_p13, _4b_decoder_1_p14, _4b_decoder_1_p15, _4b_decoder_1_p16, _4b_decoder_1_p17, _4b_decoder_1_p18, _4b_decoder_1_p19, _4b_decoder_1_p20, _4b_decoder_1_p21, _4b_decoder_1_p22, _4b_decoder_1_p23
  _8x1_and _8x1_and_1 (
    .A0(Byte1_x0), .A1(Byte1_x1), .A2(Byte1_x2), .A3(Byte1_x3), .A4(Byte1_x4), .A5(Byte1_x5), .A6(Byte1_x6),
    .A7(Byte1_x7), .AND(_4b_decoder_1_p9), .X0(_8x1_and_1_x0), .X1(_8x1_and_1_x1), .X2(_8x1_and_1_x2),
    .X3(_8x1_and_1_x3), .X4(_8x1_and_1_x4), .X5(_8x1_and_1_x5), .X6(_8x1_and_1_x6), .X7(_8x1_and_1_x7));
  _16_byte_memory_line Byte1 (
    .A0(A4), .A1(A5), .A2(A6), .A3(A7), .X0(Byte1_x0), .X1(Byte1_x1), .X2(Byte1_x2), .X3(Byte1_x3),
    .X4(Byte1_x4), .X5(Byte1_x5), .X6(Byte1_x6), .X7(Byte1_x7));  // open: V0, V1, V2, V3, V4, V5, V6, V7, S
  _8_2b_ors _8_2b_ors_5 (
    .A0(_8x1_and_2_x0), .A1(_8x1_and_2_x1), .A2(_8x1_and_2_x2), .A3(_8x1_and_2_x3), .A4(_8x1_and_2_x4),
    .A5(_8x1_and_2_x5), .A6(_8x1_and_2_x6), .A7(_8x1_and_2_x7), .B0(_8x1_and_3_x0), .B1(_8x1_and_3_x1),
    .B2(_8x1_and_3_x2), .B3(_8x1_and_3_x3), .B4(_8x1_and_3_x4), .B5(_8x1_and_3_x5), .B6(_8x1_and_3_x6),
    .B7(_8x1_and_3_x7), .X0(_8_2b_ors_5_x0), .X1(_8_2b_ors_5_x1), .X2(_8_2b_ors_5_x2), .X3(_8_2b_ors_5_x3),
    .X4(_8_2b_ors_5_x4), .X5(_8_2b_ors_5_x5), .X6(_8_2b_ors_5_x6), .X7(_8_2b_ors_5_x7));
  _8x1_and _8x1_and_2 (
    .A0(Byte2_x0), .A1(Byte2_x1), .A2(Byte2_x2), .A3(Byte2_x3), .A4(Byte2_x4), .A5(Byte2_x5), .A6(Byte2_x6),
    .A7(Byte2_x7), .AND(_4b_decoder_1_p10), .X0(_8x1_and_2_x0), .X1(_8x1_and_2_x1), .X2(_8x1_and_2_x2),
    .X3(_8x1_and_2_x3), .X4(_8x1_and_2_x4), .X5(_8x1_and_2_x5), .X6(_8x1_and_2_x6), .X7(_8x1_and_2_x7));
  _16_byte_memory_line Byte2 (
    .A0(A4), .A1(A5), .A2(A6), .A3(A7), .X0(Byte2_x0), .X1(Byte2_x1), .X2(Byte2_x2), .X3(Byte2_x3),
    .X4(Byte2_x4), .X5(Byte2_x5), .X6(Byte2_x6), .X7(Byte2_x7));  // open: V0, V1, V2, V3, V4, V5, V6, V7, S
  _8x1_and _8x1_and_3 (
    .A0(Byte3_x0), .A1(Byte3_x1), .A2(Byte3_x2), .A3(Byte3_x3), .A4(Byte3_x4), .A5(Byte3_x5), .A6(Byte3_x6),
    .A7(Byte3_x7), .AND(_4b_decoder_1_p11), .X0(_8x1_and_3_x0), .X1(_8x1_and_3_x1), .X2(_8x1_and_3_x2),
    .X3(_8x1_and_3_x3), .X4(_8x1_and_3_x4), .X5(_8x1_and_3_x5), .X6(_8x1_and_3_x6), .X7(_8x1_and_3_x7));
  _16_byte_memory_line Byte3 (
    .A0(A4), .A1(A5), .A2(A6), .A3(A7), .X0(Byte3_x0), .X1(Byte3_x1), .X2(Byte3_x2), .X3(Byte3_x3),
    .X4(Byte3_x4), .X5(Byte3_x5), .X6(Byte3_x6), .X7(Byte3_x7));  // open: V0, V1, V2, V3, V4, V5, V6, V7, S
  _8_2b_ors _8_2b_ors_6 (
    .A0(_8_2b_ors_7_x0), .A1(_8_2b_ors_7_x1), .A2(_8_2b_ors_7_x2), .A3(_8_2b_ors_7_x3), .A4(_8_2b_ors_7_x4),
    .A5(_8_2b_ors_7_x5), .A6(_8_2b_ors_7_x6), .A7(_8_2b_ors_7_x7), .B0(_8_2b_ors_8_x0), .B1(_8_2b_ors_8_x1),
    .B2(_8_2b_ors_8_x2), .B3(_8_2b_ors_8_x3), .B4(_8_2b_ors_8_x4), .B5(_8_2b_ors_8_x5), .B6(_8_2b_ors_8_x6),
    .B7(_8_2b_ors_8_x7), .X0(_8_2b_ors_6_x0), .X1(_8_2b_ors_6_x1), .X2(_8_2b_ors_6_x2), .X3(_8_2b_ors_6_x2),
    .X4(_8_2b_ors_6_x2), .X5(_8_2b_ors_6_x2), .X6(_8_2b_ors_6_x2), .X7(_8_2b_ors_6_x2));
  _8_2b_ors _8_2b_ors_7 (
    .A0(_8x1_and_4_x0), .A1(_8x1_and_4_x1), .A2(_8x1_and_4_x2), .A3(_8x1_and_4_x3), .A4(_8x1_and_4_x4),
    .A5(_8x1_and_4_x5), .A6(_8x1_and_4_x6), .A7(_8x1_and_4_x7), .B0(_8x1_and_5_x0), .B1(_8x1_and_5_x1),
    .B2(_8x1_and_5_x2), .B3(_8x1_and_5_x3), .B4(_8x1_and_5_x4), .B5(_8x1_and_5_x5), .B6(_8x1_and_5_x6),
    .B7(_8x1_and_5_x7), .X0(_8_2b_ors_7_x0), .X1(_8_2b_ors_7_x1), .X2(_8_2b_ors_7_x2), .X3(_8_2b_ors_7_x3),
    .X4(_8_2b_ors_7_x4), .X5(_8_2b_ors_7_x5), .X6(_8_2b_ors_7_x6), .X7(_8_2b_ors_7_x7));
  _8x1_and _8x1_and_4 (
    .A0(Byte4_x0), .A1(Byte4_x1), .A2(Byte4_x2), .A3(Byte4_x3), .A4(Byte4_x4), .A5(Byte4_x5), .A6(Byte4_x6),
    .A7(Byte4_x7), .AND(_4b_decoder_1_p12), .X0(_8x1_and_4_x0), .X1(_8x1_and_4_x1), .X2(_8x1_and_4_x2),
    .X3(_8x1_and_4_x3), .X4(_8x1_and_4_x4), .X5(_8x1_and_4_x5), .X6(_8x1_and_4_x6), .X7(_8x1_and_4_x7));
  _16_byte_memory_line Byte4 (
    .A0(A4), .A1(A5), .A2(A6), .A3(A7), .X0(Byte4_x0), .X1(Byte4_x1), .X2(Byte4_x2), .X3(Byte4_x3),
    .X4(Byte4_x4), .X5(Byte4_x5), .X6(Byte4_x6), .X7(Byte4_x7));  // open: V0, V1, V2, V3, V4, V5, V6, V7, S
  _8x1_and _8x1_and_5 (
    .A0(Byte5_x0), .A1(Byte5_x1), .A2(Byte5_x2), .A3(Byte5_x3), .A4(Byte5_x4), .A5(Byte5_x5), .A6(Byte5_x6),
    .A7(Byte5_x7), .AND(_4b_decoder_1_p13), .X0(_8x1_and_5_x0), .X1(_8x1_and_5_x1), .X2(_8x1_and_5_x2),
    .X3(_8x1_and_5_x3), .X4(_8x1_and_5_x4), .X5(_8x1_and_5_x5), .X6(_8x1_and_5_x6), .X7(_8x1_and_5_x7));
  _16_byte_memory_line Byte5 (
    .A0(A4), .A1(A5), .A2(A6), .A3(A7), .X0(Byte5_x0), .X1(Byte5_x1), .X2(Byte5_x2), .X3(Byte5_x3),
    .X4(Byte5_x4), .X5(Byte5_x5), .X6(Byte5_x6), .X7(Byte5_x7));  // open: V0, V1, V2, V3, V4, V5, V6, V7, S
  _8_2b_ors _8_2b_ors_8 (
    .A0(_8x1_and_6_x0), .A1(_8x1_and_6_x1), .A2(_8x1_and_6_x2), .A3(_8x1_and_6_x3), .A4(_8x1_and_6_x4),
    .A5(_8x1_and_6_x5), .A6(_8x1_and_6_x6), .A7(_8x1_and_6_x7), .B0(_8x1_and_7_x0), .B1(_8x1_and_7_x1),
    .B2(_8x1_and_7_x2), .B3(_8x1_and_7_x3), .B4(_8x1_and_7_x4), .B5(_8x1_and_7_x5), .B6(_8x1_and_7_x6),
    .B7(_8x1_and_7_x7), .X0(_8_2b_ors_8_x0), .X1(_8_2b_ors_8_x1), .X2(_8_2b_ors_8_x2), .X3(_8_2b_ors_8_x3),
    .X4(_8_2b_ors_8_x4), .X5(_8_2b_ors_8_x5), .X6(_8_2b_ors_8_x6), .X7(_8_2b_ors_8_x7));
  _8x1_and _8x1_and_6 (
    .A0(Byte6_x0), .A1(Byte6_x1), .A2(Byte6_x2), .A3(Byte6_x3), .A4(Byte6_x4), .A5(Byte6_x5), .A6(Byte6_x6),
    .A7(Byte6_x7), .AND(_4b_decoder_1_p14), .X0(_8x1_and_6_x0), .X1(_8x1_and_6_x1), .X2(_8x1_and_6_x2),
    .X3(_8x1_and_6_x3), .X4(_8x1_and_6_x4), .X5(_8x1_and_6_x5), .X6(_8x1_and_6_x6), .X7(_8x1_and_6_x7));
  _16_byte_memory_line Byte6 (
    .A0(A4), .A1(A5), .A2(A6), .A3(A7), .X0(Byte6_x0), .X1(Byte6_x1), .X2(Byte6_x2), .X3(Byte6_x3),
    .X4(Byte6_x4), .X5(Byte6_x5), .X6(Byte6_x6), .X7(Byte6_x7));  // open: V0, V1, V2, V3, V4, V5, V6, V7, S
  _8x1_and _8x1_and_7 (
    .A0(Byte7_x0), .A1(Byte7_x1), .A2(Byte7_x2), .A3(Byte7_x3), .A4(Byte7_x4), .A5(Byte7_x5), .A6(Byte7_x6),
    .A7(Byte7_x7), .AND(_4b_decoder_1_p15), .X0(_8x1_and_7_x0), .X1(_8x1_and_7_x1), .X2(_8x1_and_7_x2),
    .X3(_8x1_and_7_x3), .X4(_8x1_and_7_x4), .X5(_8x1_and_7_x5), .X6(_8x1_and_7_x6), .X7(_8x1_and_7_x7));
  _16_byte_memory_line Byte7 (
    .A0(A4), .A1(A5), .A2(A6), .A3(A7), .X0(Byte7_x0), .X1(Byte7_x1), .X2(Byte7_x2), .X3(Byte7_x3),
    .X4(Byte7_x4), .X5(Byte7_x5), .X6(Byte7_x6), .X7(Byte7_x7));  // open: V0, V1, V2, V3, V4, V5, V6, V7, S
  _8_2b_ors _8_2b_ors_9 (
    .A0(_8_2b_ors_10_x0), .A1(_8_2b_ors_10_x1), .A2(_8_2b_ors_10_x2), .A3(_8_2b_ors_10_x3),
    .A4(_8_2b_ors_10_x4), .A5(_8_2b_ors_10_x5), .A6(_8_2b_ors_10_x6), .A7(_8_2b_ors_10_x7),
    .B0(_8_2b_ors_13_x0), .B1(_8_2b_ors_13_x1), .B2(_8_2b_ors_13_x2), .B3(_8_2b_ors_13_x3),
    .B4(_8_2b_ors_13_x4), .B5(_8_2b_ors_13_x5), .B6(_8_2b_ors_13_x6), .B7(_8_2b_ors_13_x7),
    .X0(_8_2b_ors_9_x0), .X1(_8_2b_ors_9_x1), .X2(_8_2b_ors_9_x2), .X3(_8_2b_ors_9_x3), .X4(_8_2b_ors_9_x4),
    .X5(_8_2b_ors_9_x5), .X6(_8_2b_ors_9_x6), .X7(_8_2b_ors_9_x7));
  _8_2b_ors _8_2b_ors_10 (
    .A0(_8_2b_ors_11_x0), .A1(_8_2b_ors_11_x1), .A2(_8_2b_ors_11_x2), .A3(_8_2b_ors_11_x3),
    .A4(_8_2b_ors_11_x4), .A5(_8_2b_ors_11_x5), .A6(_8_2b_ors_11_x6), .A7(_8_2b_ors_11_x7),
    .B0(_8_2b_ors_12_x0), .B1(_8_2b_ors_12_x1), .B2(_8_2b_ors_12_x2), .B3(_8_2b_ors_12_x3),
    .B4(_8_2b_ors_12_x4), .B5(_8_2b_ors_12_x5), .B6(_8_2b_ors_12_x6), .B7(_8_2b_ors_12_x7),
    .X0(_8_2b_ors_10_x0), .X1(_8_2b_ors_10_x1), .X2(_8_2b_ors_10_x2), .X3(_8_2b_ors_10_x3),
    .X4(_8_2b_ors_10_x4), .X5(_8_2b_ors_10_x5), .X6(_8_2b_ors_10_x6), .X7(_8_2b_ors_10_x7));
  _8_2b_ors _8_2b_ors_11 (
    .A0(_8x1_and_8_x0), .A1(_8x1_and_8_x1), .A2(_8x1_and_8_x2), .A3(_8x1_and_8_x3), .A4(_8x1_and_8_x4),
    .A5(_8x1_and_8_x5), .A6(_8x1_and_8_x6), .A7(_8x1_and_8_x7), .B0(_8x1_and_9_x0), .B1(_8x1_and_9_x1),
    .B2(_8x1_and_9_x2), .B3(_8x1_and_9_x3), .B4(_8x1_and_9_x4), .B5(_8x1_and_9_x5), .B6(_8x1_and_9_x6),
    .B7(_8x1_and_9_x7), .X0(_8_2b_ors_11_x0), .X1(_8_2b_ors_11_x1), .X2(_8_2b_ors_11_x2),
    .X3(_8_2b_ors_11_x3), .X4(_8_2b_ors_11_x4), .X5(_8_2b_ors_11_x5), .X6(_8_2b_ors_11_x6),
    .X7(_8_2b_ors_11_x7));
  _8x1_and _8x1_and_8 (
    .A0(Byte8_x0), .A1(Byte8_x1), .A2(Byte8_x2), .A3(Byte8_x3), .A4(Byte8_x4), .A5(Byte8_x5), .A6(Byte8_x6),
    .A7(Byte8_x7), .AND(_4b_decoder_1_p16), .X0(_8x1_and_8_x0), .X1(_8x1_and_8_x1), .X2(_8x1_and_8_x2),
    .X3(_8x1_and_8_x3), .X4(_8x1_and_8_x4), .X5(_8x1_and_8_x5), .X6(_8x1_and_8_x6), .X7(_8x1_and_8_x7));
  _16_byte_memory_line Byte8 (
    .A0(A4), .A1(A5), .A2(A6), .A3(A7), .X0(Byte8_x0), .X1(Byte8_x1), .X2(Byte8_x2), .X3(Byte8_x3),
    .X4(Byte8_x4), .X5(Byte8_x5), .X6(Byte8_x6), .X7(Byte8_x7));  // open: V0, V1, V2, V3, V4, V5, V6, V7, S
  _8x1_and _8x1_and_9 (
    .A0(Byte9_x0), .A1(Byte9_x1), .A2(Byte9_x2), .A3(Byte9_x3), .A4(Byte9_x4), .A5(Byte9_x5), .A6(Byte9_x6),
    .A7(Byte9_x7), .AND(_4b_decoder_1_p17), .X0(_8x1_and_9_x0), .X1(_8x1_and_9_x1), .X2(_8x1_and_9_x2),
    .X3(_8x1_and_9_x3), .X4(_8x1_and_9_x4), .X5(_8x1_and_9_x5), .X6(_8x1_and_9_x6), .X7(_8x1_and_9_x7));
  _16_byte_memory_line Byte9 (
    .A0(A4), .A1(A5), .A2(A6), .A3(A7), .X0(Byte9_x0), .X1(Byte9_x1), .X2(Byte9_x2), .X3(Byte9_x3),
    .X4(Byte9_x4), .X5(Byte9_x5), .X6(Byte9_x6), .X7(Byte9_x7));  // open: V0, V1, V2, V3, V4, V5, V6, V7, S
  _8_2b_ors _8_2b_ors_12 (
    .A0(_8x1_and_10_x0), .A1(_8x1_and_10_x1), .A2(_8x1_and_10_x2), .A3(_8x1_and_10_x3), .A4(_8x1_and_10_x4),
    .A5(_8x1_and_10_x5), .A6(_8x1_and_10_x6), .A7(_8x1_and_10_x7), .B0(_8x1_and_11_x0), .B1(_8x1_and_11_x1),
    .B2(_8x1_and_11_x2), .B3(_8x1_and_11_x3), .B4(_8x1_and_11_x4), .B5(_8x1_and_11_x5), .B6(_8x1_and_11_x6),
    .B7(_8x1_and_11_x7), .X0(_8_2b_ors_12_x0), .X1(_8_2b_ors_12_x1), .X2(_8_2b_ors_12_x2),
    .X3(_8_2b_ors_12_x3), .X4(_8_2b_ors_12_x4), .X5(_8_2b_ors_12_x5), .X6(_8_2b_ors_12_x6),
    .X7(_8_2b_ors_12_x7));
  _8x1_and _8x1_and_10 (
    .A0(Byte10_x0), .A1(Byte10_x1), .A2(Byte10_x2), .A3(Byte10_x3), .A4(Byte10_x4), .A5(Byte10_x5),
    .A6(Byte10_x6), .A7(Byte10_x7), .AND(_4b_decoder_1_p18), .X0(_8x1_and_10_x0), .X1(_8x1_and_10_x1),
    .X2(_8x1_and_10_x2), .X3(_8x1_and_10_x3), .X4(_8x1_and_10_x4), .X5(_8x1_and_10_x5), .X6(_8x1_and_10_x6),
    .X7(_8x1_and_10_x7));
  _16_byte_memory_line Byte10 (
    .A0(A4), .A1(A5), .A2(A6), .A3(A7), .X0(Byte10_x0), .X1(Byte10_x1), .X2(Byte10_x2), .X3(Byte10_x3),
    .X4(Byte10_x4), .X5(Byte10_x5), .X6(Byte10_x6), .X7(Byte10_x7));  // open: V0, V1, V2, V3, V4, V5, V6, V7, S
  _8x1_and _8x1_and_11 (
    .A0(Byte11_x0), .A1(Byte11_x1), .A2(Byte11_x2), .A3(Byte11_x3), .A4(Byte11_x4), .A5(Byte11_x5),
    .A6(Byte11_x6), .A7(Byte11_x7), .AND(_4b_decoder_1_p19), .X0(_8x1_and_11_x0), .X1(_8x1_and_11_x1),
    .X2(_8x1_and_11_x2), .X3(_8x1_and_11_x3), .X4(_8x1_and_11_x4), .X5(_8x1_and_11_x5), .X6(_8x1_and_11_x6),
    .X7(_8x1_and_11_x7));
  _16_byte_memory_line Byte11 (
    .A0(A4), .A1(A5), .A2(A6), .A3(A7), .X0(Byte11_x0), .X1(Byte11_x1), .X2(Byte11_x2), .X3(Byte11_x3),
    .X4(Byte11_x4), .X5(Byte11_x5), .X6(Byte11_x6), .X7(Byte11_x7));  // open: V0, V1, V2, V3, V4, V5, V6, V7, S
  _8_2b_ors _8_2b_ors_13 (
    .A0(_8_2b_ors_14_x0), .A1(_8_2b_ors_14_x1), .A2(_8_2b_ors_14_x2), .A3(_8_2b_ors_14_x3),
    .A4(_8_2b_ors_14_x4), .A5(_8_2b_ors_14_x5), .A6(_8_2b_ors_14_x6), .A7(_8_2b_ors_14_x7),
    .B0(_8_2b_ors_15_x0), .B1(_8_2b_ors_15_x1), .B2(_8_2b_ors_15_x2), .B3(_8_2b_ors_15_x3),
    .B4(_8_2b_ors_15_x4), .B5(_8_2b_ors_15_x5), .B6(_8_2b_ors_15_x6), .B7(_8_2b_ors_15_x7),
    .X0(_8_2b_ors_13_x0), .X1(_8_2b_ors_13_x1), .X2(_8_2b_ors_13_x2), .X3(_8_2b_ors_13_x3),
    .X4(_8_2b_ors_13_x4), .X5(_8_2b_ors_13_x5), .X6(_8_2b_ors_13_x6), .X7(_8_2b_ors_13_x7));
  _8_2b_ors _8_2b_ors_14 (
    .A0(_8x1_and_12_x0), .A1(_8x1_and_12_x1), .A2(_8x1_and_12_x2), .A3(_8x1_and_12_x3), .A4(_8x1_and_12_x4),
    .A5(_8x1_and_12_x5), .A6(_8x1_and_12_x6), .A7(_8x1_and_12_x7), .B0(_8x1_and_13_x0), .B1(_8x1_and_13_x1),
    .B2(_8x1_and_13_x2), .B3(_8x1_and_13_x3), .B4(_8x1_and_13_x4), .B5(_8x1_and_13_x5), .B6(_8x1_and_13_x6),
    .B7(_8x1_and_13_x7), .X0(_8_2b_ors_14_x0), .X1(_8_2b_ors_14_x1), .X2(_8_2b_ors_14_x2),
    .X3(_8_2b_ors_14_x3), .X4(_8_2b_ors_14_x4), .X5(_8_2b_ors_14_x5), .X6(_8_2b_ors_14_x6),
    .X7(_8_2b_ors_14_x7));
  _8x1_and _8x1_and_12 (
    .A0(Byte12_x0), .A1(Byte12_x1), .A2(Byte12_x2), .A3(Byte12_x3), .A4(Byte12_x4), .A5(Byte12_x5),
    .A6(Byte12_x6), .A7(Byte12_x7), .AND(_4b_decoder_1_p20), .X0(_8x1_and_12_x0), .X1(_8x1_and_12_x1),
    .X2(_8x1_and_12_x2), .X3(_8x1_and_12_x3), .X4(_8x1_and_12_x4), .X5(_8x1_and_12_x5), .X6(_8x1_and_12_x6),
    .X7(_8x1_and_12_x7));
  _16_byte_memory_line Byte12 (
    .A0(A4), .A1(A5), .A2(A6), .A3(A7), .X0(Byte12_x0), .X1(Byte12_x1), .X2(Byte12_x2), .X3(Byte12_x3),
    .X4(Byte12_x4), .X5(Byte12_x5), .X6(Byte12_x6), .X7(Byte12_x7));  // open: V0, V1, V2, V3, V4, V5, V6, V7, S
  _8x1_and _8x1_and_13 (
    .A0(Byte13_x0), .A1(Byte13_x1), .A2(Byte13_x2), .A3(Byte13_x3), .A4(Byte13_x4), .A5(Byte13_x5),
    .A6(Byte13_x6), .A7(Byte13_x7), .AND(_4b_decoder_1_p21), .X0(_8x1_and_13_x0), .X1(_8x1_and_13_x1),
    .X2(_8x1_and_13_x2), .X3(_8x1_and_13_x3), .X4(_8x1_and_13_x4), .X5(_8x1_and_13_x5), .X6(_8x1_and_13_x6),
    .X7(_8x1_and_13_x7));
  _16_byte_memory_line Byte13 (
    .A0(A4), .A1(A5), .A2(A6), .A3(A7), .X0(Byte13_x0), .X1(Byte13_x1), .X2(Byte13_x2), .X3(Byte13_x3),
    .X4(Byte13_x4), .X5(Byte13_x5), .X6(Byte13_x6), .X7(Byte13_x7));  // open: V0, V1, V2, V3, V4, V5, V6, V7, S
  _8_2b_ors _8_2b_ors_15 (
    .A0(_8x1_and_14_x0), .A1(_8x1_and_14_x1), .A2(_8x1_and_14_x2), .A3(_8x1_and_14_x3), .A4(_8x1_and_14_x4),
    .A5(_8x1_and_14_x5), .A6(_8x1_and_14_x6), .A7(_8x1_and_14_x7), .B0(_8x1_and_15_x0), .B1(_8x1_and_15_x1),
    .B2(_8x1_and_15_x2), .B3(_8x1_and_15_x3), .B4(_8x1_and_15_x4), .B5(_8x1_and_15_x5), .B6(_8x1_and_15_x6),
    .B7(_8x1_and_15_x7), .X0(_8_2b_ors_15_x0), .X1(_8_2b_ors_15_x1), .X2(_8_2b_ors_15_x2),
    .X3(_8_2b_ors_15_x3), .X4(_8_2b_ors_15_x4), .X5(_8_2b_ors_15_x5), .X6(_8_2b_ors_15_x6),
    .X7(_8_2b_ors_15_x7));
  _8x1_and _8x1_and_14 (
    .A0(Byte14_x0), .A1(Byte14_x1), .A2(Byte14_x2), .A3(Byte14_x3), .A4(Byte14_x4), .A5(Byte14_x5),
    .A6(Byte14_x6), .A7(Byte14_x7), .AND(_4b_decoder_1_p22), .X0(_8x1_and_14_x0), .X1(_8x1_and_14_x1),
    .X2(_8x1_and_14_x2), .X3(_8x1_and_14_x3), .X4(_8x1_and_14_x4), .X5(_8x1_and_14_x5), .X6(_8x1_and_14_x6),
    .X7(_8x1_and_14_x7));
  _16_byte_memory_line Byte14 (
    .A0(A4), .A1(A5), .A2(A6), .A3(A7), .X0(Byte14_x0), .X1(Byte14_x1), .X2(Byte14_x2), .X3(Byte14_x3),
    .X4(Byte14_x4), .X5(Byte14_x5), .X6(Byte14_x6), .X7(Byte14_x7));  // open: V0, V1, V2, V3, V4, V5, V6, V7, S
  _8x1_and _8x1_and_15 (
    .A0(Byte15_x0), .A1(Byte15_x1), .A2(Byte15_x2), .A3(Byte15_x3), .A4(Byte15_x4), .A5(Byte15_x5),
    .A6(Byte15_x6), .A7(Byte15_x7), .AND(_4b_decoder_1_p23), .X0(_8x1_and_15_x0), .X1(_8x1_and_15_x1),
    .X2(_8x1_and_15_x2), .X3(_8x1_and_15_x3), .X4(_8x1_and_15_x4), .X5(_8x1_and_15_x5), .X6(_8x1_and_15_x6),
    .X7(_8x1_and_15_x7));
  _16_byte_memory_line Byte15 (
    .A0(A4), .A1(A5), .A2(A6), .A3(A7), .X0(Byte15_x0), .X1(Byte15_x1), .X2(Byte15_x2), .X3(Byte15_x3),
    .X4(Byte15_x4), .X5(Byte15_x5), .X6(Byte15_x6), .X7(Byte15_x7));  // open: V0, V1, V2, V3, V4, V5, V6, V7, S
endmodule
