// Digital circuit 64k_ram_page.dig as structural Verilog
module _64k_ram_page (
  input  A0,
  input  A1,
  input  A3,
  input  A4,
  input  A2,
  input  A5,
  input  A6,
  input  A7,
  input  A8,
  input  A9,
  input  A10,
  input  A11,
  input  A12,
  input  A13,
  input  A14,
  input  A15,
  input  V0,
  input  V1,
  input  V2,
  input  V3,
  input  V4,
  input  V5,
  input  V6,
  input  V7,
  input  S,
  output X0,
  output X1,
  output X2,
  output X3,
  output X4,
  output X5,
  output X6,
  output X7
);

  wire _4b_decoder_1_p5, _4b_decoder_1_p6, _4b_decoder_1_p7, _4b_decoder_1_p8, _4b_decoder_1_p9,
       _4b_decoder_1_p10, _4b_decoder_1_p11, _4b_decoder_1_p12, _4b_decoder_1_p13, _4b_decoder_1_p14,
       _4b_decoder_1_p15, _4b_decoder_1_p16, _4b_decoder_1_p17, _4b_decoder_1_p18, _4b_decoder_1_p19,
       _4b_decoder_1_p20, _8_2b_ors_2_x0, _8_2b_ors_2_x1, _8_2b_ors_2_x2, _8_2b_ors_2_x3, _8_2b_ors_2_x4,
       _8_2b_ors_2_x5, _8_2b_ors_2_x6, _8_2b_ors_2_x7, _8_2b_ors_3_x0, _8_2b_ors_3_x1, _8_2b_ors_3_x2,
       _8_2b_ors_3_x3, _8_2b_ors_3_x4, _8_2b_ors_3_x5, _8_2b_ors_3_x6, _8_2b_ors_3_x7, _8_2b_ors_4_x0,
       _8_2b_ors_4_x1, _8_2b_ors_4_x2, _8_2b_ors_4_x3, _8_2b_ors_4_x4, _8_2b_ors_4_x5, _8_2b_ors_4_x6,
       _8_2b_ors_4_x7, _8_2b_ors_5_x0, _8_2b_ors_5_x1, _8_2b_ors_5_x2, _8_2b_ors_5_x3, _8_2b_ors_5_x4,
       _8_2b_ors_5_x5, _8_2b_ors_5_x6, _8_2b_ors_5_x7, _8_2b_ors_6_x0, _8_2b_ors_6_x1, _8_2b_ors_6_x2,
       _8_2b_ors_6_x3, _8_2b_ors_6_x4, _8_2b_ors_6_x5, _8_2b_ors_6_x6, _8_2b_ors_6_x7, _8_2b_ors_7_x0,
       _8_2b_ors_7_x1, _8_2b_ors_7_x2, _8_2b_ors_7_x3, _8_2b_ors_7_x4, _8_2b_ors_7_x5, _8_2b_ors_7_x6,
       _8_2b_ors_7_x7, _8_2b_ors_8_x0, _8_2b_ors_8_x1, _8_2b_ors_8_x2, _8_2b_ors_8_x3, _8_2b_ors_8_x4,
       _8_2b_ors_8_x5, _8_2b_ors_8_x6, _8_2b_ors_8_x7, _8_2b_ors_9_x0, _8_2b_ors_9_x1, _8_2b_ors_9_x2,
       _8_2b_ors_9_x3, _8_2b_ors_9_x4, _8_2b_ors_9_x5, _8_2b_ors_9_x6, _8_2b_ors_9_x7, _8_2b_ors_10_x0,
       _8_2b_ors_10_x1, _8_2b_ors_10_x2, _8_2b_ors_10_x3, _8_2b_ors_10_x4, _8_2b_ors_10_x5, _8_2b_ors_10_x6,
       _8_2b_ors_10_x7, _8_2b_ors_11_x0, _8_2b_ors_11_x1, _8_2b_ors_11_x2, _8_2b_ors_11_x3, _8_2b_ors_11_x4,
       _8_2b_ors_11_x5, _8_2b_ors_11_x6, _8_2b_ors_11_x7, _8_2b_ors_12_x0, _8_2b_ors_12_x1, _8_2b_ors_12_x2,
       _8_2b_ors_12_x3, _8_2b_ors_12_x4, _8_2b_ors_12_x5, _8_2b_ors_12_x6, _8_2b_ors_12_x7, _8_2b_ors_13_x0,
       _8_2b_ors_13_x1, _8_2b_ors_13_x2, _8_2b_ors_13_x3, _8_2b_ors_13_x4, _8_2b_ors_13_x5, _8_2b_ors_13_x6,
       _8_2b_ors_13_x7, _8_2b_ors_14_x0, _8_2b_ors_14_x1, _8_2b_ors_14_x2, _8_2b_ors_14_x3, _8_2b_ors_14_x4,
       _8_2b_ors_14_x5, _8_2b_ors_14_x6, _8_2b_ors_14_x7, _8_2b_ors_15_x0, _8_2b_ors_15_x1, _8_2b_ors_15_x2,
       _8_2b_ors_15_x3, _8_2b_ors_15_x4, _8_2b_ors_15_x5, _8_2b_ors_15_x6, _8_2b_ors_15_x7, _8x1_and_1_x0,
       _8x1_and_1_x1, _8x1_and_1_x2, _8x1_and_1_x3, _8x1_and_1_x4, _8x1_and_1_x5, _8x1_and_1_x6,
       _8x1_and_1_x7, _8x1_and_2_x0, _8x1_and_2_x1, _8x1_and_2_x2, _8x1_and_2_x3, _8x1_and_2_x4,
       _8x1_and_2_x5, _8x1_and_2_x6, _8x1_and_2_x7, _8x1_and_3_x0, _8x1_and_3_x1, _8x1_and_3_x2,
       _8x1_and_3_x3, _8x1_and_3_x4, _8x1_and_3_x5, _8x1_and_3_x6, _8x1_and_3_x7, _8x1_and_4_x0,
       _8x1_and_4_x1, _8x1_and_4_x2, _8x1_and_4_x3, _8x1_and_4_x4, _8x1_and_4_x5, _8x1_and_4_x6,
       _8x1_and_4_x7, _8x1_and_5_x0, _8x1_and_5_x1, _8x1_and_5_x2, _8x1_and_5_x3, _8x1_and_5_x4,
       _8x1_and_5_x5, _8x1_and_5_x6, _8x1_and_5_x7, _8x1_and_6_x0, _8x1_and_6_x1, _8x1_and_6_x2,
       _8x1_and_6_x3, _8x1_and_6_x4, _8x1_and_6_x5, _8x1_and_6_x6, _8x1_and_6_x7, _8x1_and_7_x0,
       _8x1_and_7_x1, _8x1_and_7_x2, _8x1_and_7_x3, _8x1_and_7_x4, _8x1_and_7_x5, _8x1_and_7_x6,
       _8x1_and_7_x7, _8x1_and_8_x0, _8x1_and_8_x1, _8x1_and_8_x2, _8x1_and_8_x3, _8x1_and_8_x4,
       _8x1_and_8_x5, _8x1_and_8_x6, _8x1_and_8_x7, _8x1_and_9_x0, _8x1_and_9_x1, _8x1_and_9_x2,
       _8x1_and_9_x3, _8x1_and_9_x4, _8x1_and_9_x5, _8x1_and_9_x6, _8x1_and_9_x7, _8x1_and_10_x0,
       _8x1_and_10_x1, _8x1_and_10_x2, _8x1_and_10_x3, _8x1_and_10_x4, _8x1_and_10_x5, _8x1_and_10_x6,
       _8x1_and_10_x7, _8x1_and_11_x0, _8x1_and_11_x1, _8x1_and_11_x2, _8x1_and_11_x3, _8x1_and_11_x4,
       _8x1_and_11_x5, _8x1_and_11_x6, _8x1_and_11_x7, _8x1_and_12_x0, _8x1_and_12_x1, _8x1_and_12_x2,
       _8x1_and_12_x3, _8x1_and_12_x4, _8x1_and_12_x5, _8x1_and_12_x6, _8x1_and_12_x7, _8x1_and_13_x0,
       _8x1_and_13_x1, _8x1_and_13_x2, _8x1_and_13_x3, _8x1_and_13_x4, _8x1_and_13_x5, _8x1_and_13_x6,
       _8x1_and_13_x7, _8x1_and_14_x0, _8x1_and_14_x1, _8x1_and_14_x2, _8x1_and_14_x3, _8x1_and_14_x4,
       _8x1_and_14_x5, _8x1_and_14_x6, _8x1_and_14_x7, _8x1_and_15_x0, _8x1_and_15_x1, _8x1_and_15_x2,
       _8x1_and_15_x3, _8x1_and_15_x4, _8x1_and_15_x5, _8x1_and_15_x6, _8x1_and_15_x7, _8x1_and_16_x0,
       _8x1_and_16_x1, _8x1_and_16_x2, _8x1_and_16_x3, _8x1_and_16_x4, _8x1_and_16_x5, _8x1_and_16_x6,
       _8x1_and_16_x7, and_1_out, and_2_out, and_3_out, and_4_out, and_5_out, and_6_out, and_7_out,
       and_8_out, and_9_out, and_10_out, and_11_out, and_12_out, and_13_out, and_14_out, and_15_out,
       and_16_out, Page0_x0, Page0_x1, Page0_x2, Page0_x3, Page0_x4, Page0_x5, Page0_x6, Page0_x7, Page1_x0,
       Page1_x1, Page1_x2, Page1_x3, Page1_x4, Page1_x5, Page1_x6, Page1_x7, Page2_x0, Page2_x1, Page2_x2,
       Page2_x3, Page2_x4, Page2_x5, Page2_x6, Page2_x7, Page3_x0, Page3_x1, Page3_x2, Page3_x3, Page3_x4,
       Page3_x5, Page3_x6, Page3_x7, Page4_x0, Page4_x1, Page4_x2, Page4_x3, Page4_x4, Page4_x5, Page4_x6,
       Page4_x7, Page5_x0, Page5_x1, Page5_x2, Page5_x3, Page5_x4, Page5_x5, Page5_x6, Page5_x7, Page6_x0,
       Page6_x1, Page6_x2, Page6_x3, Page6_x4, Page6_x5, Page6_x6, Page6_x7, Page7_x0, Page7_x1, Page7_x2,
       Page7_x3, Page7_x4, Page7_x5, Page7_x6, Page7_x7, Page8_x0, Page8_x1, Page8_x2, Page8_x3, Page8_x4,
       Page8_x5, Page8_x6, Page8_x7, Page9_x0, Page9_x1, Page9_x2, Page9_x3, Page9_x4, Page9_x5, Page9_x6,
       Page9_x7, Page10_x0, Page10_x1, Page10_x2, Page10_x3, Page10_x4, Page10_x5, Page10_x6, Page10_x7,
       Page11_x0, Page11_x1, Page11_x2, Page11_x3, Page11_x4, Page11_x5, Page11_x6, Page11_x7, Page12_x0,
       Page12_x1, Page12_x2, Page12_x3, Page12_x4, Page12_x5, Page12_x6, Page12_x7, Page13_x0, Page13_x1,
       Page13_x2, Page13_x3, Page13_x4, Page13_x5, Page13_x6, Page13_x7, Page14_x0, Page14_x1, Page14_x2,
       Page14_x3, Page14_x4, Page14_x5, Page14_x6, Page14_x7, Page15_x0, Page15_x1, Page15_x2, Page15_x3,
       Page15_x4, Page15_x5, Page15_x6, Page15_x7;

  _8_2b_ors _8_2b_ors_1 (
    .A0(_8_2b_ors_2_x0), .A1(_8_2b_ors_2_x1), .A2(_8_2b_ors_2_x2), .A3(_8_2b_ors_2_x3), .A4(_8_2b_ors_2_x4),
    .A5(_8_2b_ors_2_x5), .A6(_8_2b_ors_2_x6), .A7(_8_2b_ors_2_x7), .B0(_8_2b_ors_9_x0), .B1(_8_2b_ors_9_x1),
    .B2(_8_2b_ors_9_x2), .B3(_8_2b_ors_9_x3), .B4(_8_2b_ors_9_x4), .B5(_8_2b_ors_9_x5), .B6(_8_2b_ors_9_x6),
    .B7(_8_2b_ors_9_x7), .X0(X0), .X1(X1), .X2(X2), .X3(X3), .X4(X4), .X5(X5), .X6(X6), .X7(X7));
  _8_2b_ors _8_2b_ors_2 (
    .A0(_8_2b_ors_3_x0), .A1(_8_2b_ors_3_x1), .A2(_8_2b_ors_3_x2), .A3(_8_2b_ors_3_x3), .A4(_8_2b_ors_3_x4),
    .A5(_8_2b_ors_3_x5), .A6(_8_2b_ors_3_x6), .A7(_8_2b_ors_3_x7), .B0(_8_2b_ors_6_x0), .B1(_8_2b_ors_6_x1),
    .B2(_8_2b_ors_6_x2), .B3(_8_2b_ors_6_x3), .B4(_8_2b_ors_6_x4), .B5(_8_2b_ors_6_x5), .B6(_8_2b_ors_6_x6),
    .B7(_8_2b_ors_6_x7), .X0(_8_2b_ors_2_x0), .X1(_8_2b_ors_2_x1), .X2(_8_2b_ors_2_x2), .X3(_8_2b_ors_2_x3),
    .X4(_8_2b_ors_2_x4), .X5(_8_2b_ors_2_x5), .X6(_8_2b_ors_2_x6), .X7(_8_2b_ors_2_x7));
  _8_2b_ors _8_2b_ors_3 (
    .A0(_8_2b_ors_4_x0), .A1(_8_2b_ors_4_x1), .A2(_8_2b_ors_4_x2), .A3(_8_2b_ors_4_x3), .A4(_8_2b_ors_4_x4),
    .A5(_8_2b_ors_4_x5), .A6(_8_2b_ors_4_x6), .A7(_8_2b_ors_4_x7), .B0(_8_2b_ors_5_x0), .B1(_8_2b_ors_5_x1),
    .B2(_8_2b_ors_5_x2), .B3(_8_2b_ors_5_x3), .B4(_8_2b_ors_5_x4), .B5(_8_2b_ors_5_x5), .B6(_8_2b_ors_5_x6),
    .B7(_8_2b_ors_5_x7), .X0(_8_2b_ors_3_x0), .X1(_8_2b_ors_3_x1), .X2(_8_2b_ors_3_x2), .X3(_8_2b_ors_3_x3),
    .X4(_8_2b_ors_3_x4), .X5(_8_2b_ors_3_x5), .X6(_8_2b_ors_3_x6), .X7(_8_2b_ors_3_x7));
  _8_2b_ors _8_2b_ors_4 (
    .A0(_8x1_and_1_x0), .A1(_8x1_and_1_x1), .A2(_8x1_and_1_x2), .A3(_8x1_and_1_x3), .A4(_8x1_and_1_x4),
    .A5(_8x1_and_1_x5), .A6(_8x1_and_1_x6), .A7(_8x1_and_1_x7), .B0(_8x1_and_2_x0), .B1(_8x1_and_2_x1),
    .B2(_8x1_and_2_x2), .B3(_8x1_and_2_x3), .B4(_8x1_and_2_x4), .B5(_8x1_and_2_x5), .B6(_8x1_and_2_x6),
    .B7(_8x1_and_2_x7), .X0(_8_2b_ors_4_x0), .X1(_8_2b_ors_4_x1), .X2(_8_2b_ors_4_x2), .X3(_8_2b_ors_4_x3),
    .X4(_8_2b_ors_4_x4), .X5(_8_2b_ors_4_x5), .X6(_8_2b_ors_4_x6), .X7(_8_2b_ors_4_x7));
  _8x1_and _8x1_and_1 (
    .A0(Page0_x0), .A1(Page0_x1), .A2(Page0_x2), .A3(Page0_x3), .A4(Page0_x4), .A5(Page0_x5), .A6(Page0_x6),
    .A7(Page0_x7), .AND(_4b_decoder_1_p5), .X0(_8x1_and_1_x0), .X1(_8x1_and_1_x1), .X2(_8x1_and_1_x2),
    .X3(_8x1_and_1_x3), .X4(_8x1_and_1_x4), .X5(_8x1_and_1_x5), .X6(_8x1_and_1_x6), .X7(_8x1_and_1_x7));
  _4k_ram_page Page0 (
    .A0(A0), .A1(A1), .A3(A2), .A4(A3), .A2(A4), .A5(A5), .A6(A6), .A7(A7), .A8(A7), .A9(A9), .A10(A10),
    .A11(A11), .V0(V0), .V1(V1), .V2(V2), .V3(V3), .V4(V4), .V5(V5), .V6(V6), .V7(V7), .S(and_1_out),
    .X0(Page0_x0), .X1(Page0_x1), .X2(Page0_x2), .X3(Page0_x3), .X4(Page0_x4), .X5(Page0_x5), .X6(Page0_x6),
    .X7(Page0_x7));
  // _4b_decoder _4b_decoder_1: pin names not known; wires that end beside it: A12, A13, A14, A15, _4b_decoder_1_p5, _4b_decoder_1_p6, _4b_decoder_1_p7, _4b_decoder_1_p8, _4b_decoder_1_p9, _4b_decoder_1_p10, _4b_decoder_1_p11, _4b_decoder_1_p12, _4b_decoder_1_p13, _4b_decoder_1_p14, _4b_decoder_1_p15, _4b_decoder_1_p16, _4b_decoder_1_p17, _4b_decoder_1_p18, _4b_decoder_1_p19, _4b_decoder_1_p20
  and and_1 (and_1_out, S, _4b_decoder_1_p5);
  _8x1_and _8x1_and_2 (
    .A0(Page1_x0), .A1(Page1_x1), .A2(Page1_x2), .A3(Page1_x3), .A4(Page1_x4), .A5(Page1_x5), .A6(Page1_x6),
    .A7(Page1_x7), .AND(_4b_decoder_1_p6), .X0(_8x1_and_2_x0), .X1(_8x1_and_2_x1), .X2(_8x1_and_2_x2),
    .X3(_8x1_and_2_x3), .X4(_8x1_and_2_x4), .X5(_8x1_and_2_x5), .X6(_8x1_and_2_x6), .X7(_8x1_and_2_x7));
  _4k_ram_page Page1 (
    .A0(A0), .A1(A1), .A3(A2), .A4(A3), .A2(A4), .A5(A5), .A6(A6), .A7(A7), .A8(A7), .A9(A9), .A10(A10),
    .A11(A11), .V0(V0), .V1(V1), .V2(V2), .V3(V3), .V4(V4), .V5(V5), .V6(V6), .V7(V7), .S(and_2_out),
    .X0(Page1_x0), .X1(Page1_x1), .X2(Page1_x2), .X3(Page1_x3), .X4(Page1_x4), .X5(Page1_x5), .X6(Page1_x6),
    .X7(Page1_x7));
  and and_2 (and_2_out, S, _4b_decoder_1_p6);
  _8_2b_ors _8_2b_ors_5 (
    .A0(_8x1_and_3_x0), .A1(_8x1_and_3_x1), .A2(_8x1_and_3_x2), .A3(_8x1_and_3_x3), .A4(_8x1_and_3_x4),
    .A5(_8x1_and_3_x5), .A6(_8x1_and_3_x6), .A7(_8x1_and_3_x7), .B0(_8x1_and_4_x0), .B1(_8x1_and_4_x1),
    .B2(_8x1_and_4_x2), .B3(_8x1_and_4_x3), .B4(_8x1_and_4_x4), .B5(_8x1_and_4_x5), .B6(_8x1_and_4_x6),
    .B7(_8x1_and_4_x7), .X0(_8_2b_ors_5_x0), .X1(_8_2b_ors_5_x1), .X2(_8_2b_ors_5_x2), .X3(_8_2b_ors_5_x3),
    .X4(_8_2b_ors_5_x4), .X5(_8_2b_ors_5_x5), .X6(_8_2b_ors_5_x6), .X7(_8_2b_ors_5_x7));
  _8x1_and _8x1_and_3 (
    .A0(Page2_x0), .A1(Page2_x1), .A2(Page2_x2), .A3(Page2_x3), .A4(Page2_x4), .A5(Page2_x5), .A6(Page2_x6),
    .A7(Page2_x7), .AND(_4b_decoder_1_p7), .X0(_8x1_and_3_x0), .X1(_8x1_and_3_x1), .X2(_8x1_and_3_x2),
    .X3(_8x1_and_3_x3), .X4(_8x1_and_3_x4), .X5(_8x1_and_3_x5), .X6(_8x1_and_3_x6), .X7(_8x1_and_3_x7));
  _4k_ram_page Page2 (
    .A0(A0), .A1(A1), .A3(A2), .A4(A3), .A2(A4), .A5(A5), .A6(A6), .A7(A7), .A8(A7), .A9(A9), .A10(A10),
    .A11(A11), .V0(V0), .V1(V1), .V2(V2), .V3(V3), .V4(V4), .V5(V5), .V6(V6), .V7(V7), .S(and_3_out),
    .X0(Page2_x0), .X1(Page2_x1), .X2(Page2_x2), .X3(Page2_x3), .X4(Page2_x4), .X5(Page2_x5), .X6(Page2_x6),
    .X7(Page2_x7));
  and and_3 (and_3_out, S, _4b_decoder_1_p7);
  _8x1_and _8x1_and_4 (
    .A0(Page3_x0), .A1(Page3_x1), .A2(Page3_x2), .A3(Page3_x3), .A4(Page3_x4), .A5(Page3_x5), .A6(Page3_x6),
    .A7(Page3_x7), .AND(_4b_decoder_1_p8), .X0(_8x1_and_4_x0), .X1(_8x1_and_4_x1), .X2(_8x1_and_4_x2),
    .X3(_8x1_and_4_x3), .X4(_8x1_and_4_x4), .X5(_8x1_and_4_x5), .X6(_8x1_and_4_x6), .X7(_8x1_and_4_x7));
  _4k_ram_page Page3 (
    .A0(A0), .A1(A1), .A3(A2), .A4(A3), .A2(A4), .A5(A5), .A6(A6), .A7(A7), .A8(A7), .A9(A9), .A10(A10),
    .A11(A11), .V0(V0), .V1(V1), .V2(V2), .V3(V3), .V4(V4), .V5(V5), .V6(V6), .V7(V7), .S(and_4_out),
    .X0(Page3_x0), .X1(Page3_x1), .X2(Page3_x2), .X3(Page3_x3), .X4(Page3_x4), .X5(Page3_x5), .X6(Page3_x6),
    .X7(Page3_x7));
  and and_4 (and_4_out, S, _4b_decoder_1_p8);
  _8_2b_ors _8_2b_ors_6 (
    .A0(_8_2b_ors_7_x0), .A1(_8_2b_ors_7_x1), .A2(_8_2b_ors_7_x2), .A3(_8_2b_ors_7_x3), .A4(_8_2b_ors_7_x4),
    .A5(_8_2b_ors_7_x5), .A6(_8_2b_ors_7_x6), .A7(_8_2b_ors_7_x7), .B0(_8_2b_ors_8_x0), .B1(_8_2b_ors_8_x1),
    .B2(_8_2b_ors_8_x2), .B3(_8_2b_ors_8_x3), .B4(_8_2b_ors_8_x4), .B5(_8_2b_ors_8_x5), .B6(_8_2b_ors_8_x6),
    .B7(_8_2b_ors_8_x7), .X0(_8_2b_ors_6_x0), .X1(_8_2b_ors_6_x1), .X2(_8_2b_ors_6_x2), .X3(_8_2b_ors_6_x3),
    .X4(_8_2b_ors_6_x4), .X5(_8_2b_ors_6_x5), .X6(_8_2b_ors_6_x6), .X7(_8_2b_ors_6_x7));
  _8_2b_ors _8_2b_ors_7 (
    .A0(_8x1_and_5_x0), .A1(_8x1_and_5_x1), .A2(_8x1_and_5_x2), .A3(_8x1_and_5_x3), .A4(_8x1_and_5_x4),
    .A5(_8x1_and_5_x5), .A6(_8x1_and_5_x6), .A7(_8x1_and_5_x7), .B0(_8x1_and_6_x0), .B1(_8x1_and_6_x1),
    .B2(_8x1_and_6_x2), .B3(_8x1_and_6_x3), .B4(_8x1_and_6_x4), .B5(_8x1_and_6_x5), .B6(_8x1_and_6_x6),
    .B7(_8x1_and_6_x7), .X0(_8_2b_ors_7_x0), .X1(_8_2b_ors_7_x1), .X2(_8_2b_ors_7_x2), .X3(_8_2b_ors_7_x3),
    .X4(_8_2b_ors_7_x4), .X5(_8_2b_ors_7_x5), .X6(_8_2b_ors_7_x6), .X7(_8_2b_ors_7_x7));
  _8x1_and _8x1_and_5 (
    .A0(Page4_x0), .A1(Page4_x1), .A2(Page4_x2), .A3(Page4_x3), .A4(Page4_x4), .A5(Page4_x5), .A6(Page4_x6),
    .A7(Page4_x7), .AND(_4b_decoder_1_p9), .X0(_8x1_and_5_x0), .X1(_8x1_and_5_x1), .X2(_8x1_and_5_x2),
    .X3(_8x1_and_5_x3), .X4(_8x1_and_5_x4), .X5(_8x1_and_5_x5), .X6(_8x1_and_5_x6), .X7(_8x1_and_5_x7));
  _4k_ram_page Page4 (
    .A0(A0), .A1(A1), .A3(A2), .A4(A3), .A2(A4), .A5(A5), .A6(A6), .A7(A7), .A8(A7), .A9(A9), .A10(A10),
    .A11(A11), .V0(V0), .V1(V1), .V2(V2), .V3(V3), .V4(V4), .V5(V5), .V6(V6), .V7(V7), .S(and_5_out),
    .X0(Page4_x0), .X1(Page4_x1), .X2(Page4_x2), .X3(Page4_x3), .X4(Page4_x4), .X5(Page4_x5), .X6(Page4_x6),
    .X7(Page4_x7));
  and and_5 (and_5_out, S, _4b_decoder_1_p9);
  _8x1_and _8x1_and_6 (
    .A0(Page5_x0), .A1(Page5_x1), .A2(Page5_x2), .A3(Page5_x3), .A4(Page5_x4), .A5(Page5_x5), .A6(Page5_x6),
    .A7(Page5_x7), .AND(_4b_decoder_1_p10), .X0(_8x1_and_6_x0), .X1(_8x1_and_6_x1), .X2(_8x1_and_6_x2),
    .X3(_8x1_and_6_x3), .X4(_8x1_and_6_x4), .X5(_8x1_and_6_x5), .X6(_8x1_and_6_x6), .X7(_8x1_and_6_x7));
  _4k_ram_page Page5 (
    .A0(A0), .A1(A1), .A3(A2), .A4(A3), .A2(A4), .A5(A5), .A6(A6), .A7(A7), .A8(A7), .A9(A9), .A10(A10),
    .A11(A11), .V0(V0), .V1(V1), .V2(V2), .V3(V3), .V4(V4), .V5(V5), .V6(V6), .V7(V7), .S(and_6_out),
    .X0(Page5_x0), .X1(Page5_x1), .X2(Page5_x2), .X3(Page5_x3), .X4(Page5_x4), .X5(Page5_x5), .X6(Page5_x6),
    .X7(Page5_x7));
  and and_6 (and_6_out, S, _4b_decoder_1_p10);
  _8_2b_ors _8_2b_ors_8 (
    .A0(_8x1_and_7_x0), .A1(_8x1_and_7_x1), .A2(_8x1_and_7_x2), .A3(_8x1_and_7_x3), .A4(_8x1_and_7_x4),
    .A5(_8x1_and_7_x5), .A6(_8x1_and_7_x6), .A7(_8x1_and_7_x7), .B0(_8x1_and_8_x0), .B1(_8x1_and_8_x1),
    .B2(_8x1_and_8_x2), .B3(_8x1_and_8_x3), .B4(_8x1_and_8_x4), .B5(_8x1_and_8_x5), .B6(_8x1_and_8_x6),
    .B7(_8x1_and_8_x7), .X0(_8_2b_ors_8_x0), .X1(_8_2b_ors_8_x1), .X2(_8_2b_ors_8_x2), .X3(_8_2b_ors_8_x3),
    .X4(_8_2b_ors_8_x4), .X5(_8_2b_ors_8_x5), .X6(_8_2b_ors_8_x6), .X7(_8_2b_ors_8_x7));
  _8x1_and _8x1_and_7 (
    .A0(Page6_x0), .A1(Page6_x1), .A2(Page6_x2), .A3(Page6_x3), .A4(Page6_x4), .A5(Page6_x5), .A6(Page6_x6),
    .A7(Page6_x7), .AND(_4b_decoder_1_p11), .X0(_8x1_and_7_x0), .X1(_8x1_and_7_x1), .X2(_8x1_and_7_x2),
    .X3(_8x1_and_7_x3), .X4(_8x1_and_7_x4), .X5(_8x1_and_7_x5), .X6(_8x1_and_7_x6), .X7(_8x1_and_7_x7));
  _4k_ram_page Page6 (
    .A0(A0), .A1(A1), .A3(A2), .A4(A3), .A2(A4), .A5(A5), .A6(A6), .A7(A7), .A8(A7), .A9(A9), .A10(A10),
    .A11(A11), .V0(V0), .V1(V1), .V2(V2), .V3(V3), .V4(V4), .V5(V5), .V6(V6), .V7(V7), .S(and_7_out),
    .X0(Page6_x0), .X1(Page6_x1), .X2(Page6_x2), .X3(Page6_x3), .X4(Page6_x4), .X5(Page6_x5), .X6(Page6_x6),
    .X7(Page6_x7));
  and and_7 (and_7_out, S, _4b_decoder_1_p11);
  _8x1_and _8x1_and_8 (
    .A0(Page7_x0), .A1(Page7_x1), .A2(Page7_x2), .A3(Page7_x3), .A4(Page7_x4), .A5(Page7_x5), .A6(Page7_x6),
    .A7(Page7_x7), .AND(_4b_decoder_1_p12), .X0(_8x1_and_8_x0), .X1(_8x1_and_8_x1), .X2(_8x1_and_8_x2),
    .X3(_8x1_and_8_x3), .X4(_8x1_and_8_x4), .X5(_8x1_and_8_x5), .X6(_8x1_and_8_x6), .X7(_8x1_and_8_x7));
  _4k_ram_page Page7 (
    .A0(A0), .A1(A1), .A3(A2), .A4(A3), .A2(A4), .A5(A5), .A6(A6), .A7(A7), .A8(A9), .A9(A10), .A10(A11),
    .V0(V0), .V1(V1), .V2(V2), .V3(V3), .V4(V4), .V5(V5), .V6(V6), .V7(V7), .S(and_8_out), .X0(Page7_x0),
    .X1(Page7_x1), .X2(Page7_x2), .X3(Page7_x3), .X4(Page7_x4), .X5(Page7_x5), .X6(Page7_x6), .X7(Page7_x7));  // open: A11
  and and_8 (and_8_out, S, _4b_decoder_1_p12);
  _8_2b_ors _8_2b_ors_9 (
    .A0(_8_2b_ors_10_x0), .A1(_8_2b_ors_10_x1), .A2(_8_2b_ors_10_x2), .A3(_8_2b_ors_10_x3),
    .A4(_8_2b_ors_10_x4), .A5(_8_2b_ors_10_x5), .A6(_8_2b_ors_10_x6), .A7(_8_2b_ors_10_x7),
    .B0(_8_2b_ors_13_x0), .B1(_8_2b_ors_13_x1), .B2(_8_2b_ors_13_x2), .B3(_8_2b_ors_13_x3),
    .B4(_8_2b_ors_13_x4), .B5(_8_2b_ors_13_x5), .B6(_8_2b_ors_13_x6), .B7(_8_2b_ors_13_x7),
    .X0(_8_2b_ors_9_x0), .X1(_8_2b_ors_9_x1), .X2(_8_2b_ors_9_x2), .X3(_8_2b_ors_9_x3), .X4(_8_2b_ors_9_x4),
    .X5(_8_2b_ors_9_x5), .X6(_8_2b_ors_9_x6), .X7(_8_2b_ors_9_x7));
  _8_2b_ors _8_2b_ors_10 (
    .A0(_8_2b_ors_11_x0), .A1(_8_2b_ors_11_x1), .A2(_8_2b_ors_11_x2), .A3(_8_2b_ors_11_x3),
    .A4(_8_2b_ors_11_x4), .A5(_8_2b_ors_11_x5), .A6(_8_2b_ors_11_x6), .A7(_8_2b_ors_11_x7),
    .B0(_8_2b_ors_12_x0), .B1(_8_2b_ors_12_x1), .B2(_8_2b_ors_12_x2), .B3(_8_2b_ors_12_x3),
    .B4(_8_2b_ors_12_x4), .B5(_8_2b_ors_12_x5), .B6(_8_2b_ors_12_x6), .B7(_8_2b_ors_12_x7),
    .X0(_8_2b_ors_10_x0), .X1(_8_2b_ors_10_x1), .X2(_8_2b_ors_10_x2), .X3(_8_2b_ors_10_x3),
    .X4(_8_2b_ors_10_x4), .X5(_8_2b_ors_10_x5), .X6(_8_2b_ors_10_x6), .X7(_8_2b_ors_10_x7));
  _8_2b_ors _8_2b_ors_11 (
    .A0(_8x1_and_9_x0), .A1(_8x1_and_9_x1), .A2(_8x1_and_9_x2), .A3(_8x1_and_9_x3), .A4(_8x1_and_9_x4),
    .A5(_8x1_and_9_x5), .A6(_8x1_and_9_x6), .A7(_8x1_and_9_x7), .B0(_8x1_and_10_x0), .B1(_8x1_and_10_x1),
    .B2(_8x1_and_10_x2), .B3(_8x1_and_10_x3), .B4(_8x1_and_10_x4), .B5(_8x1_and_10_x5), .B6(_8x1_and_10_x6),
    .B7(_8x1_and_10_x7), .X0(_8_2b_ors_11_x0), .X1(_8_2b_ors_11_x1), .X2(_8_2b_ors_11_x2),
    .X3(_8_2b_ors_11_x3), .X4(_8_2b_ors_11_x4), .X5(_8_2b_ors_11_x5), .X6(_8_2b_ors_11_x6),
    .X7(_8_2b_ors_11_x7));
  _8x1_and _8x1_and_9 (
    .A0(Page8_x0), .A1(Page8_x1), .A2(Page8_x2), .A3(Page8_x3), .A4(Page8_x4), .A5(Page8_x5), .A6(Page8_x6),
    .A7(Page8_x7), .AND(_4b_decoder_1_p13), .X0(_8x1_and_9_x0), .X1(_8x1_and_9_x1), .X2(_8x1_and_9_x2),
    .X3(_8x1_and_9_x3), .X4(_8x1_and_9_x4), .X5(_8x1_and_9_x5), .X6(_8x1_and_9_x6), .X7(_8x1_and_9_x7));
  _4k_ram_page Page8 (
    .A0(A0), .A1(A1), .A3(A2), .A4(A3), .A2(A4), .A5(A5), .A6(A6), .A7(A7), .A8(A7), .A9(A9), .A10(A10),
    .A11(A11), .V0(V0), .V1(V1), .V2(V2), .V3(V3), .V4(V4), .V5(V5), .V6(V6), .V7(V7), .S(and_9_out),
    .X0(Page8_x0), .X1(Page8_x1), .X2(Page8_x2), .X3(Page8_x3), .X4(Page8_x4), .X5(Page8_x5), .X6(Page8_x6),
    .X7(Page8_x7));
  and and_9 (and_9_out, S, _4b_decoder_1_p13);
  _8x1_and _8x1_and_10 (
    .A0(Page9_x0), .A1(Page9_x1), .A2(Page9_x2), .A3(Page9_x3), .A4(Page9_x4), .A5(Page9_x5), .A6(Page9_x6),
    .A7(Page9_x7), .AND(_4b_decoder_1_p14), .X0(_8x1_and_10_x0), .X1(_8x1_and_10_x1), .X2(_8x1_and_10_x2),
    .X3(_8x1_and_10_x3), .X4(_8x1_and_10_x4), .X5(_8x1_and_10_x5), .X6(_8x1_and_10_x6), .X7(_8x1_and_10_x7));
  _4k_ram_page Page9 (
    .A0(A0), .A1(A1), .A3(A2), .A4(A3), .A2(A4), .A5(A5), .A6(A6), .A7(A7), .A8(A7), .A9(A9), .A10(A10),
    .A11(A11), .V0(V0), .V1(V1), .V2(V2), .V3(V3), .V4(V4), .V5(V5), .V6(V6), .V7(V7), .S(and_10_out),
    .X0(Page9_x0), .X1(Page9_x1), .X2(Page9_x2), .X3(Page9_x3), .X4(Page9_x4), .X5(Page9_x5), .X6(Page9_x6),
    .X7(Page9_x7));
  and and_10 (and_10_out, S, _4b_decoder_1_p14);
  _8_2b_ors _8_2b_ors_12 (
    .A0(_8x1_and_11_x0), .A1(_8x1_and_11_x1), .A2(_8x1_and_11_x2), .A3(_8x1_and_11_x3), .A4(_8x1_and_11_x4),
    .A5(_8x1_and_11_x5), .A6(_8x1_and_11_x6), .A7(_8x1_and_11_x7), .B0(_8x1_and_12_x0), .B1(_8x1_and_12_x1),
    .B2(_8x1_and_12_x2), .B3(_8x1_and_12_x3), .B4(_8x1_and_12_x4), .B5(_8x1_and_12_x5), .B6(_8x1_and_12_x6),
    .B7(_8x1_and_12_x7), .X0(_8_2b_ors_12_x0), .X1(_8_2b_ors_12_x1), .X2(_8_2b_ors_12_x2),
    .X3(_8_2b_ors_12_x3), .X4(_8_2b_ors_12_x4), .X5(_8_2b_ors_12_x5), .X6(_8_2b_ors_12_x6),
    .X7(_8_2b_ors_12_x7));
  _8x1_and _8x1_and_11 (
    .A0(Page10_x0), .A1(Page10_x1), .A2(Page10_x2), .A3(Page10_x3), .A4(Page10_x4), .A5(Page10_x5),
    .A6(Page10_x6), .A7(Page10_x7), .AND(_4b_decoder_1_p15), .X0(_8x1_and_11_x0), .X1(_8x1_and_11_x1),
    .X2(_8x1_and_11_x2), .X3(_8x1_and_11_x3), .X4(_8x1_and_11_x4), .X5(_8x1_and_11_x5), .X6(_8x1_and_11_x6),
    .X7(_8x1_and_11_x7));
  _4k_ram_page Page10 (
    .A0(A0), .A1(A1), .A3(A2), .A4(A3), .A2(A4), .A5(A5), .A6(A6), .A7(A7), .A8(A7), .A9(A9), .A10(A10),
    .A11(A11), .V0(V0), .V1(V1), .V2(V2), .V3(V3), .V4(V4), .V5(V5), .V6(V6), .V7(V7), .S(and_11_out),
    .X0(Page10_x0), .X1(Page10_x1), .X2(Page10_x2), .X3(Page10_x3), .X4(Page10_x4), .X5(Page10_x5),
    .X6(Page10_x6), .X7(Page10_x7));
  and and_11 (and_11_out, S, _4b_decoder_1_p15);
  _8x1_and _8x1_and_12 (
    .A0(Page11_x0), .A1(Page11_x1), .A2(Page11_x2), .A3(Page11_x3), .A4(Page11_x4), .A5(Page11_x5),
    .A6(Page11_x6), .A7(Page11_x7), .AND(_4b_decoder_1_p16), .X0(_8x1_and_12_x0), .X1(_8x1_and_12_x1),
    .X2(_8x1_and_12_x2), .X3(_8x1_and_12_x3), .X4(_8x1_and_12_x4), .X5(_8x1_and_12_x5), .X6(_8x1_and_12_x6),
    .X7(_8x1_and_12_x7));
  _4k_ram_page Page11 (
    .A0(A0), .A1(A1), .A3(A2), .A4(A3), .A2(A4), .A5(A5), .A6(A6), .A7(A7), .A8(A7), .A9(A9), .A10(A10),
    .A11(A11), .V0(V0), .V1(V1), .V2(V2), .V3(V3), .V4(V4), .V5(V5), .V6(V6), .V7(V7), .S(and_12_out),
    .X0(Page11_x0), .X1(Page11_x1), .X2(Page11_x2), .X3(Page11_x3), .X4(Page11_x4), .X5(Page11_x5),
    .X6(Page11_x6), .X7(Page11_x7));
  and and_12 (and_12_out, S, _4b_decoder_1_p16);
  _8_2b_ors _8_2b_ors_13 (
    .A0(_8_2b_ors_14_x0), .A1(_8_2b_ors_14_x1), .A2(_8_2b_ors_14_x2), .A3(_8_2b_ors_14_x3),
    .A4(_8_2b_ors_14_x4), .A5(_8_2b_ors_14_x5), .A6(_8_2b_ors_14_x6), .A7(_8_2b_ors_14_x7),
    .B0(_8_2b_ors_15_x0), .B1(_8_2b_ors_15_x1), .B2(_8_2b_ors_15_x2), .B3(_8_2b_ors_15_x3),
    .B4(_8_2b_ors_15_x4), .B5(_8_2b_ors_15_x5), .B6(_8_2b_ors_15_x6), .B7(_8_2b_ors_15_x7),
    .X0(_8_2b_ors_13_x0), .X1(_8_2b_ors_13_x1), .X2(_8_2b_ors_13_x2), .X3(_8_2b_ors_13_x3),
    .X4(_8_2b_ors_13_x4), .X5(_8_2b_ors_13_x5), .X6(_8_2b_ors_13_x6), .X7(_8_2b_ors_13_x7));
  _8_2b_ors _8_2b_ors_14 (
    .A0(_8x1_and_13_x0), .A1(_8x1_and_13_x1), .A2(_8x1_and_13_x2), .A3(_8x1_and_13_x3), .A4(_8x1_and_13_x4),
    .A5(_8x1_and_13_x5), .A6(_8x1_and_13_x6), .A7(_8x1_and_13_x7), .B0(_8x1_and_14_x0), .B1(_8x1_and_14_x1),
    .B2(_8x1_and_14_x2), .B3(_8x1_and_14_x3), .B4(_8x1_and_14_x4), .B5(_8x1_and_14_x5), .B6(_8x1_and_14_x6),
    .B7(_8x1_and_14_x7), .X0(_8_2b_ors_14_x0), .X1(_8_2b_ors_14_x1), .X2(_8_2b_ors_14_x2),
    .X3(_8_2b_ors_14_x3), .X4(_8_2b_ors_14_x4), .X5(_8_2b_ors_14_x5), .X6(_8_2b_ors_14_x6),
    .X7(_8_2b_ors_14_x7));
  _8x1_and _8x1_and_13 (
    .A0(Page12_x0), .A1(Page12_x1), .A2(Page12_x2), .A3(Page12_x3), .A4(Page12_x4), .A5(Page12_x5),
    .A6(Page12_x6), .A7(Page12_x7), .AND(_4b_decoder_1_p17), .X0(_8x1_and_13_x0), .X1(_8x1_and_13_x1),
    .X2(_8x1_and_13_x2), .X3(_8x1_and_13_x3), .X4(_8x1_and_13_x4), .X5(_8x1_and_13_x5), .X6(_8x1_and_13_x6),
    .X7(_8x1_and_13_x7));
  _4k_ram_page Page12 (
    .A0(A0), .A1(A1), .A3(A2), .A4(A3), .A2(A4), .A5(A5), .A6(A6), .A7(A7), .A8(A7), .A9(A9), .A10(A10),
    .A11(A11), .V0(V0), .V1(V1), .V2(V2), .V3(V3), .V4(V4), .V5(V5), .V6(V6), .V7(V7), .S(and_13_out),
    .X0(Page12_x0), .X1(Page12_x1), .X2(Page12_x2), .X3(Page12_x3), .X4(Page12_x4), .X5(Page12_x5),
    .X6(Page12_x6), .X7(Page12_x7));
  and and_13 (and_13_out, S, _4b_decoder_1_p17);
  _8x1_and _8x1_and_14 (
    .A0(Page13_x0), .A1(Page13_x1), .A2(Page13_x2), .A3(Page13_x3), .A4(Page13_x4), .A5(Page13_x5),
    .A6(Page13_x6), .A7(Page13_x7), .AND(_4b_decoder_1_p18), .X0(_8x1_and_14_x0), .X1(_8x1_and_14_x1),
    .X2(_8x1_and_14_x2), .X3(_8x1_and_14_x3), .X4(_8x1_and_14_x4), .X5(_8x1_and_14_x5), .X6(_8x1_and_14_x6),
    .X7(_8x1_and_14_x7));
  _4k_ram_page Page13 (
    .A0(A0), .A1(A1), .A3(A2), .A4(A3), .A2(A4), .A5(A5), .A6(A6), .A7(A7), .A8(A7), .A9(A9), .A10(A10),
    .A11(A11), .V0(V0), .V1(V1), .V2(V2), .V3(V3), .V4(V4), .V5(V5), .V6(V6), .V7(V7), .S(and_14_out),
    .X0(Page13_x0), .X1(Page13_x1), .X2(Page13_x2), .X3(Page13_x3), .X4(Page13_x4), .X5(Page13_x5),
    .X6(Page13_x6), .X7(Page13_x7));
  and and_14 (and_14_out, S, _4b_decoder_1_p18);
  _8_2b_ors _8_2b_ors_15 (
    .A0(_8x1_and_15_x0), .A1(_8x1_and_15_x1), .A2(_8x1_and_15_x2), .A3(_8x1_and_15_x3), .A4(_8x1_and_15_x4),
    .A5(_8x1_and_15_x5), .A6(_8x1_and_15_x6), .A7(_8x1_and_15_x7), .B0(_8x1_and_16_x0), .B1(_8x1_and_16_x1),
    .B2(_8x1_and_16_x2), .B3(_8x1_and_16_x3), .B4(_8x1_and_16_x4), .B5(_8x1_and_16_x5), .B6(_8x1_and_16_x6),
    .B7(_8x1_and_16_x7), .X0(_8_2b_ors_15_x0), .X1(_8_2b_ors_15_x1), .X2(_8_2b_ors_15_x2),
    .X3(_8_2b_ors_15_x3), .X4(_8_2b_ors_15_x4), .X5(_8_2b_ors_15_x5), .X6(_8_2b_ors_15_x6),
    .X7(_8_2b_ors_15_x7));
  _8x1_and _8x1_and_15 (
    .A0(Page14_x0), .A1(Page14_x1), .A2(Page14_x2), .A3(Page14_x3), .A4(Page14_x4), .A5(Page14_x5),
    .A6(Page14_x6), .A7(Page14_x7), .AND(_4b_decoder_1_p19), .X0(_8x1_and_15_x0), .X1(_8x1_and_15_x1),
    .X2(_8x1_and_15_x2), .X3(_8x1_and_15_x3), .X4(_8x1_and_15_x4), .X5(_8x1_and_15_x5), .X6(_8x1_and_15_x6),
    .X7(_8x1_and_15_x7));
  _4k_ram_page Page14 (
    .A0(A0), .A1(A1), .A3(A2), .A4(A3), .A2(A4), .A5(A5), .A6(A6), .A7(A7), .A8(A7), .A9(A9), .A10(A10),
    .A11(A11), .V0(V0), .V1(V1), .V2(V2), .V3(V3), .V4(V4), .V5(V5), .V6(V6), .V7(V7), .S(and_15_out),
    .X0(Page14_x0), .X1(Page14_x1), .X2(Page14_x2), .X3(Page14_x3), .X4(Page14_x4), .X5(Page14_x5),
    .X6(Page14_x6), .X7(Page14_x7));
  and and_15 (and_15_out, S, _4b_decoder_1_p19);
  _8x1_and _8x1_and_16 (
    .A0(Page15_x0), .A1(Page15_x1), .A2(Page15_x2), .A3(Page15_x3), .A4(Page15_x4), .A5(Page15_x5),
    .A6(Page15_x6), .A7(Page15_x7), .AND(_4b_decoder_1_p20), .X0(_8x1_and_16_x0), .X1(_8x1_and_16_x1),
    .X2(_8x1_and_16_x2), .X3(_8x1_and_16_x3), .X4(_8x1_and_16_x4), .X5(_8x1_and_16_x5), .X6(_8x1_and_16_x6),
    .X7(_8x1_and_16_x7));
  _4k_ram_page Page15 (
    .A0(A0), .A1(A1), .A3(A2), .A4(A3), .A2(A4), .A5(A5), .A6(A6), .A7(A7), .A8(A7), .A9(A9), .A10(A10),
    .A11(A11), .V0(V0), .V1(V1), .V2(V2), .V3(V3), .V4(V4), .V5(V5), .V6(V6), .V7(V7), .S(and_16_out),
    .X0(Page15_x0), .X1(Page15_x1), .X2(Page15_x2), .X3(Page15_x3), .X4(Page15_x4), .X5(Page15_x5),
    .X6(Page15_x6), .X7(Page15_x7));
  and and_16 (and_16_out, S, _4b_decoder_1_p20);

  assign A8 = A7;
endmodule
