// Digital circuit 8b_register.dig as structural Verilog
module _8b_register (
  input  A0,
  input  A1,
  input  A2,
  input  A3,
  input  A4,
  input  A5,
  input  A6,
  input  A7,
  input  S,
  output X0,
  output X1,
  output X2,
  output X3,
  output X4,
  output X5,
  output X6,
  output X7
);

  wire _1b_ram_1_nq, _1b_ram_2_nq, _1b_ram_3_nq, _1b_ram_4_nq, _1b_ram_5_nq, _1b_ram_6_nq, _1b_ram_7_nq,
       _1b_ram_8_nq;

  _1b_ram _1b_ram_1 (.V(A0), .S(S), .Q(X0), .NQ(_1b_ram_1_nq));
  _1b_ram _1b_ram_2 (.V(A1), .S(S), .Q(X1), .NQ(_1b_ram_2_nq));
  _1b_ram _1b_ram_3 (.V(A2), .S(S), .Q(X2), .NQ(_1b_ram_3_nq));
  _1b_ram _1b_ram_4 (.V(A3), .S(S), .Q(X3), .NQ(_1b_ram_4_nq));
  _1b_ram _1b_ram_5 (.V(A4), .S(S), .Q(X4), .NQ(_1b_ram_5_nq));
  _1b_ram _1b_ram_6 (.V(A5), .S(S), .Q(X5), .NQ(_1b_ram_6_nq));
  _1b_ram _1b_ram_7 (.V(A6), .S(S), .Q(X6), .NQ(_1b_ram_7_nq));
  _1b_ram _1b_ram_8 (.V(A7), .S(S), .Q(X7), .NQ(_1b_ram_8_nq));
endmodule
