// Digital circuit _16b_register.dig as structural Verilog
module _16b_register (
  input  S,
  input  [15:0] V,
  output [15:0] X
);

  wire _1b_ram_1_nq, _1b_ram_2_nq, _1b_ram_3_nq, _1b_ram_4_nq, _1b_ram_5_nq, _1b_ram_6_nq, _1b_ram_7_nq,
       _1b_ram_8_nq, _1b_ram_9_nq, _1b_ram_10_nq, _1b_ram_11_nq, _1b_ram_12_nq, _1b_ram_13_nq, _1b_ram_14_nq,
       _1b_ram_15_nq, _1b_ram_16_nq;

  _1b_ram _1b_ram_1 (.V(V[0]), .S(S), .Q(X[0]), .NQ(_1b_ram_1_nq));
  _1b_ram _1b_ram_2 (.V(V[1]), .S(S), .Q(X[1]), .NQ(_1b_ram_2_nq));
  _1b_ram _1b_ram_3 (.V(V[2]), .S(S), .Q(X[2]), .NQ(_1b_ram_3_nq));
  _1b_ram _1b_ram_4 (.V(V[3]), .S(S), .Q(X[3]), .NQ(_1b_ram_4_nq));
  _1b_ram _1b_ram_5 (.V(V[4]), .S(S), .Q(X[4]), .NQ(_1b_ram_5_nq));
  _1b_ram _1b_ram_6 (.V(V[5]), .S(S), .Q(X[5]), .NQ(_1b_ram_6_nq));
  _1b_ram _1b_ram_7 (.V(V[6]), .S(S), .Q(X[6]), .NQ(_1b_ram_7_nq));
  _1b_ram _1b_ram_8 (.V(V[7]), .S(S), .Q(X[7]), .NQ(_1b_ram_8_nq));
  _1b_ram _1b_ram_9 (.V(V[8]), .S(S), .Q(X[8]), .NQ(_1b_ram_9_nq));
  _1b_ram _1b_ram_10 (.V(V[9]), .S(S), .Q(X[9]), .NQ(_1b_ram_10_nq));
  _1b_ram _1b_ram_11 (.V(V[10]), .S(S), .Q(X[10]), .NQ(_1b_ram_11_nq));
  _1b_ram _1b_ram_12 (.V(V[11]), .S(S), .Q(X[11]), .NQ(_1b_ram_12_nq));
  _1b_ram _1b_ram_13 (.V(V[12]), .S(S), .Q(X[12]), .NQ(_1b_ram_13_nq));
  _1b_ram _1b_ram_14 (.V(V[13]), .S(S), .Q(X[13]), .NQ(_1b_ram_14_nq));
  _1b_ram _1b_ram_15 (.V(V[14]), .S(S), .Q(X[14]), .NQ(_1b_ram_15_nq));
  _1b_ram _1b_ram_16 (.V(V[15]), .S(S), .Q(X[15]), .NQ(_1b_ram_16_nq));
endmodule
