// Digital circuit _1_byte_ram.dig as structural Verilog
module _1_byte_ram (
  input  S,
  input  [7:0] V,
  output [7:0] X
);

  _1b_ram _1b_ram_1 (.V(V[0]), .S(S), .Q(X[0]));  // open: NQ
  _1b_ram _1b_ram_2 (.V(V[1]), .S(S), .Q(X[1]));  // open: NQ
  _1b_ram _1b_ram_3 (.V(V[2]), .S(S), .Q(X[2]));  // open: NQ
  _1b_ram _1b_ram_4 (.V(V[3]), .S(S), .Q(X[3]));  // open: NQ
  _1b_ram _1b_ram_5 (.V(V[4]), .S(S), .Q(X[4]));  // open: NQ
  _1b_ram _1b_ram_6 (.V(V[5]), .S(S), .Q(X[5]));  // open: NQ
  _1b_ram _1b_ram_7 (.V(V[6]), .S(S), .Q(X[6]));  // open: NQ
  _1b_ram _1b_ram_8 (.V(V[7]), .S(S), .Q(X[7]));  // open: NQ
endmodule
