// Digital circuit _4b_register.dig as structural Verilog
module _4b_register (
  input  [3:0] A,
  input  S,
  output [3:0] X
);

  wire _1b_ram_1_nq, _1b_ram_2_nq, _1b_ram_3_nq, _1b_ram_4_nq;

  _1b_ram _1b_ram_1 (.V(A[0]), .S(S), .Q(X[0]), .NQ(_1b_ram_1_nq));
  _1b_ram _1b_ram_2 (.V(A[1]), .S(S), .Q(X[1]), .NQ(_1b_ram_2_nq));
  _1b_ram _1b_ram_3 (.V(A[2]), .S(S), .Q(X[2]), .NQ(_1b_ram_3_nq));
  _1b_ram _1b_ram_4 (.V(A[3]), .S(S), .Q(X[3]), .NQ(_1b_ram_4_nq));
endmodule
