// Digital circuit _4k_byte_ram.dig as structural Verilog
module _4k_byte_ram (
  input  S,
  input  [11:0] A,
  input  [7:0] V,
  output [7:0] X
);

  wire and_1_out, and_2_out, and_3_out, and_4_out, and_5_out, and_6_out, and_7_out, and_8_out, and_9_out,
       and_10_out, and_11_out, and_12_out, and_13_out, and_14_out, and_15_out, and_16_out, decoder_1_out_0,
       decoder_1_out_1, decoder_1_out_2, decoder_1_out_3, decoder_1_out_4, decoder_1_out_5, decoder_1_out_6,
       decoder_1_out_7, decoder_1_out_8, decoder_1_out_9, decoder_1_out_10, decoder_1_out_11,
       decoder_1_out_12, decoder_1_out_13, decoder_1_out_14, decoder_1_out_15;
  wire [7:0] _8x1_and_1_x, _8x1_and_2_x, _8x1_and_3_x, _8x1_and_4_x, _8x1_and_5_x, _8x1_and_6_x,
       _8x1_and_7_x, _8x1_and_8_x, _8x1_and_9_x, _8x1_and_10_x, _8x1_and_11_x, _8x1_and_12_x, _8x1_and_13_x,
       _8x1_and_14_x, _8x1_and_15_x, _8x1_and_16_x, _256_byte_ram_1_x, _256_byte_ram_2_x, _256_byte_ram_3_x,
       _256_byte_ram_4_x, _256_byte_ram_5_x, _256_byte_ram_6_x, _256_byte_ram_7_x, _256_byte_ram_8_x,
       _256_byte_ram_9_x, _256_byte_ram_10_x, _256_byte_ram_11_x, _256_byte_ram_12_x, _256_byte_ram_13_x,
       _256_byte_ram_14_x, _256_byte_ram_15_x, _256_byte_ram_16_x, or_2_out, or_3_out, or_4_out, or_5_out,
       or_6_out, or_7_out, or_8_out, or_9_out, or_10_out, or_11_out, or_12_out, or_13_out, or_14_out,
       or_15_out;

  Decoder #(.Selector_Bits(4)) decoder_1 (
    .sel(A[11:8]), .out_0(decoder_1_out_0), .out_1(decoder_1_out_1), .out_2(decoder_1_out_2),
    .out_3(decoder_1_out_3), .out_4(decoder_1_out_4), .out_5(decoder_1_out_5), .out_6(decoder_1_out_6),
    .out_7(decoder_1_out_7), .out_8(decoder_1_out_8), .out_9(decoder_1_out_9), .out_10(decoder_1_out_10),
    .out_11(decoder_1_out_11), .out_12(decoder_1_out_12), .out_13(decoder_1_out_13),
    .out_14(decoder_1_out_14), .out_15(decoder_1_out_15));
  _8x1_and _8x1_and_1 (.V(_256_byte_ram_1_x), .AND(decoder_1_out_0), .X(_8x1_and_1_x));
  _256_byte_ram _256_byte_ram_1 (.S(and_1_out), .A(A[7:0]), .V(V), .X(_256_byte_ram_1_x));
  and and_1 (and_1_out, S, decoder_1_out_0);
  assign X = or_2_out | or_9_out;  // Or or_1, 8 bits wide
  assign or_2_out = or_3_out | or_6_out;  // Or or_2, 8 bits wide
  assign or_3_out = or_4_out | or_5_out;  // Or or_3, 8 bits wide
  assign or_4_out = _8x1_and_1_x | _8x1_and_2_x;  // Or or_4, 8 bits wide
  _256_byte_ram _256_byte_ram_2 (.S(and_2_out), .A(A[7:0]), .V(V), .X(_256_byte_ram_2_x));
  and and_2 (and_2_out, S, decoder_1_out_1);
  _8x1_and _8x1_and_2 (.V(_256_byte_ram_2_x), .AND(decoder_1_out_1), .X(_8x1_and_2_x));
  and and_3 (and_3_out, S, decoder_1_out_2);
  assign or_5_out = _8x1_and_3_x | _8x1_and_4_x;  // Or or_5, 8 bits wide
  _8x1_and _8x1_and_3 (.V(_256_byte_ram_3_x), .AND(decoder_1_out_2), .X(_8x1_and_3_x));
  _256_byte_ram _256_byte_ram_3 (.S(and_3_out), .A(A[7:0]), .V(V), .X(_256_byte_ram_3_x));
  _8x1_and _8x1_and_4 (.V(_256_byte_ram_4_x), .AND(decoder_1_out_3), .X(_8x1_and_4_x));
  _256_byte_ram _256_byte_ram_4 (.S(and_4_out), .A(A[7:0]), .V(V), .X(_256_byte_ram_4_x));
  and and_4 (and_4_out, S, decoder_1_out_3);
  _8x1_and _8x1_and_5 (.V(_256_byte_ram_5_x), .AND(decoder_1_out_4), .X(_8x1_and_5_x));
  _256_byte_ram _256_byte_ram_5 (.S(and_5_out), .A(A[7:0]), .V(V), .X(_256_byte_ram_5_x));
  and and_5 (and_5_out, S, decoder_1_out_4);
  assign or_6_out = or_7_out | or_8_out;  // Or or_6, 8 bits wide
  assign or_7_out = _8x1_and_5_x | _8x1_and_6_x;  // Or or_7, 8 bits wide
  _256_byte_ram _256_byte_ram_6 (.S(and_6_out), .A(A[7:0]), .V(V), .X(_256_byte_ram_6_x));
  and and_6 (and_6_out, S, decoder_1_out_5);
  _8x1_and _8x1_and_6 (.V(_256_byte_ram_6_x), .AND(decoder_1_out_5), .X(_8x1_and_6_x));
  and and_7 (and_7_out, S, decoder_1_out_6);
  assign or_8_out = _8x1_and_7_x | _8x1_and_8_x;  // Or or_8, 8 bits wide
  _8x1_and _8x1_and_7 (.V(_256_byte_ram_7_x), .AND(decoder_1_out_6), .X(_8x1_and_7_x));
  _256_byte_ram _256_byte_ram_7 (.S(and_7_out), .A(A[7:0]), .V(V), .X(_256_byte_ram_7_x));
  _8x1_and _8x1_and_8 (.V(_256_byte_ram_8_x), .AND(decoder_1_out_7), .X(_8x1_and_8_x));
  _256_byte_ram _256_byte_ram_8 (.S(and_8_out), .A(A[7:0]), .V(V), .X(_256_byte_ram_8_x));
  and and_8 (and_8_out, S, decoder_1_out_7);
  _8x1_and _8x1_and_9 (.V(_256_byte_ram_9_x), .AND(decoder_1_out_8), .X(_8x1_and_9_x));
  _256_byte_ram _256_byte_ram_9 (.S(and_9_out), .A(A[7:0]), .V(V), .X(_256_byte_ram_9_x));
  and and_9 (and_9_out, S, decoder_1_out_8);
  assign or_9_out = or_10_out | or_13_out;  // Or or_9, 8 bits wide
  assign or_10_out = or_11_out | or_12_out;  // Or or_10, 8 bits wide
  assign or_11_out = _8x1_and_9_x | _8x1_and_10_x;  // Or or_11, 8 bits wide
  _256_byte_ram _256_byte_ram_10 (.S(and_10_out), .A(A[7:0]), .V(V), .X(_256_byte_ram_10_x));
  and and_10 (and_10_out, S, decoder_1_out_9);
  _8x1_and _8x1_and_10 (.V(_256_byte_ram_10_x), .AND(decoder_1_out_9), .X(_8x1_and_10_x));
  and and_11 (and_11_out, S, decoder_1_out_10);
  assign or_12_out = _8x1_and_11_x | _8x1_and_12_x;  // Or or_12, 8 bits wide
  _8x1_and _8x1_and_11 (.V(_256_byte_ram_11_x), .AND(decoder_1_out_10), .X(_8x1_and_11_x));
  _256_byte_ram _256_byte_ram_11 (.S(and_11_out), .A(A[7:0]), .V(V), .X(_256_byte_ram_11_x));
  _8x1_and _8x1_and_12 (.V(_256_byte_ram_12_x), .AND(decoder_1_out_11), .X(_8x1_and_12_x));
  _256_byte_ram _256_byte_ram_12 (.S(and_12_out), .A(A[7:0]), .V(V), .X(_256_byte_ram_12_x));
  and and_12 (and_12_out, S, decoder_1_out_11);
  _8x1_and _8x1_and_13 (.V(_256_byte_ram_13_x), .AND(decoder_1_out_12), .X(_8x1_and_13_x));
  _256_byte_ram _256_byte_ram_13 (.S(and_13_out), .A(A[7:0]), .V(V), .X(_256_byte_ram_13_x));
  and and_13 (and_13_out, S, decoder_1_out_12);
  assign or_13_out = or_14_out | or_15_out;  // Or or_13, 8 bits wide
  assign or_14_out = _8x1_and_13_x | _8x1_and_14_x;  // Or or_14, 8 bits wide
  _256_byte_ram _256_byte_ram_14 (.S(and_14_out), .A(A[7:0]), .V(V), .X(_256_byte_ram_14_x));
  and and_14 (and_14_out, S, decoder_1_out_13);
  _8x1_and _8x1_and_14 (.V(_256_byte_ram_14_x), .AND(decoder_1_out_13), .X(_8x1_and_14_x));
  and and_15 (and_15_out, S, decoder_1_out_14);
  assign or_15_out = _8x1_and_15_x | _8x1_and_16_x;  // Or or_15, 8 bits wide
  _8x1_and _8x1_and_15 (.V(_256_byte_ram_15_x), .AND(decoder_1_out_14), .X(_8x1_and_15_x));
  _256_byte_ram _256_byte_ram_15 (.S(and_15_out), .A(A[7:0]), .V(V), .X(_256_byte_ram_15_x));
  _8x1_and _8x1_and_16 (.V(_256_byte_ram_16_x), .AND(decoder_1_out_15), .X(_8x1_and_16_x));
  _256_byte_ram _256_byte_ram_16 (.S(and_16_out), .A(A[7:0]), .V(V), .X(_256_byte_ram_16_x));
  and and_16 (and_16_out, S, decoder_1_out_15);
endmodule
