// Digital circuit 16b_counter.dig as structural Verilog
module _16b_counter (
  input  A0,
  input  A1,
  input  A2,
  input  A3,
  input  A4,
  input  A5,
  input  A6,
  input  A7,
  input  A8,
  input  A9,
  input  A10,
  input  A11,
  input  A12,
  input  A13,
  input  A14,
  input  A15,
  input  S,
  input  Inc,
  input  dec,
  output X0,
  output X1,
  output X2,
  output X3,
  output X4,
  output X5,
  output X6,
  output X7,
  output X8,
  output X9,
  output X10,
  output X11,
  output X12,
  output X13,
  output X14,
  output X15,
  output Ov
);

  wire _1b_selector_1_x, _1b_selector_2_x, _1b_selector_3_x, _1b_selector_4_x, _1b_selector_5_x,
       _1b_selector_6_x, _1b_selector_7_x, _1b_selector_8_x, _1b_selector_9_x, _1b_selector_10_x,
       _1b_selector_11_x, _1b_selector_12_x, _1b_selector_13_x, _1b_selector_14_x, _1b_selector_15_x,
       _1b_selector_16_x, _16b_register_1_x0, _16b_register_1_x1, _16b_register_1_x2, _16b_register_1_x3,
       _16b_register_1_x4, _16b_register_1_x5, _16b_register_1_x6, _16b_register_1_x7, _16b_register_1_x8,
       _16b_register_1_x9, _16b_register_1_x10, _16b_register_1_x11, _16b_register_1_x12,
       _16b_register_1_x13, _16b_register_1_x14, _16b_register_1_x15, _16b_register_2_x0, _16b_register_2_x1,
       _16b_register_2_x2, _16b_register_2_x3, _16b_register_2_x4, _16b_register_2_x5, _16b_register_2_x6,
       _16b_register_2_x7, _16b_register_2_x8, _16b_register_2_x9, _16b_register_2_x10, _16b_register_2_x11,
       _16b_register_2_x12, _16b_register_2_x13, _16b_register_2_x14, _16b_register_2_x15, _16x1_and_1_x0,
       _16x1_and_1_x1, _16x1_and_1_x2, _16x1_and_1_x3, _16x1_and_1_x4, _16x1_and_1_x5, _16x1_and_1_x6,
       _16x1_and_1_x7, _16x1_and_1_x8, _16x1_and_1_x9, _16x1_and_1_x10, _16x1_and_1_x11, _16x1_and_1_x12,
       _16x1_and_1_x13, _16x1_and_1_x14, _16x1_and_1_x15, not_1_out, not_2_out, or_1_out, or_2_out;

  _16x1_and _16x1_and_1 (
    .A0(A0), .A1(A1), .A2(A2), .A3(A3), .A4(A4), .A5(A5), .A6(A6), .A7(A7), .A8(A8), .A9(A9), .A10(A10),
    .A11(A11), .A12(A12), .A13(A13), .A14(A14), .A15(A15), .AND(S), .X0(_16x1_and_1_x0), .X1(_16x1_and_1_x1),
    .X2(_16x1_and_1_x2), .X3(_16x1_and_1_x3), .X4(_16x1_and_1_x4), .X5(_16x1_and_1_x5), .X6(_16x1_and_1_x6),
    .X7(_16x1_and_1_x7), .X8(_16x1_and_1_x8), .X9(_16x1_and_1_x9), .X10(_16x1_and_1_x10),
    .X11(_16x1_and_1_x11), .X12(_16x1_and_1_x12), .X13(_16x1_and_1_x13), .X14(_16x1_and_1_x14),
    .X15(_16x1_and_1_x15));
  not not_1 (not_1_out, S);
  _1b_selector _1b_selector_1 (.A(_16b_register_2_x15), .B(_16x1_and_1_x15), .GoA(not_1_out), .X(_1b_selector_1_x));
  _1b_selector _1b_selector_2 (.A(_16b_register_2_x14), .B(_16x1_and_1_x14), .GoA(not_1_out), .X(_1b_selector_2_x));
  _1b_selector _1b_selector_3 (.A(_16b_register_2_x13), .B(_16x1_and_1_x13), .GoA(not_1_out), .X(_1b_selector_3_x));
  _1b_selector _1b_selector_4 (.A(_16b_register_2_x12), .B(_16x1_and_1_x12), .GoA(not_1_out), .X(_1b_selector_4_x));
  _1b_selector _1b_selector_5 (.A(_16b_register_2_x11), .B(_16x1_and_1_x11), .GoA(not_1_out), .X(_1b_selector_5_x));
  _1b_selector _1b_selector_6 (.A(_16b_register_2_x10), .B(_16x1_and_1_x10), .GoA(not_1_out), .X(_1b_selector_6_x));
  _1b_selector _1b_selector_7 (.A(_16b_register_2_x9), .B(_16x1_and_1_x9), .GoA(not_1_out), .X(_1b_selector_7_x));
  _1b_selector _1b_selector_8 (.A(_16b_register_2_x8), .B(_16x1_and_1_x8), .GoA(not_1_out), .X(_1b_selector_8_x));
  _1b_selector _1b_selector_9 (.A(_16b_register_2_x7), .B(_16x1_and_1_x7), .GoA(not_1_out), .X(_1b_selector_9_x));
  _1b_selector _1b_selector_10 (.A(_16b_register_2_x6), .B(_16x1_and_1_x6), .GoA(not_1_out), .X(_1b_selector_10_x));
  _1b_selector _1b_selector_11 (.A(_16b_register_2_x5), .B(_16x1_and_1_x5), .GoA(not_1_out), .X(_1b_selector_11_x));
  _1b_selector _1b_selector_12 (.A(_16b_register_2_x4), .B(_16x1_and_1_x4), .GoA(not_1_out), .X(_1b_selector_12_x));
  _1b_selector _1b_selector_13 (.A(_16b_register_2_x3), .B(_16x1_and_1_x3), .GoA(not_1_out), .X(_1b_selector_13_x));
  _1b_selector _1b_selector_14 (.A(_16b_register_2_x2), .B(_16x1_and_1_x2), .GoA(not_1_out), .X(_1b_selector_14_x));
  or or_1 (or_1_out, Inc, dec);
  _1b_selector _1b_selector_15 (.A(_16b_register_2_x1), .B(_16x1_and_1_x1), .GoA(not_1_out), .X(_1b_selector_15_x));
  _1b_selector _1b_selector_16 (.A(_16b_register_2_x0), .B(_16x1_and_1_x0), .GoA(not_1_out), .X(_1b_selector_16_x));
  _16b_adder _16b_adder_1 (
    .Cin(1'b0), .A0(_1b_selector_16_x), .A1(_1b_selector_15_x), .A2(_1b_selector_14_x),
    .A3(_1b_selector_13_x), .A4(_1b_selector_12_x), .A5(_1b_selector_11_x), .A6(_1b_selector_10_x),
    .A7(_1b_selector_9_x), .A8(_1b_selector_8_x), .A9(_1b_selector_7_x), .A10(_1b_selector_6_x),
    .A11(_1b_selector_5_x), .A12(_1b_selector_4_x), .A13(_1b_selector_3_x), .A14(_1b_selector_2_x),
    .A15(_1b_selector_1_x), .B0(or_1_out), .B1(dec), .B2(dec), .B3(dec), .B4(dec), .B5(dec), .B6(dec),
    .B7(dec), .B8(dec), .B9(dec), .B10(dec), .B11(dec), .B12(dec), .B13(dec), .B14(dec), .B15(dec), .C(Ov),
    .X0(X0), .X1(X1), .X2(X2), .X3(X3), .X4(X4), .X5(X5), .X6(X6), .X7(X7), .X8(X8), .X9(X9), .X10(X10),
    .X11(X11), .X12(X12), .X13(X13), .X14(X14), .X15(X15));
  or or_2 (or_2_out, or_1_out, S);
  _16b_register _16b_register_1 (
    .A0(X0), .A1(X1), .A2(X2), .A3(X3), .A4(X4), .A5(X5), .A6(X6), .A7(X7), .A8(X8), .A9(X9), .A10(X10),
    .A11(X11), .A12(X12), .A13(X13), .A14(X14), .A15(X15), .S(or_2_out), .X0(_16b_register_1_x0),
    .X1(_16b_register_1_x1), .X2(_16b_register_1_x2), .X3(_16b_register_1_x3), .X4(_16b_register_1_x4),
    .X5(_16b_register_1_x5), .X6(_16b_register_1_x6), .X7(_16b_register_1_x7), .X8(_16b_register_1_x8),
    .X9(_16b_register_1_x9), .X10(_16b_register_1_x10), .X11(_16b_register_1_x11), .X12(_16b_register_1_x12),
    .X13(_16b_register_1_x13), .X14(_16b_register_1_x14), .X15(_16b_register_1_x15));
  not not_2 (not_2_out, or_2_out);
  _16b_register _16b_register_2 (
    .A0(_16b_register_1_x0), .A1(_16b_register_1_x1), .A2(_16b_register_1_x2), .A3(_16b_register_1_x3),
    .A4(_16b_register_1_x4), .A5(_16b_register_1_x5), .A6(_16b_register_1_x6), .A7(_16b_register_1_x7),
    .A8(_16b_register_1_x8), .A9(_16b_register_1_x9), .A10(_16b_register_1_x10), .A11(_16b_register_1_x11),
    .A12(_16b_register_1_x12), .A13(_16b_register_1_x13), .A14(_16b_register_1_x14),
    .A15(_16b_register_1_x15), .S(not_2_out), .X0(_16b_register_2_x0), .X1(_16b_register_2_x1),
    .X2(_16b_register_2_x2), .X3(_16b_register_2_x3), .X4(_16b_register_2_x4), .X5(_16b_register_2_x5),
    .X6(_16b_register_2_x6), .X7(_16b_register_2_x7), .X8(_16b_register_2_x8), .X9(_16b_register_2_x9),
    .X10(_16b_register_2_x10), .X11(_16b_register_2_x11), .X12(_16b_register_2_x12),
    .X13(_16b_register_2_x13), .X14(_16b_register_2_x14), .X15(_16b_register_2_x15));
endmodule
