// Digital circuit 8b_counter.dig as structural Verilog
module _8b_counter (
  input  A0,
  input  A1,
  input  A2,
  input  A3,
  input  A4,
  input  A5,
  input  A6,
  input  A7,
  input  S,
  input  Inc,
  input  dec,
  output X0,
  output X1,
  output X2,
  output X3,
  output X4,
  output X5,
  output X6,
  output X7,
  output Ov
);

  wire _1b_selector_1_x, _1b_selector_2_x, _1b_selector_3_x, _1b_selector_4_x, _1b_selector_5_x,
       _1b_selector_6_x, _1b_selector_7_x, _1b_selector_8_x, _8b_register_1_x0, _8b_register_1_x1,
       _8b_register_1_x2, _8b_register_1_x3, _8b_register_1_x4, _8b_register_1_x5, _8b_register_1_x6,
       _8b_register_1_x7, _8b_register_2_x0, _8b_register_2_x1, _8b_register_2_x2, _8b_register_2_x3,
       _8b_register_2_x4, _8b_register_2_x5, _8b_register_2_x6, _8b_register_2_x7, _8x1_and_1_x0,
       _8x1_and_1_x1, _8x1_and_1_x2, _8x1_and_1_x3, _8x1_and_1_x4, _8x1_and_1_x5, _8x1_and_1_x6,
       _8x1_and_1_x7, not_1_out, not_2_out, or_1_out, or_2_out;

  _8x1_and _8x1_and_1 (
    .A0(A0), .A1(A1), .A2(A2), .A3(A3), .A4(A4), .A5(A5), .A6(A6), .A7(A7), .AND(S), .X0(_8x1_and_1_x0),
    .X1(_8x1_and_1_x1), .X2(_8x1_and_1_x2), .X3(_8x1_and_1_x3), .X4(_8x1_and_1_x4), .X5(_8x1_and_1_x5),
    .X6(_8x1_and_1_x6), .X7(_8x1_and_1_x7));
  not not_1 (not_1_out, S);
  _1b_selector _1b_selector_1 (.A(_8b_register_2_x7), .B(_8x1_and_1_x7), .GoA(not_1_out), .X(_1b_selector_1_x));
  _1b_selector _1b_selector_2 (.A(_8b_register_2_x6), .B(_8x1_and_1_x6), .GoA(not_1_out), .X(_1b_selector_2_x));
  _1b_selector _1b_selector_3 (.A(_8b_register_2_x5), .B(_8x1_and_1_x5), .GoA(not_1_out), .X(_1b_selector_3_x));
  _1b_selector _1b_selector_4 (.A(_8b_register_2_x4), .B(_8x1_and_1_x4), .GoA(not_1_out), .X(_1b_selector_4_x));
  _1b_selector _1b_selector_5 (.A(_8b_register_2_x3), .B(_8x1_and_1_x3), .GoA(not_1_out), .X(_1b_selector_5_x));
  _1b_selector _1b_selector_6 (.A(_8b_register_2_x2), .B(_8x1_and_1_x2), .GoA(not_1_out), .X(_1b_selector_6_x));
  or or_1 (or_1_out, Inc, dec);
  _1b_selector _1b_selector_7 (.A(_8b_register_2_x1), .B(_8x1_and_1_x1), .GoA(not_1_out), .X(_1b_selector_7_x));
  _1b_selector _1b_selector_8 (.A(_8b_register_2_x0), .B(_8x1_and_1_x0), .GoA(not_1_out), .X(_1b_selector_8_x));
  _8b_adder _8b_adder_1 (
    .A0(_1b_selector_8_x), .A1(_1b_selector_7_x), .A2(_1b_selector_6_x), .A3(_1b_selector_5_x),
    .A4(_1b_selector_4_x), .A5(_1b_selector_3_x), .A6(_1b_selector_2_x), .A7(_1b_selector_1_x),
    .B0(or_1_out), .B1(dec), .B2(dec), .B3(dec), .B4(dec), .B5(dec), .B6(dec), .B7(dec), .Cin(1'b0), .X0(X0),
    .X1(X1), .X2(X2), .X3(X3), .X4(X4), .X5(X5), .X6(X6), .X7(X7), .C(Ov));
  or or_2 (or_2_out, or_1_out, S);
  _8b_register _8b_register_1 (
    .A0(X0), .A1(X1), .A2(X2), .A3(X3), .A4(X4), .A5(X5), .A6(X6), .A7(X7), .S(or_2_out),
    .X0(_8b_register_1_x0), .X1(_8b_register_1_x1), .X2(_8b_register_1_x2), .X3(_8b_register_1_x3),
    .X4(_8b_register_1_x4), .X5(_8b_register_1_x5), .X6(_8b_register_1_x6), .X7(_8b_register_1_x7));
  not not_2 (not_2_out, or_2_out);
  _8b_register _8b_register_2 (
    .A0(_8b_register_1_x0), .A1(_8b_register_1_x1), .A2(_8b_register_1_x2), .A3(_8b_register_1_x3),
    .A4(_8b_register_1_x4), .A5(_8b_register_1_x5), .A6(_8b_register_1_x6), .A7(_8b_register_1_x7),
    .S(not_2_out), .X0(_8b_register_2_x0), .X1(_8b_register_2_x1), .X2(_8b_register_2_x2),
    .X3(_8b_register_2_x3), .X4(_8b_register_2_x4), .X5(_8b_register_2_x5), .X6(_8b_register_2_x6),
    .X7(_8b_register_2_x7));
endmodule
