// Digital circuit _16b_counter.dig as structural Verilog
module _16b_counter (
  input  [15:0] V,
  input  S,
  input  Inc,
  input  dec,
  output [15:0] X,
  output Ov
);

  wire _1b_selector_1_x, _1b_selector_2_x, _1b_selector_3_x, _1b_selector_4_x, _1b_selector_5_x,
       _1b_selector_6_x, _1b_selector_7_x, _1b_selector_8_x, _1b_selector_9_x, _1b_selector_10_x,
       _1b_selector_11_x, _1b_selector_12_x, _1b_selector_13_x, _1b_selector_14_x, _1b_selector_15_x,
       _1b_selector_16_x, _16b_register_1_x0, _16b_register_1_x1, _16b_register_1_x2, _16b_register_1_x3,
       _16b_register_1_x4, _16b_register_1_x5, _16b_register_1_x6, _16b_register_1_x7, _16b_register_1_x8,
       _16b_register_1_x9, _16b_register_1_x10, _16b_register_1_x11, _16b_register_1_x12,
       _16b_register_1_x13, _16b_register_1_x14, _16b_register_1_x15, _16b_register_2_x0, _16b_register_2_x1,
       _16b_register_2_x2, _16b_register_2_x3, _16b_register_2_x4, _16b_register_2_x5, _16b_register_2_x6,
       _16b_register_2_x7, _16b_register_2_x8, _16b_register_2_x9, _16b_register_2_x10, _16b_register_2_x11,
       _16b_register_2_x12, _16b_register_2_x13, _16b_register_2_x14, _16b_register_2_x15, _16x1_and_1_x0,
       _16x1_and_1_x1, _16x1_and_1_x2, _16x1_and_1_x3, _16x1_and_1_x4, _16x1_and_1_x5, _16x1_and_1_x6,
       _16x1_and_1_x7, _16x1_and_1_x8, _16x1_and_1_x9, _16x1_and_1_x10, _16x1_and_1_x11, _16x1_and_1_x12,
       _16x1_and_1_x13, _16x1_and_1_x14, _16x1_and_1_x15, not_1_out, not_2_out, or_1_out, or_2_out;

  _16x1_and _16x1_and_1 (
    .A0(V[0]), .A1(V[1]), .A2(V[2]), .A3(V[3]), .A4(V[4]), .A5(V[5]), .A6(V[6]), .A7(V[7]), .A8(V[8]),
    .A9(V[9]), .A10(V[10]), .A11(V[11]), .A12(V[12]), .A13(V[13]), .A14(V[14]), .A15(V[15]), .AND(S),
    .X0(_16x1_and_1_x0), .X1(_16x1_and_1_x1), .X2(_16x1_and_1_x2), .X3(_16x1_and_1_x3), .X4(_16x1_and_1_x4),
    .X5(_16x1_and_1_x5), .X6(_16x1_and_1_x6), .X7(_16x1_and_1_x7), .X8(_16x1_and_1_x8), .X9(_16x1_and_1_x9),
    .X10(_16x1_and_1_x10), .X11(_16x1_and_1_x11), .X12(_16x1_and_1_x12), .X13(_16x1_and_1_x13),
    .X14(_16x1_and_1_x14), .X15(_16x1_and_1_x15));
  not not_1 (not_1_out, S);
  _1b_selector _1b_selector_1 (.A(_16b_register_2_x15), .B(_16x1_and_1_x15), .GoA(not_1_out), .X(_1b_selector_1_x));
  _1b_selector _1b_selector_2 (.A(_16b_register_2_x14), .B(_16x1_and_1_x14), .GoA(not_1_out), .X(_1b_selector_2_x));
  _1b_selector _1b_selector_3 (.A(_16b_register_2_x13), .B(_16x1_and_1_x13), .GoA(not_1_out), .X(_1b_selector_3_x));
  _1b_selector _1b_selector_4 (.A(_16b_register_2_x12), .B(_16x1_and_1_x12), .GoA(not_1_out), .X(_1b_selector_4_x));
  _1b_selector _1b_selector_5 (.A(_16b_register_2_x11), .B(_16x1_and_1_x11), .GoA(not_1_out), .X(_1b_selector_5_x));
  _1b_selector _1b_selector_6 (.A(_16b_register_2_x10), .B(_16x1_and_1_x10), .GoA(not_1_out), .X(_1b_selector_6_x));
  _1b_selector _1b_selector_7 (.A(_16b_register_2_x9), .B(_16x1_and_1_x9), .GoA(not_1_out), .X(_1b_selector_7_x));
  _1b_selector _1b_selector_8 (.A(_16b_register_2_x8), .B(_16x1_and_1_x8), .GoA(not_1_out), .X(_1b_selector_8_x));
  _1b_selector _1b_selector_9 (.A(_16b_register_2_x7), .B(_16x1_and_1_x7), .GoA(not_1_out), .X(_1b_selector_9_x));
  _1b_selector _1b_selector_10 (.A(_16b_register_2_x6), .B(_16x1_and_1_x6), .GoA(not_1_out), .X(_1b_selector_10_x));
  _1b_selector _1b_selector_11 (.A(_16b_register_2_x5), .B(_16x1_and_1_x5), .GoA(not_1_out), .X(_1b_selector_11_x));
  _1b_selector _1b_selector_12 (.A(_16b_register_2_x4), .B(_16x1_and_1_x4), .GoA(not_1_out), .X(_1b_selector_12_x));
  _1b_selector _1b_selector_13 (.A(_16b_register_2_x3), .B(_16x1_and_1_x3), .GoA(not_1_out), .X(_1b_selector_13_x));
  _1b_selector _1b_selector_14 (.A(_16b_register_2_x2), .B(_16x1_and_1_x2), .GoA(not_1_out), .X(_1b_selector_14_x));
  or or_1 (or_1_out, Inc, dec);
  _1b_selector _1b_selector_15 (.A(_16b_register_2_x1), .B(_16x1_and_1_x1), .GoA(not_1_out), .X(_1b_selector_15_x));
  _1b_selector _1b_selector_16 (.A(_16b_register_2_x0), .B(_16x1_and_1_x0), .GoA(not_1_out), .X(_1b_selector_16_x));
  _16b_adder _16b_adder_1 (
    .Cin(1'b0), .A0(_1b_selector_16_x), .A1(_1b_selector_15_x), .A2(_1b_selector_14_x),
    .A3(_1b_selector_13_x), .A4(_1b_selector_12_x), .A5(_1b_selector_11_x), .A6(_1b_selector_10_x),
    .A7(_1b_selector_9_x), .A8(_1b_selector_8_x), .A9(_1b_selector_7_x), .A10(_1b_selector_6_x),
    .A11(_1b_selector_5_x), .A12(_1b_selector_4_x), .A13(_1b_selector_3_x), .A14(_1b_selector_2_x),
    .A15(_1b_selector_1_x), .B0(or_1_out), .B1(dec), .B2(dec), .B3(dec), .B4(dec), .B5(dec), .B6(dec),
    .B7(dec), .B8(dec), .B9(dec), .B10(dec), .B11(dec), .B12(dec), .B13(dec), .B14(dec), .B15(dec), .C(Ov),
    .X0(X[0]), .X1(X[1]), .X2(X[2]), .X3(X[3]), .X4(X[4]), .X5(X[5]), .X6(X[6]), .X7(X[7]), .X8(X[8]),
    .X9(X[9]), .X10(X[10]), .X11(X[11]), .X12(X[12]), .X13(X[13]), .X14(X[14]), .X15(X[15]));
  or or_2 (or_2_out, or_1_out, S);
  _16b_register _16b_register_1 (
    .A0(X[0]), .A1(X[1]), .A2(X[2]), .A3(X[3]), .A4(X[4]), .A5(X[5]), .A6(X[6]), .A7(X[7]), .A8(X[8]),
    .A9(X[9]), .A10(X[10]), .A11(X[11]), .A12(X[12]), .A13(X[13]), .A14(X[14]), .A15(X[15]), .S(or_2_out),
    .X0(_16b_register_1_x0), .X1(_16b_register_1_x1), .X2(_16b_register_1_x2), .X3(_16b_register_1_x3),
    .X4(_16b_register_1_x4), .X5(_16b_register_1_x5), .X6(_16b_register_1_x6), .X7(_16b_register_1_x7),
    .X8(_16b_register_1_x8), .X9(_16b_register_1_x9), .X10(_16b_register_1_x10), .X11(_16b_register_1_x11),
    .X12(_16b_register_1_x12), .X13(_16b_register_1_x13), .X14(_16b_register_1_x14), .X15(_16b_register_1_x15));
  not not_2 (not_2_out, or_2_out);
  _16b_register _16b_register_2 (
    .A0(_16b_register_1_x0), .A1(_16b_register_1_x1), .A2(_16b_register_1_x2), .A3(_16b_register_1_x3),
    .A4(_16b_register_1_x4), .A5(_16b_register_1_x5), .A6(_16b_register_1_x6), .A7(_16b_register_1_x7),
    .A8(_16b_register_1_x8), .A9(_16b_register_1_x9), .A10(_16b_register_1_x10), .A11(_16b_register_1_x11),
    .A12(_16b_register_1_x12), .A13(_16b_register_1_x13), .A14(_16b_register_1_x14),
    .A15(_16b_register_1_x15), .S(not_2_out), .X0(_16b_register_2_x0), .X1(_16b_register_2_x1),
    .X2(_16b_register_2_x2), .X3(_16b_register_2_x3), .X4(_16b_register_2_x4), .X5(_16b_register_2_x5),
    .X6(_16b_register_2_x6), .X7(_16b_register_2_x7), .X8(_16b_register_2_x8), .X9(_16b_register_2_x9),
    .X10(_16b_register_2_x10), .X11(_16b_register_2_x11), .X12(_16b_register_2_x12),
    .X13(_16b_register_2_x13), .X14(_16b_register_2_x14), .X15(_16b_register_2_x15));
endmodule
