// Digital circuit _8b_counter.dig as structural Verilog
module _8b_counter (
  input  [7:0] V,
  input  S,
  input  Inc,
  input  dec,
  output [7:0] X,
  output Ov
);

  wire _1b_selector_1_x, _1b_selector_2_x, _1b_selector_3_x, _1b_selector_4_x, _1b_selector_5_x,
       _1b_selector_6_x, _1b_selector_7_x, _1b_selector_8_x, _8b_register_1_x0, _8b_register_1_x1,
       _8b_register_1_x2, _8b_register_1_x3, _8b_register_1_x4, _8b_register_1_x5, _8b_register_1_x6,
       _8b_register_1_x7, _8b_register_2_x0, _8b_register_2_x1, _8b_register_2_x2, _8b_register_2_x3,
       _8b_register_2_x4, _8b_register_2_x5, _8b_register_2_x6, _8b_register_2_x7, _8x1_and_1_x0,
       _8x1_and_1_x1, _8x1_and_1_x2, _8x1_and_1_x3, _8x1_and_1_x4, _8x1_and_1_x5, _8x1_and_1_x6,
       _8x1_and_1_x7, not_1_out, not_2_out, or_1_out, or_2_out;

  _8x1_and _8x1_and_1 (
    .A0(V[0]), .A1(V[1]), .A2(V[2]), .A3(V[3]), .A4(V[4]), .A5(V[5]), .A6(V[6]), .A7(V[7]), .AND(S),
    .X0(_8x1_and_1_x0), .X1(_8x1_and_1_x1), .X2(_8x1_and_1_x2), .X3(_8x1_and_1_x3), .X4(_8x1_and_1_x4),
    .X5(_8x1_and_1_x5), .X6(_8x1_and_1_x6), .X7(_8x1_and_1_x7));
  not not_1 (not_1_out, S);
  _1b_selector _1b_selector_1 (.A(_8b_register_2_x7), .B(_8x1_and_1_x7), .GoA(not_1_out), .X(_1b_selector_1_x));
  _1b_selector _1b_selector_2 (.A(_8b_register_2_x6), .B(_8x1_and_1_x6), .GoA(not_1_out), .X(_1b_selector_2_x));
  _1b_selector _1b_selector_3 (.A(_8b_register_2_x5), .B(_8x1_and_1_x5), .GoA(not_1_out), .X(_1b_selector_3_x));
  _1b_selector _1b_selector_4 (.A(_8b_register_2_x4), .B(_8x1_and_1_x4), .GoA(not_1_out), .X(_1b_selector_4_x));
  _1b_selector _1b_selector_5 (.A(_8b_register_2_x3), .B(_8x1_and_1_x3), .GoA(not_1_out), .X(_1b_selector_5_x));
  _1b_selector _1b_selector_6 (.A(_8b_register_2_x2), .B(_8x1_and_1_x2), .GoA(not_1_out), .X(_1b_selector_6_x));
  or or_1 (or_1_out, Inc, dec);
  _1b_selector _1b_selector_7 (.A(_8b_register_2_x1), .B(_8x1_and_1_x1), .GoA(not_1_out), .X(_1b_selector_7_x));
  _1b_selector _1b_selector_8 (.A(_8b_register_2_x0), .B(_8x1_and_1_x0), .GoA(not_1_out), .X(_1b_selector_8_x));
  _8b_adder _8b_adder_1 (
    .A0(_1b_selector_8_x), .A1(_1b_selector_7_x), .A2(_1b_selector_6_x), .A3(_1b_selector_5_x),
    .A4(_1b_selector_4_x), .A5(_1b_selector_3_x), .A6(_1b_selector_2_x), .A7(_1b_selector_1_x),
    .B0(or_1_out), .B1(dec), .B2(dec), .B3(dec), .B4(dec), .B5(dec), .B6(dec), .B7(dec), .Cin(1'b0),
    .X0(X[0]), .X1(X[1]), .X2(X[2]), .X3(X[3]), .X4(X[4]), .X5(X[5]), .X6(X[6]), .X7(X[7]), .C(Ov));
  or or_2 (or_2_out, or_1_out, S);
  _8b_register _8b_register_1 (
    .A0(X[0]), .A1(X[1]), .A2(X[2]), .A3(X[3]), .A4(X[4]), .A5(X[5]), .A6(X[6]), .A7(X[7]), .S(or_2_out),
    .X0(_8b_register_1_x0), .X1(_8b_register_1_x1), .X2(_8b_register_1_x2), .X3(_8b_register_1_x3),
    .X4(_8b_register_1_x4), .X5(_8b_register_1_x5), .X6(_8b_register_1_x6), .X7(_8b_register_1_x7));
  not not_2 (not_2_out, or_2_out);
  _8b_register _8b_register_2 (
    .A0(_8b_register_1_x0), .A1(_8b_register_1_x1), .A2(_8b_register_1_x2), .A3(_8b_register_1_x3),
    .A4(_8b_register_1_x4), .A5(_8b_register_1_x5), .A6(_8b_register_1_x6), .A7(_8b_register_1_x7),
    .S(not_2_out), .X0(_8b_register_2_x0), .X1(_8b_register_2_x1), .X2(_8b_register_2_x2),
    .X3(_8b_register_2_x3), .X4(_8b_register_2_x4), .X5(_8b_register_2_x5), .X6(_8b_register_2_x6),
    .X7(_8b_register_2_x7));
endmodule
