// Digital circuit one_time_bit.dig as structural Verilog
module one_time_bit (
  input  Cl,
  output Rst,
  output Exc,
  output PC_plus__plus
);

  wire and_1_out, and_2_out, counter_1_out, counterpreset_1_out, delay_1_out, delay_2_out, not_1_out,
       not_2_out, or_1_out, or_2_out, or_3_out;

  or or_1 (or_1_out, or_1_out, Cl);
  not not_1 (not_1_out, Cl);
  and and_1 (and_1_out, or_1_out, not_1_out);
  or or_2 (or_2_out, or_2_out, and_1_out);
  not not_2 (not_2_out, and_1_out);
  xor xor_1 (Rst, or_1_out, or_2_out);
  and and_2 (and_2_out, or_2_out, not_2_out);
  Counter counter_1 (.en(and_2_out), .C(and_2_out), .clr(1'b0), .out(counter_1_out));  // open: ovf
  Delay #(.delayTime(2)) delay_1 (.in(and_2_out), .out(delay_1_out));
  and and_3 (PC_plus__plus, counter_1_out, delay_1_out);
  or or_3 (or_3_out, and_2_out, Rst);
  CounterPreset counterpreset_1 (
    .en(and_2_out), .C(or_3_out), .dir(1'b0), .in(1'b1), .ld(Rst), .clr(1'b0), .out(counterpreset_1_out));  // open: ovf
  and and_4 (Exc, counterpreset_1_out, delay_2_out);
  Delay #(.delayTime(2)) delay_2 (.in(and_2_out), .out(delay_2_out));
endmodule
