// Digital circuit one_time_bit_.dig as structural Verilog
module one_time_bit (
  input  Clk,
  output Rst,
  output Clk_2
);

  wire delay_1_out, not_1_out, or_1_out;

  not not_1 (not_1_out, or_1_out);
  and and_1 (Rst, Clk, not_1_out);
  or or_1 (or_1_out, Rst, or_1_out);
  Delay #(.delayTime(2)) delay_1 (.in(or_1_out), .out(delay_1_out));
  and and_2 (Clk_2, Clk, delay_1_out);
endmodule
